// Logisim project БВТ2003_Тураев_Некруз_Процессор.circ as structural Verilog: 14 circuits, main circuit main
module main (
  input  in_1,
  input  HLT,
  input  OUT,
  input  MOV,
  input  LDO,
  input  STO,
  input  JMP_X,
  input  JMPF,
  input  [2:0] \Выбор_флага ,
  input  REG_ST,
  input  REG_LD,
  input  [1:0] REG_num,
  input  ALU,
  input  [2:0] \Выбор_команды ,
  input  INV_A,
  output [15:0] out_16,
  output [15:0] out_17,
  output [5:0] out_18,
  output [9:0] out_19,
  output [15:0] out_20,
  output [9:0] out_21,
  output [5:0] out_22,
  output out_23,
  output out_24
);

  wire Alu_t, and_1_out, and_2_out, and_3_out, and_4_out, and_5_out, and_6_out, and_7_out, and_8_out,
       and_9_out, button_1_out, button_2_out, Clear, clock_1_out, comparator_1_gt, comparator_2_gt,
       counter_6_q, f_1_out_2, f_2_out_2, f_3_out_2, f_4_out_2, flag_dec_1_out_2, \flag_dec_1_флаг_вкл ,
       FlagAdr, FlagAdrO, INP, instr_1_out_5, instrfl_1_flag, LDO_t, MOV_t, MV, not_2_out, not_3_out,
       not_4_out, not_5_out, not_6_out, not_7_out, not_8_out, or_1_out, or_2_out, or_3_out, or_5_out,
       or_6_out, or_7_out, or_8_out, or_9_out, OUT_t, read_1_out_3, RecReg, STO_t, T, Takt, TaktKom;
  wire [1:0] bit_extender_1_out, counter_9_q, multiplexer_1_out, multiplexer_2_out, multiplexer_6_out,
       multiplexer_7_out, Reg, Reg_num_t, SelALU, SelDev, SelReg;
  wire [2:0] counter_5_q, counter_8_q, \flag_dec_1_флаг ;
  wire [3:0] ALU_INSTR, multiplexer_10_out, register_9_q, register_10_q, register_11_q, register_12_q;
  wire [5:0] counter_1_q, Flags, instr_1_out_4, multiplexer_4_out, multiplexer_5_out, \алу_1_out_4 ;
  wire [6:0] keyboard_1_data, multiplexer_11_out, outhex_1_y6, register_13_q;
  wire [9:0] adr_1_out_4, AdReg, counter_3_q, multiplexer_3_out;
  wire [15:0] multiplexer_8_out, reg_file_1_out_4, register_6_q, \алу_1_out_5 ;

  Counter #(.width(6), .max('h3f), .ongoal("stay")) counter_1 (
    .Q(counter_1_q), .clk(clock_1_out), .clr(Clear));  // open: load, D, count, carry
  Button button_1 (.out(button_1_out));
  Button button_2 (.out(button_2_out));
  not not_1 (TaktKom, or_1_out);
  or or_1 (or_1_out, ~counter_1_q[0], ~counter_1_q[1], ~counter_1_q[2], ~counter_1_q[3], ~counter_1_q[4], ~counter_1_q[5]);  // OR_Gate
  Read read_1 (.in_2(button_1_out), .out_3(read_1_out_3), .out_4(Clear), .in_1(clock_1_out));
  Keyboard keyboard_1 (.clk(read_1_out_3), .clr(button_2_out), .data(keyboard_1_data));  // open: re, avail
  // Probe on out_18
  // Probe on out_19
  // Probe on out_20
  // Probe on keyboard_1_data
  TTY tty_1 (.data(keyboard_1_data), .clk(read_1_out_3), .clr(button_2_out));  // open: we
  // Probe on instr_1_out_4
  INSTR instr_1 (
    .Simbol(keyboard_1_data), .out_4(instr_1_out_4), .Takt(read_1_out_3), .in_3(Clear),
    .out_5(instr_1_out_5), .out_6(out_20));
  // Probe on adr_1_out_4
  ADR adr_1 (.in_2(keyboard_1_data), .in_3(read_1_out_3), .out_4(adr_1_out_4), .in_1(instr_1_out_5));
  Register #(.width(6)) register_1 (.D(instr_1_out_4), .Q(out_18), .clk(TaktKom));  // open: en, clr
  Register #(.width(10)) register_2 (.D(adr_1_out_4), .Q(out_19), .clk(TaktKom));  // open: en, clr
  Multiplexer #(.width(2)) multiplexer_1 (
    .in0(SelDev), .in1(SelReg), .out(multiplexer_1_out), .sel(RecReg));  // open: en
  Multiplexer #(.width(2)) multiplexer_2 (
    .in0(multiplexer_1_out), .in1(SelALU), .out(multiplexer_2_out), .sel(Alu_t));  // open: en
  \ОЗУ_DEC  \u_озу_dec_1  (
    .in_1(out_22), .SelDev(SelDev), .OUT(OUT_t), .INP(INP), .MOV(MOV_t), .STO(STO_t), .LDO(LDO_t),
    .Flag(FlagAdrO), .MV(MV));
  REG_DEC reg_dec_1 (.in_1(out_22), .out_2(Reg_num_t), .out_4(SelReg), .Flag(RecReg));
  Flag_DEC flag_dec_1 (
    .in_1(out_22), .out_2(flag_dec_1_out_2), .\Флаг (\flag_dec_1_флаг ), .\Флаг_вкл (\flag_dec_1_флаг_вкл ));
  ALU_DEC alu_dec_1 (.in_1(out_22), .out_2(ALU_INSTR), .out_3(SelALU), .out_4(Alu_t));
  // Probe on out_20
  not not_2 (not_2_out, and_1_out);
  and and_1 (and_1_out, or_2_out, and_3_out);
  or or_2 (or_2_out, INP, STO_t);
  Multiplexer #(.width(10)) multiplexer_3 (
    .in0(out_17[15:6]), .in1(out_19), .out(multiplexer_3_out), .sel(T));  // open: en
  or or_3 (or_3_out, flag_dec_1_out_2, instrfl_1_flag);
  InstrFl instrfl_1 (.in_1(Flags), .in_2(\flag_dec_1_флаг ), .Falg_On(\flag_dec_1_флаг_вкл ), .Flag(instrfl_1_flag));
  RAM #(.addrWidth(10), .dataWidth(16), .bus("separate")) ram_1 (
    .addr(out_21), .din(register_6_q), .data(out_17), .clk(not_2_out));  // open: str, sel, ld, clr
  or or_4 (FlagAdr, MV, or_3_out);
  Counter counter_2 (.clk(or_3_out));  // open: load, D, count, Q, carry, clr
  Clock clock_1 (.out(clock_1_out));
  and and_2 (and_2_out, RecReg, and_3_out);
  Multiplexer #(.width(6)) multiplexer_4 (
    .in0(out_17[5:0]), .in1(out_18), .out(multiplexer_4_out), .sel(T));  // open: en
  REG_FILE reg_file_1 (.in_1(register_6_q), .REG_num(Reg), .CLOCK(and_2_out), .out_4(reg_file_1_out_4));
  Comparator #(.width(10)) comparator_1 (.a(10'hf), .b(out_21), .gt(comparator_1_gt));  // open: eq, lt
  Register #(.width(10)) register_3 (.D(multiplexer_3_out), .Q(AdReg), .clk(not_3_out), .clr(HLT));  // open: en
  not not_3 (not_3_out, and_3_out);
  Multiplexer #(.width(6)) multiplexer_5 (
    .in0(multiplexer_4_out), .in1(6'b000111), .out(multiplexer_5_out), .sel(not_4_out));  // open: en
  or or_5 (or_5_out, comparator_1_gt, T);
  not not_4 (not_4_out, or_5_out);
  Comparator #(.width(10)) comparator_2 (.a(10'h5), .b(AdReg), .gt(comparator_2_gt));  // open: eq, lt
  Bit_Extender #(.in_width(10), .out_width(2)) bit_extender_1 (.in(AdReg), .out(bit_extender_1_out));
  Register #(.width(6)) register_4 (.D(multiplexer_5_out), .Q(out_22), .clk(f_1_out_2));  // open: en, clr
  f f_1 (.in_1(not_3_out), .out_2(f_1_out_2));
  Multiplexer #(.width(2)) multiplexer_6 (
    .in0(2'b00), .in1(bit_extender_1_out), .out(multiplexer_6_out), .sel(comparator_2_gt));  // open: en
  and and_3 (and_3_out, ~Takt, TaktKom, clock_1_out);  // AND_Gate
  \АЛУ  \u_алу_1  (
    .in_1(register_6_q), .in_2(reg_file_1_out_4), .out_5(\алу_1_out_5 ), .in_3(ALU_INSTR),
    .out_4(\алу_1_out_4 ));
  or or_6 (or_6_out, FlagAdr, FlagAdrO);
  Counter #(.width(10), .max('h2f), .ongoal("stay")) counter_3 (
    .load(FlagAdr), .D(AdReg), .count(not_5_out), .Q(counter_3_q), .clk(f_3_out_2), .clr(HLT));  // open: carry
  not not_5 (not_5_out, FlagAdr);
  Multiplexer #(.width(2)) multiplexer_7 (
    .in0(Reg_num_t), .in1(multiplexer_6_out), .out(multiplexer_7_out), .sel(MOV_t));  // open: en
  f f_2 (.in_1(or_7_out), .out_2(f_2_out_2));
  or or_7 (or_7_out, MOV_t, RecReg);
  Multiplexer #(.select(2), .width(16)) multiplexer_8 (
    .in0(out_20), .in1(out_17), .in2(\алу_1_out_5 ), .in3(reg_file_1_out_4), .out(multiplexer_8_out),
    .sel(multiplexer_2_out));  // open: en
  Multiplexer #(.width(10)) multiplexer_9 (.in0(counter_3_q), .in1(AdReg), .out(out_21), .sel(or_6_out));  // open: en
  Register #(.width(2)) register_5 (.D(multiplexer_7_out), .Q(Reg), .clk(f_2_out_2));  // open: en, clr
  // Probe on register_6_q
  Register #(.width(16)) register_6 (.D(multiplexer_8_out), .Q(register_6_q), .clk(and_4_out));  // open: en, clr
  and and_4 (and_4_out, and_3_out, or_8_out);
  or or_8 (or_8_out, INP, MOV_t, Alu_t, LDO_t, OUT_t);
  f f_3 (.in_1(and_5_out), .out_2(f_3_out_2));
  Register #(.width(6)) register_7 (.D(\алу_1_out_4 ), .Q(Flags), .clk(and_3_out));  // open: en, clr
  and and_5 (and_5_out, ~FlagAdrO, and_3_out);  // AND_Gate
  // Probe on out_16
  Register #(.width(16), .trigger("falling")) register_8 (.D(register_6_q), .Q(out_16), .clk(OUT_t));  // open: en, clr
  Counter #(.width(1), .max('h1), .ongoal("stay")) counter_4 (
    .Q(T), .clk(and_6_out), .clr(counter_6_q));  // open: load, D, count, carry
  and and_6 (and_6_out, TaktKom, and_3_out);
  not not_6 (not_6_out, TaktKom);
  Counter #(.width(3), .max('h5), .ongoal("stay")) counter_5 (
    .Q(counter_5_q), .clk(clock_1_out));  // open: load, D, count, carry, clr
  Counter #(.width(1), .max('h1), .ongoal("stay"), .trigger("falling")) counter_6 (
    .Q(counter_6_q), .clk(and_3_out), .clr(not_6_out));  // open: load, D, count, carry
  Counter #(.width(1), .max('h1), .ongoal("stay"), .trigger("falling")) counter_7 (
    .Q(Takt), .clk(OUT_t), .clr(not_7_out));  // open: load, D, count, carry
  not not_7 (not_7_out, or_9_out);
  // Probe on out_16
  and and_7 (and_7_out, counter_5_q[0], ~counter_5_q[1], counter_5_q[2]);  // AND_Gate
  and and_8 (and_8_out, and_7_out, and_9_out);
  TTY #(.trigger("falling")) tty_2 (.data(multiplexer_11_out), .clk(f_4_out_2), .clr(in_1));  // open: we
  f f_4 (.in_1(and_8_out), .out_2(f_4_out_2));
  // Probe on out_16[3:0]
  Register #(.width(4)) register_9 (.D(out_16[15:12]), .Q(register_9_q), .clk(clock_1_out));  // open: en, clr
  Counter #(.width(3), .max('h4), .ongoal("stay")) counter_8 (
    .Q(counter_8_q), .clk(clock_1_out), .clr(OUT_t));  // open: load, D, count, carry
  Register #(.width(4)) register_10 (.D(out_16[11:8]), .Q(register_10_q), .clk(clock_1_out));  // open: en, clr
  Register #(.width(4)) register_11 (.D(out_16[7:4]), .Q(register_11_q), .clk(clock_1_out));  // open: en, clr
  and and_9 (and_9_out, clock_1_out, or_9_out);
  or or_9 (or_9_out, counter_8_q[0], counter_8_q[1], ~counter_8_q[2]);  // OR_Gate
  Register #(.width(4)) register_12 (.D(out_16[3:0]), .Q(register_12_q), .clk(clock_1_out));  // open: en, clr
  Register #(.width(7)) register_13 (.D(7'b0100000), .Q(register_13_q), .clk(clock_1_out));  // open: en, clr
  Counter #(.width(2), .max('h3), .ongoal("stay")) counter_9 (
    .Q(counter_9_q), .clk(and_9_out), .clr(OUT_t));  // open: load, D, count, carry
  Multiplexer #(.select(2), .width(4)) multiplexer_10 (
    .in0(register_9_q), .in1(register_10_q), .in2(register_11_q), .in3(register_12_q),
    .out(multiplexer_10_out), .sel(counter_9_q));  // open: en
  OutHex outhex_1 (
    .x0(multiplexer_10_out[3]), .y0(outhex_1_y6[6]), .x1(multiplexer_10_out[2]), .x2(multiplexer_10_out[1]),
    .y1(outhex_1_y6[5]), .x3(multiplexer_10_out[0]), .y2(outhex_1_y6[4]), .y3(outhex_1_y6[3]),
    .y4(outhex_1_y6[2]), .y5(outhex_1_y6[1]), .y6(outhex_1_y6[0]));
  // Probe on multiplexer_11_out
  Multiplexer #(.width(7)) multiplexer_11 (
    .in0(outhex_1_y6), .in1(register_13_q), .out(multiplexer_11_out), .sel(not_8_out));  // open: en
  not not_8 (not_8_out, or_9_out);

  // Other names for the same wires on the sheet: ADRESS[9:0] = out_19; INSTR[5:0] = out_22; INSTRK[5:0] = out_18;
  //   NUMBER[15:0] = out_20; А[9:0] = out_21

  // Notes on the sheet:
  //   READ
  //   CLEAR
  //   По аски
  //   Выбор устройство
  //   Устройство ввода
  //   00
  //   01
  //   Записать в память
  //   Записать в регистр
  //   11
  //   INSTR
  //   10
  //   ADRESS
  //   Выбор регистра
  //   Записать в TEMP
  //   Выбрать адресс памяти
  //   TEMP
  //   FLAGS
  //   OUT
endmodule

module \АЛУ  (
  input  [15:0] in_1,
  input  [15:0] in_2,
  input  [3:0] in_3,
  output [5:0] out_4,
  output [15:0] out_5
);

  wire [15:0] adder_1_out, and_1_out, multiplexer_1_out, not_1_out, or_1_out, shifter_1_out, shifter_2_out,
       subtractor_1_out, xor_1_out;

  // Probe on multiplexer_1_out
  Multiplexer #(.width(16)) multiplexer_1 (
    .in0(in_1), .in1(not_1_out), .out(multiplexer_1_out), .sel(in_3[3]));  // open: en
  assign not_1_out = ~in_1;  // NOT_Gate not_1, 16 bits wide
  // Probe on in_2
  Adder #(.width(16)) adder_1 (.a(multiplexer_1_out), .b(in_2), .out(adder_1_out), .cout(out_4[0]));  // open: cin
  Subtractor #(.width(16)) subtractor_1 (
    .a(multiplexer_1_out), .b(in_2), .out(subtractor_1_out), .bout(out_4[1]));  // open: bin
  Shifter #(.width(16)) shifter_1 (.in(multiplexer_1_out), .\dist (4'b0001), .out(shifter_1_out));
  Shifter #(.width(16), .shift("lr")) shifter_2 (.in(multiplexer_1_out), .\dist (4'b0001), .out(shifter_2_out));
  assign and_1_out = multiplexer_1_out & in_2;  // AND_Gate and_1, 16 bits wide
  assign or_1_out = multiplexer_1_out | in_2;  // OR_Gate or_1, 16 bits wide
  assign xor_1_out = multiplexer_1_out ^ in_2;  // XOR_Gate xor_1, 16 bits wide
  Multiplexer #(.select(3), .width(16)) multiplexer_2 (
    .in0(multiplexer_1_out), .in1(adder_1_out), .in2(subtractor_1_out), .in3(and_1_out), .in4(or_1_out),
    .in5(xor_1_out), .in6(shifter_1_out), .in7(shifter_2_out), .out(out_5), .sel(in_3[2:0]));  // open: en
  Comparator #(.width(16)) comparator_1 (.a(out_5), .b({16{1'b0}}), .eq(out_4[2]));  // open: gt, lt
  Comparator #(.width(16)) comparator_2 (.a(multiplexer_1_out), .b(in_2), .gt(out_4[3]), .eq(out_4[4]), .lt(out_4[5]));
  // Probe on out_5
  // OR_Gate or_2 has open pins: in0=out_5[8], in1=out_5[15], in2=out_5[14], in3=out_5[13], in4=out_5[12], in5=out_5[11], in6=out_5[10], in7=out_5[9], in8=out_5[7], in9=out_5[6], in10=out_5[5], in11=out_5[4], in12=out_5[3], in13=out_5[2], in14=out_5[1], in15=out_5[0], out=open
  // Probe on out_4

  // Notes on the sheet:
  //   A
  //   B
  //   0 - Переполнение 
  //   1 - Флаг отрицательного
  //   2 - нуля
  //   3 - a > b
  //   4 - a = b
  //   5 - a < b
  //   Output
  //   FLGS
endmodule

module REG_FILE (
  input  [15:0] in_1,
  input  [1:0] REG_num,
  input  CLOCK,
  output [15:0] out_4
);

  wire demultiplexer_1_out0, demultiplexer_1_out1, demultiplexer_1_out2, demultiplexer_1_out3;
  wire [15:0] register_1_q, register_2_q, register_3_q, register_4_q;

  Register #(.width(16)) register_1 (.D(in_1), .en(demultiplexer_1_out0), .Q(register_1_q), .clk(CLOCK));  // open: clr
  Register #(.width(16)) register_2 (.D(in_1), .en(demultiplexer_1_out1), .Q(register_2_q), .clk(CLOCK));  // open: clr
  Demultiplexer #(.select(2)) demultiplexer_1 (
    .out0(demultiplexer_1_out0), .out1(demultiplexer_1_out1), .out2(demultiplexer_1_out2),
    .out3(demultiplexer_1_out3), .in(1'b1), .sel(REG_num));  // open: en
  Register #(.width(16)) register_3 (.D(in_1), .en(demultiplexer_1_out2), .Q(register_3_q), .clk(CLOCK));  // open: clr
  Register #(.width(16)) register_4 (.D(in_1), .en(demultiplexer_1_out3), .Q(register_4_q), .clk(CLOCK));  // open: clr
  Multiplexer #(.select(2), .width(16)) multiplexer_1 (
    .in0(register_1_q), .in1(register_2_q), .in2(register_3_q), .in3(register_4_q), .out(out_4), .sel(REG_num));  // open: en

  // Notes on the sheet:
  //   WR_REG
  //   RESET
  //   RegA 
  //   Reg B
  //   Reg C
  //   Reg D
endmodule

module d (
  input  q1,
  output w0,
  output w1,
  output w2,
  output w3,
  output w4,
  output w5,
  output w6
);


  assign w0 = 1'b0;
  assign w1 = 1'b0;
  assign w2 = 1'b0;
  assign w3 = 1'b0;
  assign w4 = 1'b0;
  assign w5 = 1'b0;
  assign w6 = q1;
endmodule

module INPDEC (
  input  in_1,
  output [1:0] out_2,
  output out_3
);

  Demultiplexer #(.width(3)) demultiplexer_1 (.out1({out_3, out_2}), .in(3'b001), .sel(in_1));  // open: out0, en
endmodule

module ALU_DEC (
  input  [5:0] in_1,
  output [3:0] out_2,
  output [1:0] out_3,
  output out_4
);

  wire comparator_1_eq, comparator_2_eq;

  Register #(.width(4)) register_1 (.D(in_1[3:0]), .Q(out_2), .clk(out_4));  // open: en, clr
  Comparator #(.width(2)) comparator_1 (.a({in_1[4], in_1[5]}), .b(2'b10), .eq(comparator_1_eq));  // open: gt, lt
  Comparator #(.width(4)) comparator_2 (.a(in_1[3:0]), .b(4'b0000), .eq(comparator_2_eq));  // open: gt, lt
  and and_1 (out_4, comparator_1_eq, ~comparator_2_eq);  // AND_Gate

  assign out_3 = {in_1[4], in_1[5]};
endmodule

module REG_DEC (
  input  [5:0] in_1,
  output [1:0] out_2,
  output Flag,
  output [1:0] out_4
);

  and and_1 (Flag, in_1[2], ~in_1[3], in_1[4], in_1[5]);  // AND_Gate
  Register #(.width(2)) register_1 (.D(in_1[1:0]), .Q(out_2), .clk(Flag));  // open: en, clr
  Register #(.width(2)) register_2 (.D(in_1[5:4]), .Q(out_4), .clk(Flag));  // open: en, clr

  // Notes on the sheet:
  //   Выбор регистра
  //   Выбор устройства
endmodule

module Flag_DEC (
  input  [5:0] in_1,
  output out_2,
  output [2:0] \Флаг ,
  output \Флаг_вкл 
);

  and and_1 (out_2, in_1[0], in_1[1], in_1[2], in_1[3], ~in_1[4], ~in_1[5]);  // AND_Gate
  and and_2 (\Флаг_вкл , in_1[3], ~in_1[4], ~in_1[5]);  // AND_Gate

  assign \Флаг  = in_1[2:0];

  // Notes on the sheet:
  //   Безусловный переход
endmodule

module InstrFl (
  input  [5:0] in_1,
  input  [2:0] in_2,
  input  Falg_On,
  output Flag
);

  wire and_1_out, and_2_out, and_3_out, and_4_out, and_5_out, and_6_out, comparator_1_eq, comparator_2_eq,
       comparator_3_eq, comparator_4_eq, comparator_5_eq, comparator_6_eq, or_1_out;

  Comparator #(.width(3)) comparator_1 (.a(in_2), .b(3'b000), .eq(comparator_1_eq));  // open: gt, lt
  Comparator #(.width(3)) comparator_2 (.a(in_2), .b(3'b001), .eq(comparator_2_eq));  // open: gt, lt
  Comparator #(.width(3)) comparator_3 (.a(in_2), .b(3'b010), .eq(comparator_3_eq));  // open: gt, lt
  Comparator #(.width(3)) comparator_4 (.a(in_2), .b(3'b011), .eq(comparator_4_eq));  // open: gt, lt
  Comparator #(.width(3)) comparator_5 (.a(in_2), .b(3'b100), .eq(comparator_5_eq));  // open: gt, lt
  Comparator #(.width(3)) comparator_6 (.a(in_2), .b(3'b101), .eq(comparator_6_eq));  // open: gt, lt
  and and_1 (and_1_out, in_1[0], comparator_1_eq);
  and and_2 (and_2_out, in_1[1], comparator_2_eq);
  and and_3 (and_3_out, in_1[2], comparator_3_eq);
  and and_4 (and_4_out, in_1[3], comparator_4_eq);
  and and_5 (and_5_out, in_1[4], comparator_5_eq);
  and and_6 (and_6_out, in_1[5], comparator_6_eq);
  or or_1 (or_1_out, and_1_out, and_2_out, and_3_out, and_4_out, and_5_out, and_6_out);
  and and_7 (Flag, or_1_out, Falg_On);
endmodule

module \ОЗУ_DEC  (
  input  [5:0] in_1,
  output MV,
  output INP,
  output OUT,
  output MOV,
  output LDO,
  output STO,
  output [1:0] SelDev,
  output Flag
);

  wire and_1_out, buffer_1_out, buffer_2_out, buffer_3_out;

  SelDEV seldev_1 (.x0(in_1[0]), .x1(in_1[1]), .x2(in_1[2]), .y0(SelDev[0]), .y1(SelDev[1]));
  and and_1 (and_1_out, ~in_1[3], ~in_1[4], ~in_1[5]);  // AND_Gate
  buf buffer_1 (buffer_1_out, in_1[0]);
  buf buffer_2 (buffer_2_out, in_1[1]);
  buf buffer_3 (buffer_3_out, in_1[2]);
  and and_2 (MV, ~in_1[0], ~in_1[1], ~in_1[2], ~in_1[3], in_1[4], ~in_1[5]);  // AND_Gate
  and and_3 (INP, in_1[0], ~in_1[1], ~in_1[2], and_1_out);  // AND_Gate
  and and_4 (OUT, ~buffer_1_out, buffer_2_out, ~buffer_3_out, and_1_out);  // AND_Gate
  and and_5 (MOV, in_1[0], in_1[1], ~in_1[2], and_1_out);  // AND_Gate
  and and_6 (LDO, ~in_1[0], ~in_1[1], in_1[2], and_1_out);  // AND_Gate
  and and_7 (STO, in_1[0], ~in_1[1], in_1[2], and_1_out);  // AND_Gate
  or or_1 (Flag, INP, OUT, LDO, STO);

  // Notes on the sheet:
  //   В адр
endmodule

module SelDEV (
  input  x0,
  input  x1,
  input  x2,
  output y0,
  output y1
);

  wire and_1_out, and_2_out, not_1_out, not_2_out, not_3_out;

  not not_1 (not_1_out, x1);
  not not_2 (not_2_out, x2);
  not not_3 (not_3_out, x2);
  and and_1 (and_1_out, not_1_out, x2);
  and and_2 (and_2_out, x1, not_2_out);
  and and_3 (y1, x0, x1, not_3_out);
  or or_1 (y0, and_1_out, and_2_out);
endmodule

module f (
  input  in_1,
  output out_2
);

  wire buffer_1_out, buffer_2_out, buffer_3_out, buffer_4_out, buffer_5_out, buffer_6_out, buffer_7_out,
       buffer_8_out, buffer_9_out, buffer_10_out, buffer_11_out;

  buf buffer_1 (buffer_1_out, buffer_3_out);
  buf buffer_2 (buffer_2_out, buffer_1_out);
  buf buffer_3 (buffer_3_out, in_1);
  buf buffer_4 (buffer_4_out, buffer_6_out);
  buf buffer_5 (buffer_5_out, buffer_4_out);
  buf buffer_6 (buffer_6_out, buffer_2_out);
  buf buffer_7 (buffer_7_out, buffer_5_out);
  buf buffer_8 (buffer_8_out, buffer_9_out);
  buf buffer_9 (buffer_9_out, buffer_7_out);
  buf buffer_10 (buffer_10_out, buffer_8_out);
  buf buffer_11 (buffer_11_out, buffer_10_out);
  buf buffer_12 (out_2, buffer_11_out);
endmodule

module OutHex (
  input  x0,
  input  x1,
  input  x2,
  input  x3,
  output y0,
  output y1,
  output y2,
  output y3,
  output y4,
  output y5,
  output y6
);

  wire and_1_out, and_2_out, and_3_out, and_4_out, and_6_out, and_7_out, and_8_out, and_9_out, and_10_out,
       and_11_out, and_12_out, and_13_out, and_14_out, and_15_out, not_1_out, not_2_out, not_3_out,
       not_4_out, not_5_out, not_6_out, not_7_out, not_8_out, not_9_out, not_10_out, not_11_out, not_12_out,
       not_13_out, not_14_out, not_15_out, not_16_out, not_17_out;

  and and_1 (and_1_out, x0, x2);
  and and_2 (and_2_out, x0, x1);
  not not_1 (not_1_out, x0);
  not not_2 (not_2_out, x1);
  and and_3 (and_3_out, not_2_out, not_3_out);
  not not_3 (not_3_out, x2);
  not not_4 (not_4_out, x0);
  not not_5 (not_5_out, x1);
  and and_4 (and_4_out, not_5_out, not_6_out);
  not not_6 (not_6_out, x2);
  not not_7 (not_7_out, x1);
  and and_5 (y3, x0, not_7_out, not_8_out);
  not not_8 (not_8_out, x2);
  not not_9 (not_9_out, x0);
  and and_6 (and_6_out, not_9_out, x1);
  and and_7 (and_7_out, x1, x3);
  and and_8 (and_8_out, x1, x2);
  not not_10 (not_10_out, x0);
  not not_11 (not_11_out, x2);
  not not_12 (not_12_out, x3);
  not not_13 (not_13_out, x0);
  and and_9 (and_9_out, not_13_out, x3);
  not not_14 (not_14_out, x1);
  and and_10 (and_10_out, not_14_out, not_15_out, x3);
  not not_15 (not_15_out, x2);
  and and_11 (and_11_out, x0, x2, not_16_out);
  not not_16 (not_16_out, x3);
  and and_12 (and_12_out, x0, x1, not_17_out);
  not not_17 (not_17_out, x3);
  or or_1 (y0, and_1_out, and_2_out);
  or or_2 (y1, not_1_out, and_3_out);
  or or_3 (y2, not_4_out, and_4_out);
  or or_4 (y4, and_6_out, and_7_out, and_8_out);
  and and_13 (and_13_out, not_10_out, x2);
  and and_14 (and_14_out, x2, x3);
  or or_5 (y5, and_13_out, and_14_out, and_15_out);
  and and_15 (and_15_out, x0, x1, not_11_out, not_12_out);
  or or_6 (y6, and_9_out, and_10_out, and_11_out, and_12_out);
endmodule

module Takt1 (
  input  x0,
  input  x1,
  input  x2,
  output y0
);

  wire and_1_out, not_1_out, not_2_out;

  not not_1 (not_1_out, x1);
  not not_2 (not_2_out, x2);
  and and_1 (and_1_out, not_1_out, not_2_out);
  or or_1 (y0, and_1_out, x0);
endmodule
