// Logisim project БВТ2003_Тураев_Некруз_№1.circ as structural Verilog: 3 circuits, main circuit main
module main (
  input  in_1,
  input  in_2,
  output out_3,
  output out_4
);

  xor xor_1 (out_3, in_1, in_2);
  and and_1 (out_4, in_1, in_2);
endmodule

module \полусумматор  (
  input  in_1,
  input  in_2,
  input  in_3,
  output out_4,
  output out_5
);

  wire main_1_out_3, main_1_out_4, main_2_out_4;

  main main_1 (.in_1(in_2), .out_3(main_1_out_3), .in_2(in_3), .out_4(main_1_out_4));
  main main_2 (.in_1(in_1), .out_3(out_4), .in_2(main_1_out_3), .out_4(main_2_out_4));
  or or_1 (out_5, main_2_out_4, main_1_out_4);
endmodule

module \Сумматор  (
  input  in_1,
  input  in_2,
  input  in_3,
  input  in_4,
  input  in_5,
  input  in_6,
  input  in_7,
  input  in_8,
  input  in_9,
  input  in_10,
  input  in_11,
  input  in_12,
  input  in_13,
  input  in_14,
  input  in_15,
  input  in_16,
  output out_17,
  output out_18,
  output out_19,
  output out_20,
  output out_21,
  output out_22,
  output out_23,
  output out_24,
  output out_25
);

  wire \полусумматор_2_out_4 , \полусумматор_3_out_4 , \полусумматор_4_out_4 , \полусумматор_5_out_4 ,
       \полусумматор_6_out_4 , \полусумматор_7_out_4 , \полусумматор_8_out_4 ;

  \полусумматор  \u_полусумматор_1  (
    .in_1(\полусумматор_2_out_4 ), .out_4(out_17), .in_2(in_1), .out_5(out_18), .in_3(in_2));
  \полусумматор  \u_полусумматор_2  (
    .in_1(\полусумматор_3_out_4 ), .out_4(\полусумматор_2_out_4 ), .in_2(in_3), .out_5(out_19), .in_3(in_4));
  \полусумматор  \u_полусумматор_3  (
    .in_1(\полусумматор_4_out_4 ), .out_4(\полусумматор_3_out_4 ), .in_2(in_5), .out_5(out_20), .in_3(in_6));
  \полусумматор  \u_полусумматор_4  (
    .in_1(\полусумматор_5_out_4 ), .out_4(\полусумматор_4_out_4 ), .in_2(in_7), .out_5(out_21), .in_3(in_8));
  \полусумматор  \u_полусумматор_5  (
    .in_1(\полусумматор_6_out_4 ), .out_4(\полусумматор_5_out_4 ), .in_2(in_9), .out_5(out_22), .in_3(in_10));
  \полусумматор  \u_полусумматор_6  (
    .in_1(\полусумматор_7_out_4 ), .out_4(\полусумматор_6_out_4 ), .in_2(in_11), .out_5(out_23), .in_3(in_12));
  \полусумматор  \u_полусумматор_7  (
    .in_1(\полусумматор_8_out_4 ), .out_4(\полусумматор_7_out_4 ), .in_2(in_13), .out_5(out_24), .in_3(in_14));
  \полусумматор  \u_полусумматор_8  (
    .in_1(1'b0), .out_4(\полусумматор_8_out_4 ), .in_2(in_15), .out_5(out_25), .in_3(in_16));
endmodule
