// Logisim project БВТ2003_Тураев_Некруз_№10(Star).circ as structural Verilog: 14 circuits, main circuit Компилятор
module \Компилятор  (
  output [5:0] out_1,
  output [9:0] out_2,
  output [15:0] out_3
);

  wire button_1_out, button_2_out, Clear, clock_1_out, instr_1_out_5, read_1_out_3;
  wire [6:0] keyboard_1_data;

  Button button_1 (.out(button_1_out));
  Button button_2 (.out(button_2_out));
  Clock clock_1 (.out(clock_1_out));
  Read read_1 (.in_2(button_1_out), .out_3(read_1_out_3), .out_4(Clear), .in_1(clock_1_out));
  Keyboard keyboard_1 (.clk(read_1_out_3), .clr(button_2_out), .data(keyboard_1_data));  // open: re, avail
  // Probe on keyboard_1_data
  TTY tty_1 (.data(keyboard_1_data), .clk(read_1_out_3), .clr(button_2_out));  // open: we
  INSTR instr_1 (
    .Simbol(keyboard_1_data), .out_4(out_1), .Takt(read_1_out_3), .in_3(Clear), .out_5(instr_1_out_5),
    .out_6(out_3));
  ADR adr_1 (.in_2(keyboard_1_data), .in_3(read_1_out_3), .out_4(out_2), .in_1(instr_1_out_5));
  // Probe on out_1
  // Probe on out_2
  // Probe on out_3

  // Other names for the same wires on the sheet: ADRESS[9:0] = out_2; INSTR[5:0] = out_1; NUMBER[15:0] = out_3

  // Notes on the sheet:
  //   READ
  //   CLEAR
  //   По аски
endmodule

module INP (
  input  q1,
  output w0,
  output w1,
  output w2,
  output w3,
  output w4,
  output w5,
  output out_8
);


  assign w0 = 1'b0;
  assign w1 = 1'b0;
  assign w2 = 1'b0;
  assign w3 = 1'b0;
  assign w4 = 1'b0;
  assign w5 = 1'b0;
endmodule

module XexDec (
  input  y0,
  input  y1,
  input  y2,
  input  y3,
  input  y4,
  input  y5,
  input  y6,
  output x0,
  output x1,
  output x2,
  output x3,
  output x4
);

  wire and_1_out, and_2_out, and_3_out, and_4_out, and_5_out, and_6_out, and_7_out, and_8_out, and_9_out,
       and_10_out, and_11_out, and_12_out, and_13_out, and_14_out, and_15_out, and_16_out, and_17_out,
       and_18_out, and_19_out, and_20_out, and_21_out, and_22_out, and_23_out, and_24_out, and_25_out,
       and_26_out, and_27_out, and_28_out, and_29_out, and_30_out, and_31_out, and_32_out, and_33_out,
       and_34_out, and_35_out, and_36_out, and_37_out, and_38_out, and_39_out, and_40_out, and_41_out,
       not_1_out, not_2_out, not_3_out, not_4_out, not_5_out, not_6_out, not_7_out, not_8_out, not_9_out,
       not_10_out, not_11_out, not_12_out, not_13_out, not_14_out, not_15_out, not_16_out, not_17_out,
       not_18_out, not_19_out, not_20_out, not_21_out, not_22_out, not_23_out, not_24_out, not_25_out,
       not_26_out, not_27_out, not_28_out, not_29_out, not_30_out, not_31_out, not_32_out, not_33_out,
       not_34_out, not_35_out, or_1_out, or_2_out, or_4_out, or_5_out, or_6_out, or_7_out, or_8_out,
       or_9_out, or_10_out, or_11_out, or_12_out, or_13_out, or_14_out, or_15_out, or_16_out, or_17_out,
       or_18_out, or_19_out, or_20_out, or_21_out, or_22_out, or_23_out, or_24_out, or_25_out, or_26_out,
       or_29_out, or_30_out;

  not not_1 (not_1_out, y1);
  not not_2 (not_2_out, y4);
  not not_3 (not_3_out, y5);
  not not_4 (not_4_out, y6);
  not not_5 (not_5_out, y1);
  not not_6 (not_6_out, y1);
  not not_7 (not_7_out, y2);
  not not_8 (not_8_out, y1);
  not not_9 (not_9_out, y5);
  not not_10 (not_10_out, y1);
  not not_11 (not_11_out, y1);
  not not_12 (not_12_out, y4);
  not not_13 (not_13_out, y1);
  not not_14 (not_14_out, y0);
  not not_15 (not_15_out, y1);
  and and_1 (and_1_out, not_1_out, not_2_out);
  and and_2 (and_2_out, not_3_out, not_4_out);
  and and_3 (and_3_out, not_5_out, y4);
  and and_4 (and_4_out, y5, y6);
  not not_16 (not_16_out, y1);
  not not_17 (not_17_out, y2);
  or or_1 (or_1_out, not_6_out, not_7_out);
  or or_2 (or_2_out, y3, y0);
  not not_18 (not_18_out, y0);
  not not_19 (not_19_out, y1);
  and and_5 (and_5_out, not_8_out, not_9_out);
  not not_20 (not_20_out, y6);
  and and_6 (and_6_out, not_10_out, y5);
  not not_21 (not_21_out, y1);
  not not_22 (not_22_out, y2);
  not not_23 (not_23_out, y0);
  not not_24 (not_24_out, y1);
  and and_7 (and_7_out, not_11_out, not_12_out);
  not not_25 (not_25_out, y5);
  not not_26 (not_26_out, y1);
  not not_27 (not_27_out, y1);
  not not_28 (not_28_out, y6);
  not not_29 (not_29_out, y0);
  and and_8 (and_8_out, not_13_out, y4);
  not not_30 (not_30_out, y1);
  not not_31 (not_31_out, y2);
  and and_9 (and_9_out, not_14_out, not_15_out);
  and and_10 (and_10_out, and_1_out, and_2_out);
  and and_11 (and_11_out, and_3_out, and_4_out);
  and and_12 (and_12_out, not_16_out, y3);
  and and_13 (and_13_out, y3, y5);
  and and_14 (and_14_out, y3, y4);
  and and_15 (and_15_out, y1, not_17_out);
  and and_16 (and_16_out, y0, y2);
  or or_3 (x1, or_1_out, or_2_out);
  and and_17 (and_17_out, not_18_out, not_19_out);
  and and_18 (and_18_out, and_5_out, not_20_out);
  and and_19 (and_19_out, and_6_out, y6);
  and and_20 (and_20_out, not_21_out, y3);
  and and_21 (and_21_out, y3, y5);
  and and_22 (and_22_out, y1, not_22_out);
  and and_23 (and_23_out, y0, y2);
  and and_24 (and_24_out, not_23_out, not_24_out);
  and and_25 (and_25_out, and_7_out, not_25_out);
  not not_32 (not_32_out, y0);
  not not_33 (not_33_out, y6);
  and and_26 (and_26_out, not_26_out, y4);
  not not_34 (not_34_out, y1);
  not not_35 (not_35_out, y2);
  and and_27 (and_27_out, not_27_out, not_28_out);
  and and_28 (and_28_out, not_29_out, y6);
  and and_29 (and_29_out, and_8_out, y5);
  and and_30 (and_30_out, not_30_out, y3);
  and and_31 (and_31_out, y3, y5);
  and and_32 (and_32_out, y3, y4);
  and and_33 (and_33_out, y1, not_31_out);
  and and_34 (and_34_out, y0, y2);
  or or_4 (or_4_out, and_9_out, and_10_out);
  or or_5 (or_5_out, and_11_out, and_12_out);
  or or_6 (or_6_out, and_13_out, and_14_out);
  or or_7 (or_7_out, and_15_out, and_16_out);
  or or_8 (or_8_out, and_17_out, and_18_out);
  or or_9 (or_9_out, and_19_out, y4);
  or or_10 (or_10_out, and_20_out, and_21_out);
  or or_11 (or_11_out, and_22_out, and_23_out);
  or or_12 (or_12_out, and_24_out, and_25_out);
  and and_35 (and_35_out, not_32_out, y5);
  and and_36 (and_36_out, y5, not_33_out);
  and and_37 (and_37_out, and_26_out, y6);
  and and_38 (and_38_out, not_34_out, y3);
  and and_39 (and_39_out, y3, y4);
  and and_40 (and_40_out, y1, not_35_out);
  and and_41 (and_41_out, y0, y2);
  or or_13 (or_13_out, and_27_out, and_28_out);
  or or_14 (or_14_out, and_29_out, and_30_out);
  or or_15 (or_15_out, and_31_out, and_32_out);
  or or_16 (or_16_out, and_33_out, and_34_out);
  or or_17 (or_17_out, or_4_out, or_5_out);
  or or_18 (or_18_out, or_6_out, or_7_out);
  or or_19 (or_19_out, or_8_out, or_9_out);
  or or_20 (or_20_out, or_10_out, or_11_out);
  or or_21 (or_21_out, or_12_out, and_35_out);
  or or_22 (or_22_out, and_36_out, and_37_out);
  or or_23 (or_23_out, and_38_out, and_39_out);
  or or_24 (or_24_out, and_40_out, and_41_out);
  or or_25 (or_25_out, or_13_out, or_14_out);
  or or_26 (or_26_out, or_15_out, or_16_out);
  or or_27 (x0, or_17_out, or_18_out);
  or or_28 (x2, or_19_out, or_20_out);
  or or_29 (or_29_out, or_21_out, or_22_out);
  or or_30 (or_30_out, or_23_out, or_24_out);
  or or_31 (x4, or_25_out, or_26_out);
  or or_32 (x3, or_29_out, or_30_out);
endmodule

module ADR (
  input  in_1,
  input  [6:0] in_2,
  input  in_3,
  output [9:0] out_4
);

  wire and_3_out, and_4_out, not_1_out, not_2_out, not_3_out, not_4_out, not_5_out, not_6_out, xexdec_1_x0;
  wire [3:0] register_1_q, register_2_q, register_3_q, xexdec_1_x4;
  wire [11:0] register_4_q;

  XexDec xexdec_1 (
    .y0(in_2[6]), .y1(in_2[5]), .y2(in_2[4]), .y3(in_2[3]), .y4(in_2[2]), .y5(in_2[1]), .y6(in_2[0]),
    .x0(xexdec_1_x0), .x1(xexdec_1_x4[3]), .x2(xexdec_1_x4[2]), .x3(xexdec_1_x4[1]), .x4(xexdec_1_x4[0]));
  // Probe on xexdec_1_x4
  // Probe on xexdec_1_x0
  not not_1 (not_1_out, in_1);
  // AND_Gate and_1 has open pins: in0=in_1, in1=xexdec_1_x0, in2=in_3, out=open
  not not_2 (not_2_out, xexdec_1_x0);
  // AND_Gate and_2 has open pins: in0=not_2_out, in1=in_3, out=open
  not not_3 (not_3_out, xexdec_1_x0);
  and and_3 (and_3_out, not_3_out, in_3);
  not not_4 (not_4_out, in_1);
  Register #(.width(4), .trigger("falling")) register_1 (
    .D(xexdec_1_x4), .Q(register_1_q), .clk(and_4_out), .clr(not_4_out));  // open: en
  Register #(.width(4), .trigger("falling")) register_2 (
    .D(register_1_q), .Q(register_2_q), .clk(and_4_out), .clr(not_4_out));  // open: en
  Register #(.width(4), .trigger("falling")) register_3 (
    .D(register_2_q), .Q(register_3_q), .clk(and_4_out), .clr(not_4_out));  // open: en
  not not_5 (not_5_out, xexdec_1_x0);
  not not_6 (not_6_out, in_3);
  and and_4 (and_4_out, not_5_out, not_6_out);
  // Probe on {register_3_q, register_2_q, register_1_q}
  Register #(.width(12)) register_4 (
    .D({register_3_q, register_2_q, register_1_q}), .Q(register_4_q), .clk(in_3), .clr(not_1_out));  // open: en
  Bit_Extender #(.in_width(12), .out_width(10)) bit_extender_1 (.in(register_4_q), .out(out_4));
  // Probe on out_4
endmodule

module \Ф  (
  input  in_1,
  output out_2
);

  wire not_1_out, not_2_out, not_3_out, not_4_out, not_5_out, not_6_out, not_7_out;

  not not_1 (not_1_out, in_1);
  not not_2 (not_2_out, not_3_out);
  not not_3 (not_3_out, not_1_out);
  not not_4 (not_4_out, not_2_out);
  not not_5 (not_5_out, not_6_out);
  not not_6 (not_6_out, not_4_out);
  not not_7 (not_7_out, not_5_out);
  not not_8 (out_2, not_7_out);
endmodule

module Count (
  input  \у0 ,
  input  \у1 ,
  input  y2,
  output x1
);


  assign x1 = \у0 ;
endmodule

module INSTR (
  input  Takt,
  input  [6:0] Simbol,
  input  in_3,
  output [5:0] out_4,
  output out_5,
  output [15:0] out_6
);

  wire _1, _2, _3, _4, _5, _10, _11, _12, _13, _14, _15, _16, _17, and_1_out, and_2_out, and_3_out,
       and_4_out, and_5_out, and_6_out, and_7_out, and_8_out, and_9_out, and_10_out, and_11_out, and_12_out,
       and_13_out, and_14_out, and_15_out, and_16_out, and_17_out, and_18_out, and_19_out, and_20_out,
       and_21_out, and_22_out, and_23_out, and_24_out, and_25_out, and_26_out, and_27_out, and_28_out,
       and_29_out, and_30_out, and_31_out, and_32_out, and_33_out, and_34_out, and_35_out, and_36_out,
       and_37_out, and_38_out, and_39_out, and_40_out, and_41_out, and_42_out, and_43_out, and_44_out,
       and_45_out, and_46_out, and_47_out, and_48_out, and_49_out, and_50_out, and_51_out, and_52_out,
       and_53_out, and_54_out, and_55_out, and_56_out, and_57_out, and_58_out, and_59_out, and_60_out,
       and_61_out, and_62_out, and_63_out, and_64_out, and_65_out, and_66_out, and_67_out, and_68_out,
       and_69_out, and_70_out, and_71_out, and_72_out, and_73_out, and_74_out, and_75_out, and_76_out,
       and_77_out, and_78_out, and_79_out, Clear2, Clear3, comparator_1_eq, comparator_2_eq, comparator_3_eq,
       comparator_4_eq, comparator_5_eq, comparator_6_eq, comparator_7_eq, comparator_8_eq, comparator_9_eq,
       comparator_10_eq, comparator_11_eq, comparator_12_eq, comparator_13_eq, comparator_14_eq,
       comparator_15_eq, comparator_16_eq, comparator_17_eq, comparator_18_eq, comparator_19_eq,
       comparator_20_eq, comparator_21_eq, comparator_22_eq, comparator_23_eq, comparator_24_eq,
       comparator_26_eq, comparator_27_eq, comparator_28_eq, comparator_29_eq, comparator_30_eq,
       comparator_31_eq, comparator_32_eq, comparator_33_eq, comparator_34_eq, comparator_35_eq,
       comparator_36_eq, comparator_37_eq, comparator_38_eq, comparator_39_eq, comparator_40_eq,
       comparator_41_eq, comparator_42_eq, comparator_43_eq, comparator_44_eq, comparator_45_eq,
       comparator_46_lt, comparator_47_lt, comparator_48_lt, comparator_49_lt, comparator_50_lt,
       comparator_51_lt, comparator_52_lt, comparator_53_lt, comparator_54_lt, comparator_55_lt,
       comparator_56_lt, comparator_57_lt, comparator_58_lt, comparator_59_lt, comparator_60_gt,
       comparator_61_gt, comparator_62_gt, comparator_63_gt, comparator_64_lt, comparator_65_lt,
       comparator_66_lt, comparator_67_lt, comparator_68_lt, comparator_69_lt, comparator_70_eq,
       comparator_71_eq, comparator_72_eq, comparator_73_eq, comparator_74_eq, comparator_75_eq,
       comparator_76_eq, comparator_77_eq, comparator_78_eq, comparator_79_eq, comparator_80_eq,
       comparator_81_eq, comparator_82_eq, comparator_83_eq, comparator_84_eq, comparator_85_eq,
       comparator_86_eq, comparator_87_eq, comparator_88_eq, comparator_89_eq, comparator_90_eq,
       comparator_91_eq, comparator_92_eq, comparator_93_eq, comparator_94_eq, comparator_95_eq,
       comparator_96_eq, comparator_97_eq, comparator_98_eq, comparator_99_eq, comparator_100_eq,
       comparator_101_eq, comparator_102_eq, comparator_103_eq, comparator_104_eq, comparator_105_eq,
       comparator_106_eq, comparator_107_eq, comparator_108_eq, comparator_109_eq, comparator_110_eq,
       comparator_111_eq, comparator_112_eq, comparator_113_eq, comparator_114_eq, comparator_115_eq,
       comparator_116_eq, comparator_117_eq, comparator_118_eq, comparator_119_eq, comparator_120_eq,
       comparator_121_eq, comparator_122_eq, comparator_123_eq, comparator_124_eq, comparator_125_eq,
       comparator_126_eq, comparator_127_eq, comparator_128_eq, comparator_129_eq, comparator_130_eq,
       comparator_131_eq, comparator_132_eq, comparator_133_eq, comparator_134_eq, comparator_135_eq,
       comparator_136_eq, comparator_137_eq, comparator_138_eq, comparator_139_eq, comparator_140_eq,
       comparator_141_eq, comparator_142_eq, comparator_143_eq, comparator_144_eq, comparator_145_eq,
       comparator_146_eq, comparator_147_eq, comparator_148_eq, comparator_149_eq, comparator_150_eq,
       comparator_151_eq, comparator_152_eq, counter_2_q, d_ff_1_q, d_ff_2_q, d_ff_5_q, d_ff_10_q, d_ff_13_q,
       d_ff_14_q, d_ff_17_q, d_ff_18_q, d_ff_21_q, d_ff_24_q, d_ff_25_q, d_ff_26_q, d_ff_27_q, d_ff_28_q,
       d_ff_29_q, d_ff_31_q, d_ff_32_q, d_ff_34_q, d_ff_35_q, d_ff_37_q, d_ff_38_q, d_ff_40_q, d_ff_41_q,
       d_ff_43_q, d_ff_44_q, d_ff_46_q, d_ff_47_q, d_ff_49_q, d_ff_50_q, d_ff_51_q, d_ff_52_q, d_ff_53_q,
       d_ff_54_q, d_ff_55_q, d_ff_56_q, d_ff_57_q, d_ff_58_q, d_ff_59_q, d_ff_60_q, d_ff_61_q, d_ff_62_q,
       d_ff_63_q, d_ff_64_q, d_ff_65_q, d_ff_66_q, d_ff_67_q, d_ff_68_q, d_ff_69_q, d_ff_70_q, d_ff_72_q,
       d_ff_73_q, d_ff_74_q, d_ff_75_q, d_ff_76_q, d_ff_78_q, d_ff_79_q, d_ff_80_q, d_ff_81_q, d_ff_82_q,
       d_ff_84_q, d_ff_85_q, d_ff_86_q, d_ff_87_q, d_ff_88_q, d_ff_90_q, d_ff_91_q, d_ff_92_q, d_ff_93_q,
       d_ff_94_q, d_ff_96_q, d_ff_97_q, d_ff_98_q, d_ff_99_q, d_ff_100_q, Finstr, iskl_1_x, not_1_out,
       not_2_out, OK, or_1_out, or_3_out, or_5_out, or_6_out, SpINP, SpJMPF0, SpJMPF1, SpJMPF2, SpJMPF3,
       SpJMPF4, SpJMPF5, SpLDO, SpMOV, SpMV, SpOUT, SpSTO, \ф_1_out_2 ;
  wire [2:0] counter_3_q;
  wire [3:0] decsimbol_1_out_3, register_21_q, register_22_q, register_23_q, register_24_q;
  wire [5:0] ADD, AND, demultiplexer_1_out1, demultiplexer_2_out1, demultiplexer_3_out1,
       demultiplexer_4_out1, demultiplexer_5_out1, demultiplexer_6_out1, demultiplexer_7_out1,
       demultiplexer_8_out1, demultiplexer_9_out1, demultiplexer_10_out1, demultiplexer_11_out1,
       demultiplexer_12_out1, demultiplexer_13_out1, demultiplexer_14_out1, demultiplexer_15_out1,
       demultiplexer_16_out1, demultiplexer_17_out1, demultiplexer_18_out1, demultiplexer_19_out1,
       demultiplexer_20_out1, demultiplexer_21_out1, demultiplexer_22_out1, demultiplexer_23_out1,
       demultiplexer_24_out1, INP, INVA, JMPF0, JMPF1, JMPF2, JMPF3, JMPF4, JMPF5, LDO, MOV, MV, OR, OUT,
       REG0, REG1, REG2, REG3, register_1_q, SHL, SHR, STO, SUB, XOR;
  wire [6:0] register_16_q;

  and and_1 (and_1_out, Takt, Finstr);
  not not_1 (not_1_out, or_3_out);
  and and_2 (and_2_out, and_1_out, or_1_out);
  or or_1 (or_1_out, not_1_out, iskl_1_x);
  Iskl iskl_1 (.y0(out_4[5]), .y1(out_4[4]), .y2(out_4[3]), .y3(out_4[2]), .y4(out_4[1]), .y5(out_4[0]), .x(iskl_1_x));
  Counter #(.width(6), .max('h3f)) counter_1 (.Q(out_4), .clk(and_2_out), .clr(in_3));  // open: load, D, count, carry
  Comparator #(.width(6)) comparator_1 (.a(out_4), .b(MV), .eq(comparator_1_eq));  // open: gt, lt
  Comparator #(.width(6)) comparator_2 (.a(out_4), .b(INVA), .eq(comparator_2_eq));  // open: gt, lt
  Comparator #(.width(6)) comparator_3 (.a(out_4), .b(AND), .eq(comparator_3_eq));  // open: gt, lt
  Comparator #(.width(6)) comparator_4 (.a(out_4), .b(SUB), .eq(comparator_4_eq));  // open: gt, lt
  Comparator #(.width(6)) comparator_5 (.a(out_4), .b(ADD), .eq(comparator_5_eq));  // open: gt, lt
  Comparator #(.width(6)) comparator_6 (.a(out_4), .b(OR), .eq(comparator_6_eq));  // open: gt, lt
  Comparator #(.width(6)) comparator_7 (.a(out_4), .b(XOR), .eq(comparator_7_eq));  // open: gt, lt
  Comparator #(.width(6)) comparator_8 (.a(out_4), .b(SHL), .eq(comparator_8_eq));  // open: gt, lt
  Comparator #(.width(6)) comparator_9 (.a(out_4), .b(SHR), .eq(comparator_9_eq));  // open: gt, lt
  Comparator #(.width(6)) comparator_10 (.a(out_4), .b(INP), .eq(comparator_10_eq));  // open: gt, lt
  Comparator #(.width(6)) comparator_11 (.a(out_4), .b(OUT), .eq(comparator_11_eq));  // open: gt, lt
  Comparator #(.width(6)) comparator_12 (.a(out_4), .b(MOV), .eq(comparator_12_eq));  // open: gt, lt
  Comparator #(.width(6)) comparator_13 (.a(out_4), .b(LDO), .eq(comparator_13_eq));  // open: gt, lt
  Comparator #(.width(6)) comparator_14 (.a(out_4), .b(STO), .eq(comparator_14_eq));  // open: gt, lt
  Comparator #(.width(6)) comparator_15 (.a(out_4), .b(REG0), .eq(comparator_15_eq));  // open: gt, lt
  Comparator #(.width(6)) comparator_16 (.a(out_4), .b(REG1), .eq(comparator_16_eq));  // open: gt, lt
  Comparator #(.width(6)) comparator_17 (.a(out_4), .b(REG2), .eq(comparator_17_eq));  // open: gt, lt
  Comparator #(.width(6)) comparator_18 (.a(out_4), .b(REG3), .eq(comparator_18_eq));  // open: gt, lt
  Comparator #(.width(6)) comparator_19 (.a(out_4), .b(JMPF0), .eq(comparator_19_eq));  // open: gt, lt
  Comparator #(.width(6)) comparator_20 (.a(out_4), .b(JMPF1), .eq(comparator_20_eq));  // open: gt, lt
  Comparator #(.width(6)) comparator_21 (.a(out_4), .b(JMPF2), .eq(comparator_21_eq));  // open: gt, lt
  Comparator #(.width(6)) comparator_22 (.a(out_4), .b(JMPF3), .eq(comparator_22_eq));  // open: gt, lt
  Comparator #(.width(6)) comparator_23 (.a(out_4), .b(JMPF4), .eq(comparator_23_eq));  // open: gt, lt
  Comparator #(.width(6)) comparator_24 (.a(out_4), .b(JMPF5), .eq(comparator_24_eq));  // open: gt, lt
  or or_2 (out_5, SpJMPF2, SpJMPF1, SpJMPF0, SpOUT, SpMOV, SpINP, SpSTO, SpLDO, SpMV, SpJMPF3, SpJMPF4, SpJMPF5);
  Register #(.width(6), .trigger("falling")) register_1 (
    .D(out_4), .Q(register_1_q), .clk(or_1_out), .clr(in_3));  // open: en
  Comparator #(.width(6)) comparator_25 (.a(out_4), .b(register_1_q), .eq(OK));  // open: gt, lt
  or or_3 (or_3_out, comparator_1_eq, comparator_2_eq, comparator_3_eq, comparator_4_eq, comparator_5_eq, comparator_6_eq, comparator_7_eq, comparator_8_eq, comparator_9_eq, comparator_10_eq, comparator_11_eq, comparator_12_eq, comparator_13_eq, comparator_14_eq, comparator_15_eq, comparator_16_eq, comparator_17_eq, comparator_18_eq, comparator_19_eq, comparator_20_eq, comparator_21_eq, comparator_22_eq, comparator_23_eq, comparator_24_eq);
  // Probe on out_4
  Comparator #(.width(7)) comparator_26 (.a(Simbol), .b(7'b1001001), .eq(comparator_26_eq));  // open: gt, lt
  Comparator #(.width(7)) comparator_27 (.a(Simbol), .b(7'b1001110), .eq(comparator_27_eq));  // open: gt, lt
  Comparator #(.width(7)) comparator_28 (.a(Simbol), .b(7'b1010000), .eq(comparator_28_eq));  // open: gt, lt
  Comparator #(.width(7)) comparator_29 (.a(Simbol), .b(7'b0100000), .eq(comparator_29_eq));  // open: gt, lt
  Comparator #(.width(7)) comparator_30 (.a(Simbol), .b(7'b1001111), .eq(comparator_30_eq));  // open: gt, lt
  Comparator #(.width(7)) comparator_31 (.a(Simbol), .b(7'b1010101), .eq(comparator_31_eq));  // open: gt, lt
  Comparator #(.width(7)) comparator_32 (.a(Simbol), .b(7'b1010100), .eq(comparator_32_eq));  // open: gt, lt
  Comparator #(.width(7)) comparator_33 (.a(Simbol), .b(7'b0100000), .eq(comparator_33_eq));  // open: gt, lt
  Comparator #(.width(7)) comparator_34 (.a(Simbol), .b(7'b1001101), .eq(comparator_34_eq));  // open: gt, lt
  Comparator #(.width(7)) comparator_35 (.a(Simbol), .b(7'b1001111), .eq(comparator_35_eq));  // open: gt, lt
  Comparator #(.width(7)) comparator_36 (.a(Simbol), .b(7'b1010110), .eq(comparator_36_eq));  // open: gt, lt
  Comparator #(.width(7)) comparator_37 (.a(Simbol), .b(7'b0100000), .eq(comparator_37_eq));  // open: gt, lt
  Comparator #(.width(7)) comparator_38 (.a(Simbol), .b(7'b1001100), .eq(comparator_38_eq));  // open: gt, lt
  Comparator #(.width(7)) comparator_39 (.a(Simbol), .b(7'b1000100), .eq(comparator_39_eq));  // open: gt, lt
  Comparator #(.width(7)) comparator_40 (.a(Simbol), .b(7'b1001111), .eq(comparator_40_eq));  // open: gt, lt
  Comparator #(.width(7)) comparator_41 (.a(Simbol), .b(7'b0100000), .eq(comparator_41_eq));  // open: gt, lt
  Comparator #(.width(7)) comparator_42 (.a(Simbol), .b(7'b1010011), .eq(comparator_42_eq));  // open: gt, lt
  Comparator #(.width(7)) comparator_43 (.a(Simbol), .b(7'b1010100), .eq(comparator_43_eq));  // open: gt, lt
  Comparator #(.width(7)) comparator_44 (.a(Simbol), .b(7'b1001111), .eq(comparator_44_eq));  // open: gt, lt
  Comparator #(.width(7)) comparator_45 (.a(Simbol), .b(7'b0100000), .eq(comparator_45_eq));  // open: gt, lt
  Comparator #(.width(6)) comparator_46 (.a({6{1'b0}}), .b(MV), .lt(comparator_46_lt));  // open: gt, eq
  Comparator #(.width(6)) comparator_47 (.a({6{1'b0}}), .b(INVA), .lt(comparator_47_lt));  // open: gt, eq
  Comparator #(.width(6)) comparator_48 (.a({6{1'b0}}), .b(AND), .lt(comparator_48_lt));  // open: gt, eq
  Comparator #(.width(6)) comparator_49 (.a({6{1'b0}}), .b(SUB), .lt(comparator_49_lt));  // open: gt, eq
  Comparator #(.width(6)) comparator_50 (.a({6{1'b0}}), .b(ADD), .lt(comparator_50_lt));  // open: gt, eq
  Comparator #(.width(6)) comparator_51 (.a({6{1'b0}}), .b(OR), .lt(comparator_51_lt));  // open: gt, eq
  Comparator #(.width(6)) comparator_52 (.a({6{1'b0}}), .b(XOR), .lt(comparator_52_lt));  // open: gt, eq
  Comparator #(.width(6)) comparator_53 (.a({6{1'b0}}), .b(SHL), .lt(comparator_53_lt));  // open: gt, eq
  Comparator #(.width(6)) comparator_54 (.a({6{1'b0}}), .b(SHR), .lt(comparator_54_lt));  // open: gt, eq
  Comparator #(.width(6)) comparator_55 (.a({6{1'b0}}), .b(INP), .lt(comparator_55_lt));  // open: gt, eq
  Comparator #(.width(6)) comparator_56 (.a({6{1'b0}}), .b(OUT), .lt(comparator_56_lt));  // open: gt, eq
  Comparator #(.width(6)) comparator_57 (.a({6{1'b0}}), .b(MOV), .lt(comparator_57_lt));  // open: gt, eq
  Comparator #(.width(6)) comparator_58 (.a({6{1'b0}}), .b(LDO), .lt(comparator_58_lt));  // open: gt, eq
  Comparator #(.width(6)) comparator_59 (.a({6{1'b0}}), .b(STO), .lt(comparator_59_lt));  // open: gt, eq
  Comparator #(.width(6)) comparator_60 (.a({6{1'b0}}), .b(REG0), .gt(comparator_60_gt));  // open: eq, lt
  Comparator #(.width(6)) comparator_61 (.a({6{1'b0}}), .b(REG1), .gt(comparator_61_gt));  // open: eq, lt
  Comparator #(.width(6)) comparator_62 (.a({6{1'b0}}), .b(REG2), .gt(comparator_62_gt));  // open: eq, lt
  Comparator #(.width(6)) comparator_63 (.a({6{1'b0}}), .b(REG3), .gt(comparator_63_gt));  // open: eq, lt
  Comparator #(.width(6)) comparator_64 (.a({6{1'b0}}), .b(JMPF0), .lt(comparator_64_lt));  // open: gt, eq
  Comparator #(.width(6)) comparator_65 (.a({6{1'b0}}), .b(JMPF1), .lt(comparator_65_lt));  // open: gt, eq
  Comparator #(.width(6)) comparator_66 (.a({6{1'b0}}), .b(JMPF2), .lt(comparator_66_lt));  // open: gt, eq
  Comparator #(.width(6)) comparator_67 (.a({6{1'b0}}), .b(JMPF3), .lt(comparator_67_lt));  // open: gt, eq
  Comparator #(.width(6)) comparator_68 (.a({6{1'b0}}), .b(JMPF4), .lt(comparator_68_lt));  // open: gt, eq
  Comparator #(.width(6)) comparator_69 (.a({6{1'b0}}), .b(JMPF5), .lt(comparator_69_lt));  // open: gt, eq
  and and_3 (and_3_out, d_ff_1_q, comparator_27_eq);
  and and_4 (and_4_out, d_ff_2_q, comparator_28_eq);
  and and_5 (and_5_out, _1, comparator_29_eq);
  and and_6 (and_6_out, d_ff_5_q, comparator_31_eq);
  and and_7 (and_7_out, Clear2, comparator_32_eq);
  and and_8 (and_8_out, _2, comparator_33_eq);
  and and_9 (and_9_out, Clear3, comparator_35_eq);
  and and_10 (and_10_out, d_ff_10_q, comparator_36_eq);
  and and_11 (and_11_out, _3, comparator_37_eq);
  and and_12 (and_12_out, d_ff_13_q, comparator_39_eq);
  and and_13 (and_13_out, d_ff_14_q, comparator_40_eq);
  and and_14 (and_14_out, _4, comparator_41_eq);
  and and_15 (and_15_out, d_ff_17_q, comparator_43_eq);
  and and_16 (and_16_out, d_ff_18_q, comparator_44_eq);
  and and_17 (and_17_out, _5, comparator_45_eq);
  D_Flip_Flop d_ff_1 (.clk(Takt), .D(comparator_26_eq), .Q(d_ff_1_q));  // open: Qn, preset, en, reset
  D_Flip_Flop d_ff_2 (.clk(Takt), .D(and_3_out), .Q(d_ff_2_q));  // open: Qn, preset, en, reset
  D_Flip_Flop d_ff_3 (.clk(Takt), .D(and_4_out), .Q(_1), .preset(_1), .reset(in_3));  // open: Qn, en
  D_Flip_Flop d_ff_4 (.clk(Takt), .D(and_5_out), .Q(SpINP), .preset(SpINP), .reset(in_3));  // open: Qn, en
  D_Flip_Flop d_ff_5 (.clk(Takt), .D(comparator_30_eq), .Q(d_ff_5_q));  // open: Qn, preset, en, reset
  D_Flip_Flop d_ff_6 (.clk(Takt), .D(and_6_out), .Q(Clear2));  // open: Qn, preset, en, reset
  Demultiplexer #(.width(6)) demultiplexer_1 (.out1(demultiplexer_1_out1), .in(6'b000010), .sel(_2));  // open: out0, en
  D_Flip_Flop d_ff_7 (.clk(Takt), .D(and_7_out), .Q(_2), .preset(_2), .reset(in_3));  // open: Qn, en
  D_Flip_Flop d_ff_8 (.clk(Takt), .D(and_8_out), .Q(SpOUT), .preset(SpOUT), .reset(in_3));  // open: Qn, en
  D_Flip_Flop d_ff_9 (.clk(Takt), .D(comparator_34_eq), .Q(Clear3));  // open: Qn, preset, en, reset
  D_Flip_Flop d_ff_10 (.clk(Takt), .D(and_9_out), .Q(d_ff_10_q));  // open: Qn, preset, en, reset
  Demultiplexer #(.width(6)) demultiplexer_2 (.out1(demultiplexer_2_out1), .in(6'b000011), .sel(_3));  // open: out0, en
  D_Flip_Flop d_ff_11 (.clk(Takt), .D(and_10_out), .Q(_3), .preset(_3), .reset(in_3));  // open: Qn, en
  D_Flip_Flop d_ff_12 (.clk(Takt), .D(and_11_out), .Q(SpMOV), .preset(SpMOV), .reset(in_3));  // open: Qn, en
  D_Flip_Flop d_ff_13 (.clk(Takt), .D(comparator_38_eq), .Q(d_ff_13_q));  // open: Qn, preset, en, reset
  D_Flip_Flop d_ff_14 (.clk(Takt), .D(and_12_out), .Q(d_ff_14_q));  // open: Qn, preset, en, reset
  Demultiplexer #(.width(6)) demultiplexer_3 (.out1(demultiplexer_3_out1), .in(6'b000100), .sel(_4));  // open: out0, en
  D_Flip_Flop d_ff_15 (.clk(Takt), .D(and_13_out), .Q(_4), .preset(_4), .reset(in_3));  // open: Qn, en
  D_Flip_Flop d_ff_16 (.clk(Takt), .D(and_14_out), .Q(SpLDO), .preset(SpLDO), .reset(in_3));  // open: Qn, en
  D_Flip_Flop d_ff_17 (.clk(Takt), .D(comparator_42_eq), .Q(d_ff_17_q));  // open: Qn, preset, en, reset
  D_Flip_Flop d_ff_18 (.clk(Takt), .D(and_15_out), .Q(d_ff_18_q));  // open: Qn, preset, en, reset
  Demultiplexer #(.width(6)) demultiplexer_4 (.out1(demultiplexer_4_out1), .in(6'b000101), .sel(_5));  // open: out0, en
  D_Flip_Flop d_ff_19 (.clk(Takt), .D(and_16_out), .Q(_5));  // open: Qn, preset, en, reset
  D_Flip_Flop d_ff_20 (.clk(Takt), .D(and_17_out), .Q(SpSTO), .preset(SpSTO), .reset(in_3));  // open: Qn, en
  Demultiplexer #(.width(6)) demultiplexer_5 (.out1(demultiplexer_5_out1), .in(6'b000001), .sel(_1));  // open: out0, en
  Register #(.width(6), .trigger("falling")) register_2 (
    .D(demultiplexer_1_out1), .Q(OUT), .clk(Takt), .clr(in_3));  // open: en
  Register #(.width(6), .trigger("falling")) register_3 (
    .D(demultiplexer_2_out1), .Q(MOV), .clk(Takt), .clr(in_3));  // open: en
  Register #(.width(6), .trigger("falling")) register_4 (
    .D(demultiplexer_3_out1), .Q(LDO), .clk(Takt), .clr(in_3));  // open: en
  Register #(.width(6), .trigger("falling")) register_5 (
    .D(demultiplexer_4_out1), .Q(STO), .clk(_5), .clr(in_3));  // open: en
  Register #(.width(6), .trigger("falling")) register_6 (
    .D(demultiplexer_5_out1), .Q(INP), .clk(Takt), .clr(in_3));  // open: en
  or or_4 (Finstr, comparator_46_lt, comparator_47_lt, comparator_48_lt, comparator_49_lt, comparator_50_lt, comparator_51_lt, comparator_52_lt, comparator_53_lt, comparator_54_lt, comparator_55_lt, comparator_56_lt, comparator_57_lt, comparator_58_lt, comparator_59_lt, comparator_60_gt, comparator_61_gt, comparator_62_gt, comparator_63_gt, comparator_64_lt, comparator_65_lt, comparator_66_lt, comparator_67_lt, comparator_68_lt, comparator_69_lt);
  Comparator #(.width(7)) comparator_70 (.a(Simbol), .b(7'b1001101), .eq(comparator_70_eq));  // open: gt, lt
  Comparator #(.width(7)) comparator_71 (.a(Simbol), .b(7'b1010110), .eq(comparator_71_eq));  // open: gt, lt
  Comparator #(.width(7)) comparator_72 (.a(Simbol), .b(7'b0100000), .eq(comparator_72_eq));  // open: gt, lt
  Comparator #(.width(7)) comparator_73 (.a(Simbol), .b(7'b1001001), .eq(comparator_73_eq));  // open: gt, lt
  Comparator #(.width(7)) comparator_74 (.a(Simbol), .b(7'b1001110), .eq(comparator_74_eq));  // open: gt, lt
  Comparator #(.width(7)) comparator_75 (.a(Simbol), .b(7'b1010110), .eq(comparator_75_eq));  // open: gt, lt
  Comparator #(.width(7)) comparator_76 (.a(Simbol), .b(7'b1000001), .eq(comparator_76_eq));  // open: gt, lt
  Comparator #(.width(7)) comparator_77 (.a(Simbol), .b(7'b1000001), .eq(comparator_77_eq));  // open: gt, lt
  Comparator #(.width(7)) comparator_78 (.a(Simbol), .b(7'b1001110), .eq(comparator_78_eq));  // open: gt, lt
  Comparator #(.width(7)) comparator_79 (.a(Simbol), .b(7'b1000100), .eq(comparator_79_eq));  // open: gt, lt
  Comparator #(.width(7)) comparator_80 (.a(Simbol), .b(7'b1010011), .eq(comparator_80_eq));  // open: gt, lt
  Comparator #(.width(7)) comparator_81 (.a(Simbol), .b(7'b1010101), .eq(comparator_81_eq));  // open: gt, lt
  Comparator #(.width(7)) comparator_82 (.a(Simbol), .b(7'b1000010), .eq(comparator_82_eq));  // open: gt, lt
  Comparator #(.width(7)) comparator_83 (.a(Simbol), .b(7'b1000001), .eq(comparator_83_eq));  // open: gt, lt
  Comparator #(.width(7)) comparator_84 (.a(Simbol), .b(7'b1000100), .eq(comparator_84_eq));  // open: gt, lt
  Comparator #(.width(7)) comparator_85 (.a(Simbol), .b(7'b1000100), .eq(comparator_85_eq));  // open: gt, lt
  Comparator #(.width(7)) comparator_86 (.a(Simbol), .b(7'b1011000), .eq(comparator_86_eq));  // open: gt, lt
  Comparator #(.width(7)) comparator_87 (.a(Simbol), .b(7'b1001111), .eq(comparator_87_eq));  // open: gt, lt
  Comparator #(.width(7)) comparator_88 (.a(Simbol), .b(7'b1010010), .eq(comparator_88_eq));  // open: gt, lt
  Comparator #(.width(7)) comparator_89 (.a(Simbol), .b(7'b1011000), .eq(comparator_89_eq));  // open: gt, lt
  Comparator #(.width(7)) comparator_90 (.a(Simbol), .b(7'b1001111), .eq(comparator_90_eq));  // open: gt, lt
  Comparator #(.width(7)) comparator_91 (.a(Simbol), .b(7'b1010010), .eq(comparator_91_eq));  // open: gt, lt
  Comparator #(.width(7)) comparator_92 (.a(Simbol), .b(7'b1010011), .eq(comparator_92_eq));  // open: gt, lt
  Comparator #(.width(7)) comparator_93 (.a(Simbol), .b(7'b1001000), .eq(comparator_93_eq));  // open: gt, lt
  Comparator #(.width(7)) comparator_94 (.a(Simbol), .b(7'b1001100), .eq(comparator_94_eq));  // open: gt, lt
  Comparator #(.width(7)) comparator_95 (.a(Simbol), .b(7'b1010011), .eq(comparator_95_eq));  // open: gt, lt
  Comparator #(.width(7)) comparator_96 (.a(Simbol), .b(7'b1001000), .eq(comparator_96_eq));  // open: gt, lt
  Comparator #(.width(7)) comparator_97 (.a(Simbol), .b(7'b1010010), .eq(comparator_97_eq));  // open: gt, lt
  and and_18 (and_18_out, d_ff_21_q, comparator_71_eq);
  and and_19 (and_19_out, _10, comparator_72_eq);
  and and_20 (and_20_out, d_ff_24_q, comparator_74_eq);
  and and_21 (and_21_out, d_ff_25_q, comparator_75_eq);
  and and_22 (and_22_out, d_ff_26_q, comparator_76_eq);
  and and_23 (and_23_out, d_ff_28_q, comparator_78_eq);
  and and_24 (and_24_out, d_ff_29_q, comparator_79_eq);
  and and_25 (and_25_out, d_ff_31_q, comparator_81_eq);
  and and_26 (and_26_out, d_ff_32_q, comparator_82_eq);
  and and_27 (and_27_out, d_ff_34_q, comparator_84_eq);
  and and_28 (and_28_out, d_ff_35_q, comparator_85_eq);
  not not_2 (not_2_out, comparator_86_eq);
  and and_29 (and_29_out, d_ff_37_q, comparator_87_eq);
  and and_30 (and_30_out, d_ff_38_q, comparator_88_eq);
  and and_31 (and_31_out, d_ff_40_q, comparator_90_eq);
  and and_32 (and_32_out, d_ff_41_q, comparator_91_eq);
  and and_33 (and_33_out, d_ff_43_q, comparator_93_eq);
  and and_34 (and_34_out, d_ff_44_q, comparator_94_eq);
  and and_35 (and_35_out, d_ff_46_q, comparator_96_eq);
  and and_36 (and_36_out, d_ff_47_q, comparator_97_eq);
  D_Flip_Flop d_ff_21 (.clk(Takt), .D(comparator_70_eq), .Q(d_ff_21_q));  // open: Qn, preset, en, reset
  Demultiplexer #(.width(6)) demultiplexer_6 (
    .out1(demultiplexer_6_out1), .in(6'b010000), .sel(_10));  // open: out0, en
  D_Flip_Flop d_ff_22 (.clk(Takt), .D(and_18_out), .Q(_10), .preset(_10), .reset(in_3));  // open: Qn, en
  D_Flip_Flop d_ff_23 (.clk(Takt), .D(and_19_out), .Q(SpMV), .preset(SpMV), .reset(in_3));  // open: Qn, en
  D_Flip_Flop d_ff_24 (.clk(Takt), .D(comparator_73_eq), .Q(d_ff_24_q));  // open: Qn, preset, en, reset
  D_Flip_Flop d_ff_25 (.clk(Takt), .D(and_20_out), .Q(d_ff_25_q));  // open: Qn, preset, en, reset
  D_Flip_Flop d_ff_26 (.clk(Takt), .D(and_21_out), .Q(d_ff_26_q));  // open: Qn, preset, en, reset
  Demultiplexer #(.width(6)) demultiplexer_7 (
    .out1(demultiplexer_7_out1), .in(6'b011000), .sel(d_ff_27_q));  // open: out0, en
  D_Flip_Flop d_ff_27 (.clk(Takt), .D(and_22_out), .Q(d_ff_27_q), .preset(d_ff_27_q), .reset(in_3));  // open: Qn, en
  D_Flip_Flop d_ff_28 (.clk(Takt), .D(comparator_77_eq), .Q(d_ff_28_q));  // open: Qn, preset, en, reset
  D_Flip_Flop d_ff_29 (.clk(Takt), .D(and_23_out), .Q(d_ff_29_q));  // open: Qn, preset, en, reset
  D_Flip_Flop d_ff_30 (.clk(Takt), .D(and_24_out), .Q(_11), .preset(_11), .reset(in_3));  // open: Qn, en
  D_Flip_Flop d_ff_31 (.clk(Takt), .D(comparator_80_eq), .Q(d_ff_31_q));  // open: Qn, preset, en, reset
  D_Flip_Flop d_ff_32 (.clk(Takt), .D(and_25_out), .Q(d_ff_32_q));  // open: Qn, preset, en, reset
  D_Flip_Flop d_ff_33 (.clk(Takt), .D(and_26_out), .Q(_12), .preset(_12), .reset(in_3));  // open: Qn, en
  D_Flip_Flop d_ff_34 (.clk(Takt), .D(comparator_83_eq), .Q(d_ff_34_q));  // open: Qn, preset, en, reset
  D_Flip_Flop d_ff_35 (.clk(Takt), .D(and_27_out), .Q(d_ff_35_q));  // open: Qn, preset, en, reset
  D_Flip_Flop d_ff_36 (.clk(Takt), .D(and_28_out), .Q(_13), .preset(_13), .reset(in_3));  // open: Qn, en
  D_Flip_Flop d_ff_37 (.clk(Takt), .D(not_2_out), .Q(d_ff_37_q));  // open: Qn, preset, en, reset
  D_Flip_Flop d_ff_38 (.clk(Takt), .D(and_29_out), .Q(d_ff_38_q));  // open: Qn, preset, en, reset
  Demultiplexer #(.width(6)) demultiplexer_8 (
    .out1(demultiplexer_8_out1), .in(6'b010100), .sel(_14));  // open: out0, en
  D_Flip_Flop d_ff_39 (.clk(Takt), .D(and_30_out), .Q(_14), .preset(_14), .reset(in_3));  // open: Qn, en
  D_Flip_Flop d_ff_40 (.clk(Takt), .D(comparator_89_eq), .Q(d_ff_40_q));  // open: Qn, preset, en, reset
  D_Flip_Flop d_ff_41 (.clk(Takt), .D(and_31_out), .Q(d_ff_41_q));  // open: Qn, preset, en, reset
  D_Flip_Flop d_ff_42 (.clk(Takt), .D(and_32_out), .Q(_15), .preset(_15), .reset(in_3));  // open: Qn, en
  D_Flip_Flop d_ff_43 (.clk(Takt), .D(comparator_92_eq), .Q(d_ff_43_q));  // open: Qn, preset, en, reset
  D_Flip_Flop d_ff_44 (.clk(Takt), .D(and_33_out), .Q(d_ff_44_q));  // open: Qn, preset, en, reset
  D_Flip_Flop d_ff_45 (.clk(Takt), .D(and_34_out), .Q(_16), .preset(_16), .reset(in_3));  // open: Qn, en
  D_Flip_Flop d_ff_46 (.clk(Takt), .D(comparator_95_eq), .Q(d_ff_46_q));  // open: Qn, preset, en, reset
  D_Flip_Flop d_ff_47 (.clk(Takt), .D(and_35_out), .Q(d_ff_47_q));  // open: Qn, preset, en, reset
  D_Flip_Flop d_ff_48 (.clk(Takt), .D(and_36_out), .Q(_17), .preset(_17), .reset(in_3));  // open: Qn, en
  Register #(.width(6), .trigger("falling")) register_7 (
    .D(demultiplexer_6_out1), .Q(MV), .clk(Takt), .clr(in_3));  // open: en
  Demultiplexer #(.width(6)) demultiplexer_9 (
    .out1(demultiplexer_9_out1), .in(6'b010011), .sel(_11));  // open: out0, en
  Demultiplexer #(.width(6)) demultiplexer_10 (
    .out1(demultiplexer_10_out1), .in(6'b010010), .sel(_12));  // open: out0, en
  Demultiplexer #(.width(6)) demultiplexer_11 (
    .out1(demultiplexer_11_out1), .in(6'b010001), .sel(_13));  // open: out0, en
  Demultiplexer #(.width(6)) demultiplexer_12 (
    .out1(demultiplexer_12_out1), .in(6'b010101), .sel(_15));  // open: out0, en
  Demultiplexer #(.width(6)) demultiplexer_13 (
    .out1(demultiplexer_13_out1), .in(6'b010110), .sel(_16));  // open: out0, en
  Demultiplexer #(.width(6)) demultiplexer_14 (
    .out1(demultiplexer_14_out1), .in(6'b010111), .sel(_17));  // open: out0, en
  Register #(.width(6), .trigger("falling")) register_8 (
    .D(demultiplexer_7_out1), .Q(INVA), .clk(Takt), .clr(in_3));  // open: en
  Register #(.width(6), .trigger("falling")) register_9 (
    .D(demultiplexer_9_out1), .Q(AND), .clk(Takt), .clr(in_3));  // open: en
  Register #(.width(6), .trigger("falling")) register_10 (
    .D(demultiplexer_10_out1), .Q(SUB), .clk(Takt), .clr(in_3));  // open: en
  Register #(.width(6), .trigger("falling")) register_11 (
    .D(demultiplexer_11_out1), .Q(ADD), .clk(Takt), .clr(in_3));  // open: en
  Register #(.width(6), .trigger("falling")) register_12 (
    .D(demultiplexer_8_out1), .Q(OR), .clk(Takt), .clr(in_3));  // open: en
  Register #(.width(6), .trigger("falling")) register_13 (
    .D(demultiplexer_12_out1), .Q(XOR), .clk(Takt), .clr(in_3));  // open: en
  Register #(.width(6), .trigger("falling")) register_14 (
    .D(demultiplexer_13_out1), .Q(SHL), .clk(Takt), .clr(in_3));  // open: en
  Register #(.width(6), .trigger("falling")) register_15 (
    .D(demultiplexer_14_out1), .Q(SHR), .clk(Takt), .clr(in_3));  // open: en
  Comparator #(.width(7)) comparator_98 (.a(Simbol), .b(7'b1010010), .eq(comparator_98_eq));  // open: gt, lt
  and and_37 (and_37_out, d_ff_49_q, comparator_99_eq);
  Comparator #(.width(7)) comparator_99 (.a(Simbol), .b(7'b1000101), .eq(comparator_99_eq));  // open: gt, lt
  and and_38 (and_38_out, d_ff_50_q, comparator_100_eq);
  Comparator #(.width(7)) comparator_100 (.a(Simbol), .b(7'b1000111), .eq(comparator_100_eq));  // open: gt, lt
  and and_39 (and_39_out, d_ff_51_q, comparator_101_eq);
  Comparator #(.width(7)) comparator_101 (.a(Simbol), .b(7'b0110000), .eq(comparator_101_eq));  // open: gt, lt
  Comparator #(.width(7)) comparator_102 (.a(Simbol), .b(7'b1010010), .eq(comparator_102_eq));  // open: gt, lt
  and and_40 (and_40_out, d_ff_53_q, comparator_103_eq);
  Comparator #(.width(7)) comparator_103 (.a(Simbol), .b(7'b1000101), .eq(comparator_103_eq));  // open: gt, lt
  and and_41 (and_41_out, d_ff_54_q, comparator_104_eq);
  Comparator #(.width(7)) comparator_104 (.a(Simbol), .b(7'b1000111), .eq(comparator_104_eq));  // open: gt, lt
  and and_42 (and_42_out, d_ff_55_q, comparator_105_eq);
  Comparator #(.width(7)) comparator_105 (.a(Simbol), .b(7'b0110001), .eq(comparator_105_eq));  // open: gt, lt
  Comparator #(.width(7)) comparator_106 (.a(Simbol), .b(7'b1010010), .eq(comparator_106_eq));  // open: gt, lt
  and and_43 (and_43_out, d_ff_57_q, comparator_107_eq);
  Comparator #(.width(7)) comparator_107 (.a(Simbol), .b(7'b1000101), .eq(comparator_107_eq));  // open: gt, lt
  and and_44 (and_44_out, d_ff_58_q, comparator_108_eq);
  Comparator #(.width(7)) comparator_108 (.a(Simbol), .b(7'b1000111), .eq(comparator_108_eq));  // open: gt, lt
  and and_45 (and_45_out, d_ff_59_q, comparator_109_eq);
  Comparator #(.width(7)) comparator_109 (.a(Simbol), .b(7'b0110010), .eq(comparator_109_eq));  // open: gt, lt
  Comparator #(.width(7)) comparator_110 (.a(Simbol), .b(7'b1010010), .eq(comparator_110_eq));  // open: gt, lt
  and and_46 (and_46_out, d_ff_61_q, comparator_111_eq);
  Comparator #(.width(7)) comparator_111 (.a(Simbol), .b(7'b1000101), .eq(comparator_111_eq));  // open: gt, lt
  and and_47 (and_47_out, d_ff_62_q, comparator_112_eq);
  Comparator #(.width(7)) comparator_112 (.a(Simbol), .b(7'b1000111), .eq(comparator_112_eq));  // open: gt, lt
  and and_48 (and_48_out, d_ff_63_q, comparator_113_eq);
  Comparator #(.width(7)) comparator_113 (.a(Simbol), .b(7'b0110011), .eq(comparator_113_eq));  // open: gt, lt
  Register #(.width(7), .trigger("falling")) register_16 (.D(Simbol), .Q(register_16_q), .clk(Takt));  // open: en, clr
  Comparator #(.width(7)) comparator_114 (.a(Simbol), .b(7'b0100011), .eq(comparator_114_eq));  // open: gt, lt
  D_Flip_Flop d_ff_49 (.clk(Takt), .D(comparator_98_eq), .Q(d_ff_49_q));  // open: Qn, preset, en, reset
  D_Flip_Flop d_ff_50 (.clk(Takt), .D(and_37_out), .Q(d_ff_50_q));  // open: Qn, preset, en, reset
  D_Flip_Flop d_ff_51 (.clk(Takt), .D(and_38_out), .Q(d_ff_51_q));  // open: Qn, preset, en, reset
  D_Flip_Flop d_ff_52 (.clk(Takt), .D(and_39_out), .Q(d_ff_52_q), .preset(d_ff_52_q), .reset(in_3));  // open: Qn, en
  D_Flip_Flop d_ff_53 (.clk(Takt), .D(comparator_102_eq), .Q(d_ff_53_q));  // open: Qn, preset, en, reset
  D_Flip_Flop d_ff_54 (.clk(Takt), .D(and_40_out), .Q(d_ff_54_q));  // open: Qn, preset, en, reset
  D_Flip_Flop d_ff_55 (.clk(Takt), .D(and_41_out), .Q(d_ff_55_q));  // open: Qn, preset, en, reset
  D_Flip_Flop d_ff_56 (.clk(Takt), .D(and_42_out), .Q(d_ff_56_q), .preset(d_ff_56_q), .reset(in_3));  // open: Qn, en
  D_Flip_Flop d_ff_57 (.clk(Takt), .D(comparator_106_eq), .Q(d_ff_57_q));  // open: Qn, preset, en, reset
  D_Flip_Flop d_ff_58 (.clk(Takt), .D(and_43_out), .Q(d_ff_58_q));  // open: Qn, preset, en, reset
  D_Flip_Flop d_ff_59 (.clk(Takt), .D(and_44_out), .Q(d_ff_59_q));  // open: Qn, preset, en, reset
  D_Flip_Flop d_ff_60 (.clk(Takt), .D(and_45_out), .Q(d_ff_60_q), .preset(d_ff_60_q), .reset(in_3));  // open: Qn, en
  D_Flip_Flop d_ff_61 (.clk(Takt), .D(comparator_110_eq), .Q(d_ff_61_q));  // open: Qn, preset, en, reset
  D_Flip_Flop d_ff_62 (.clk(Takt), .D(and_46_out), .Q(d_ff_62_q));  // open: Qn, preset, en, reset
  D_Flip_Flop d_ff_63 (.clk(Takt), .D(and_47_out), .Q(d_ff_63_q));  // open: Qn, preset, en, reset
  D_Flip_Flop d_ff_64 (.clk(Takt), .D(and_48_out), .Q(d_ff_64_q), .preset(d_ff_64_q), .reset(in_3));  // open: Qn, en
  DecSimbol decsimbol_1 (.out_3(decsimbol_1_out_3), .in_1(Simbol), .in_2(Takt));
  Comparator #(.width(7)) comparator_115 (.a(register_16_q), .b(7'b0100000), .eq(comparator_115_eq));  // open: gt, lt
  Comparator #(.width(7)) comparator_116 (.a(register_16_q), .b({7{1'b0}}), .eq(comparator_116_eq));  // open: gt, lt
  Demultiplexer #(.width(6)) demultiplexer_15 (
    .out1(demultiplexer_15_out1), .in(6'b110100), .sel(d_ff_52_q));  // open: out0, en
  Demultiplexer #(.width(6)) demultiplexer_16 (
    .out1(demultiplexer_16_out1), .in(6'b110101), .sel(d_ff_56_q));  // open: out0, en
  Demultiplexer #(.width(6)) demultiplexer_17 (
    .out1(demultiplexer_17_out1), .in(6'b110110), .sel(d_ff_60_q));  // open: out0, en
  Demultiplexer #(.width(6)) demultiplexer_18 (
    .out1(demultiplexer_18_out1), .in(6'b110111), .sel(d_ff_64_q));  // open: out0, en
  Counter #(.width(1), .max('h1)) counter_2 (
    .Q(counter_2_q), .clk(or_5_out), .clr(d_ff_65_q));  // open: load, D, count, carry
  or or_5 (or_5_out, comparator_115_eq, comparator_116_eq);
  D_Flip_Flop d_ff_65 (.clk(\ф_1_out_2 ), .D(comparator_114_eq), .Q(d_ff_65_q));  // open: Qn, preset, en, reset
  \Ф  \u_ф_1  (.in_1(Takt), .out_2(\ф_1_out_2 ));
  Register #(.width(6), .trigger("falling")) register_17 (
    .D(demultiplexer_15_out1), .Q(REG0), .clk(Takt), .clr(in_3));  // open: en
  Register #(.width(6), .trigger("falling")) register_18 (
    .D(demultiplexer_16_out1), .Q(REG1), .clk(Takt), .clr(in_3));  // open: en
  Register #(.width(6), .trigger("falling")) register_19 (
    .D(demultiplexer_17_out1), .Q(REG2), .clk(Takt), .clr(in_3));  // open: en
  Register #(.width(6), .trigger("falling")) register_20 (
    .D(demultiplexer_18_out1), .Q(REG3), .clk(Takt), .clr(in_3));  // open: en
  and and_49 (and_49_out, or_6_out, ~counter_2_q, Takt);  // AND_Gate
  Counter #(.width(3), .max('h4), .ongoal("stay"), .trigger("falling")) counter_3 (
    .Q(counter_3_q), .clk(Takt), .clr(d_ff_65_q));  // open: load, D, count, carry
  or or_6 (or_6_out, counter_3_q[0], counter_3_q[1], ~counter_3_q[2]);  // OR_Gate
  Register #(.width(4), .trigger("falling")) register_21 (
    .D(decsimbol_1_out_3), .Q(register_21_q), .clk(and_49_out), .clr(d_ff_65_q));  // open: en
  Register #(.width(4), .trigger("falling")) register_22 (
    .D(register_21_q), .Q(register_22_q), .clk(and_49_out), .clr(d_ff_65_q));  // open: en
  Register #(.width(4), .trigger("falling")) register_23 (
    .D(register_22_q), .Q(register_23_q), .clk(and_49_out), .clr(d_ff_65_q));  // open: en
  Register #(.width(4), .trigger("falling")) register_24 (
    .D(register_23_q), .Q(register_24_q), .clk(and_49_out), .clr(d_ff_65_q));  // open: en
  Comparator #(.width(7)) comparator_117 (.a(Simbol), .b(7'b1001010), .eq(comparator_117_eq));  // open: gt, lt
  and and_50 (and_50_out, d_ff_66_q, comparator_118_eq);
  Comparator #(.width(7)) comparator_118 (.a(Simbol), .b(7'b1001101), .eq(comparator_118_eq));  // open: gt, lt
  and and_51 (and_51_out, d_ff_67_q, comparator_119_eq);
  Comparator #(.width(7)) comparator_119 (.a(Simbol), .b(7'b1010000), .eq(comparator_119_eq));  // open: gt, lt
  and and_52 (and_52_out, d_ff_68_q, comparator_120_eq);
  Comparator #(.width(7)) comparator_120 (.a(Simbol), .b(7'b1000110), .eq(comparator_120_eq));  // open: gt, lt
  and and_53 (and_53_out, d_ff_69_q, comparator_121_eq);
  Comparator #(.width(7)) comparator_121 (.a(Simbol), .b(7'b0110000), .eq(comparator_121_eq));  // open: gt, lt
  and and_54 (and_54_out, d_ff_70_q, comparator_122_eq);
  Comparator #(.width(7)) comparator_122 (.a(Simbol), .b(7'b0100000), .eq(comparator_122_eq));  // open: gt, lt
  Comparator #(.width(7)) comparator_123 (.a(Simbol), .b(7'b1001010), .eq(comparator_123_eq));  // open: gt, lt
  and and_55 (and_55_out, d_ff_72_q, comparator_124_eq);
  Comparator #(.width(7)) comparator_124 (.a(Simbol), .b(7'b1001101), .eq(comparator_124_eq));  // open: gt, lt
  and and_56 (and_56_out, d_ff_73_q, comparator_125_eq);
  Comparator #(.width(7)) comparator_125 (.a(Simbol), .b(7'b1010000), .eq(comparator_125_eq));  // open: gt, lt
  and and_57 (and_57_out, d_ff_74_q, comparator_126_eq);
  Comparator #(.width(7)) comparator_126 (.a(Simbol), .b(7'b1000110), .eq(comparator_126_eq));  // open: gt, lt
  and and_58 (and_58_out, d_ff_75_q, comparator_127_eq);
  Comparator #(.width(7)) comparator_127 (.a(Simbol), .b(7'b0110001), .eq(comparator_127_eq));  // open: gt, lt
  and and_59 (and_59_out, d_ff_76_q, comparator_128_eq);
  Comparator #(.width(7)) comparator_128 (.a(Simbol), .b(7'b0100000), .eq(comparator_128_eq));  // open: gt, lt
  Comparator #(.width(7)) comparator_129 (.a(Simbol), .b(7'b1001010), .eq(comparator_129_eq));  // open: gt, lt
  and and_60 (and_60_out, d_ff_78_q, comparator_130_eq);
  Comparator #(.width(7)) comparator_130 (.a(Simbol), .b(7'b1001101), .eq(comparator_130_eq));  // open: gt, lt
  and and_61 (and_61_out, d_ff_79_q, comparator_131_eq);
  Comparator #(.width(7)) comparator_131 (.a(Simbol), .b(7'b1010000), .eq(comparator_131_eq));  // open: gt, lt
  and and_62 (and_62_out, d_ff_80_q, comparator_132_eq);
  Comparator #(.width(7)) comparator_132 (.a(Simbol), .b(7'b1000110), .eq(comparator_132_eq));  // open: gt, lt
  and and_63 (and_63_out, d_ff_81_q, comparator_133_eq);
  Comparator #(.width(7)) comparator_133 (.a(Simbol), .b(7'b0110010), .eq(comparator_133_eq));  // open: gt, lt
  and and_64 (and_64_out, d_ff_82_q, comparator_134_eq);
  Comparator #(.width(7)) comparator_134 (.a(Simbol), .b(7'b0100000), .eq(comparator_134_eq));  // open: gt, lt
  D_Flip_Flop d_ff_66 (.clk(Takt), .D(comparator_117_eq), .Q(d_ff_66_q));  // open: Qn, preset, en, reset
  D_Flip_Flop d_ff_67 (.clk(Takt), .D(and_50_out), .Q(d_ff_67_q));  // open: Qn, preset, en, reset
  D_Flip_Flop d_ff_68 (.clk(Takt), .D(and_51_out), .Q(d_ff_68_q));  // open: Qn, preset, en, reset
  D_Flip_Flop d_ff_69 (.clk(Takt), .D(and_52_out), .Q(d_ff_69_q));  // open: Qn, preset, en, reset
  D_Flip_Flop d_ff_70 (.clk(Takt), .D(and_53_out), .Q(d_ff_70_q));  // open: Qn, preset, en, reset
  D_Flip_Flop d_ff_71 (.clk(Takt), .D(and_54_out), .Q(SpJMPF0), .preset(SpJMPF0), .reset(in_3));  // open: Qn, en
  D_Flip_Flop d_ff_72 (.clk(Takt), .D(comparator_123_eq), .Q(d_ff_72_q));  // open: Qn, preset, en, reset
  D_Flip_Flop d_ff_73 (.clk(Takt), .D(and_55_out), .Q(d_ff_73_q));  // open: Qn, preset, en, reset
  D_Flip_Flop d_ff_74 (.clk(Takt), .D(and_56_out), .Q(d_ff_74_q));  // open: Qn, preset, en, reset
  D_Flip_Flop d_ff_75 (.clk(Takt), .D(and_57_out), .Q(d_ff_75_q));  // open: Qn, preset, en, reset
  D_Flip_Flop d_ff_76 (.clk(Takt), .D(and_58_out), .Q(d_ff_76_q));  // open: Qn, preset, en, reset
  D_Flip_Flop d_ff_77 (.clk(Takt), .D(and_59_out), .Q(SpJMPF1), .preset(SpJMPF1), .reset(in_3));  // open: Qn, en
  D_Flip_Flop d_ff_78 (.clk(Takt), .D(comparator_129_eq), .Q(d_ff_78_q));  // open: Qn, preset, en, reset
  D_Flip_Flop d_ff_79 (.clk(Takt), .D(and_60_out), .Q(d_ff_79_q));  // open: Qn, preset, en, reset
  D_Flip_Flop d_ff_80 (.clk(Takt), .D(and_61_out), .Q(d_ff_80_q));  // open: Qn, preset, en, reset
  D_Flip_Flop d_ff_81 (.clk(Takt), .D(and_62_out), .Q(d_ff_81_q));  // open: Qn, preset, en, reset
  D_Flip_Flop d_ff_82 (.clk(Takt), .D(and_63_out), .Q(d_ff_82_q));  // open: Qn, preset, en, reset
  D_Flip_Flop d_ff_83 (.clk(Takt), .D(and_64_out), .Q(SpJMPF2), .preset(SpJMPF2), .reset(in_3));  // open: Qn, en
  Register #(.width(16)) register_25 (
    .D({register_24_q, register_23_q, register_22_q, register_21_q}), .Q(out_6), .clk(SpINP));  // open: en, clr
  Demultiplexer #(.width(6)) demultiplexer_19 (
    .out1(demultiplexer_19_out1), .in(6'b001000), .sel(d_ff_70_q));  // open: out0, en
  Demultiplexer #(.width(6)) demultiplexer_20 (
    .out1(demultiplexer_20_out1), .in(6'b001001), .sel(d_ff_76_q));  // open: out0, en
  Demultiplexer #(.width(6)) demultiplexer_21 (
    .out1(demultiplexer_21_out1), .in(6'b001010), .sel(d_ff_82_q));  // open: out0, en
  Register #(.width(6), .trigger("falling")) register_26 (
    .D(demultiplexer_19_out1), .Q(JMPF0), .clk(d_ff_70_q), .clr(in_3));  // open: en
  Register #(.width(6), .trigger("falling")) register_27 (
    .D(demultiplexer_20_out1), .Q(JMPF1), .clk(d_ff_76_q), .clr(in_3));  // open: en
  Register #(.width(6), .trigger("falling")) register_28 (
    .D(demultiplexer_21_out1), .Q(JMPF2), .clk(d_ff_82_q), .clr(in_3));  // open: en
  Comparator #(.width(7)) comparator_135 (.a(Simbol), .b(7'b1001010), .eq(comparator_135_eq));  // open: gt, lt
  Comparator #(.width(7)) comparator_136 (.a(Simbol), .b(7'b1001101), .eq(comparator_136_eq));  // open: gt, lt
  Comparator #(.width(7)) comparator_137 (.a(Simbol), .b(7'b1010000), .eq(comparator_137_eq));  // open: gt, lt
  Comparator #(.width(7)) comparator_138 (.a(Simbol), .b(7'b1000110), .eq(comparator_138_eq));  // open: gt, lt
  Comparator #(.width(7)) comparator_139 (.a(Simbol), .b(7'b0110011), .eq(comparator_139_eq));  // open: gt, lt
  Comparator #(.width(7)) comparator_140 (.a(Simbol), .b(7'b0100000), .eq(comparator_140_eq));  // open: gt, lt
  Comparator #(.width(7)) comparator_141 (.a(Simbol), .b(7'b1001010), .eq(comparator_141_eq));  // open: gt, lt
  Comparator #(.width(7)) comparator_142 (.a(Simbol), .b(7'b1001101), .eq(comparator_142_eq));  // open: gt, lt
  Comparator #(.width(7)) comparator_143 (.a(Simbol), .b(7'b1010000), .eq(comparator_143_eq));  // open: gt, lt
  Comparator #(.width(7)) comparator_144 (.a(Simbol), .b(7'b1000110), .eq(comparator_144_eq));  // open: gt, lt
  Comparator #(.width(7)) comparator_145 (.a(Simbol), .b(7'b0110100), .eq(comparator_145_eq));  // open: gt, lt
  Comparator #(.width(7)) comparator_146 (.a(Simbol), .b(7'b0100000), .eq(comparator_146_eq));  // open: gt, lt
  Comparator #(.width(7)) comparator_147 (.a(Simbol), .b(7'b1001010), .eq(comparator_147_eq));  // open: gt, lt
  Comparator #(.width(7)) comparator_148 (.a(Simbol), .b(7'b1001101), .eq(comparator_148_eq));  // open: gt, lt
  Comparator #(.width(7)) comparator_149 (.a(Simbol), .b(7'b1010000), .eq(comparator_149_eq));  // open: gt, lt
  Comparator #(.width(7)) comparator_150 (.a(Simbol), .b(7'b1000110), .eq(comparator_150_eq));  // open: gt, lt
  Comparator #(.width(7)) comparator_151 (.a(Simbol), .b(7'b0110101), .eq(comparator_151_eq));  // open: gt, lt
  Comparator #(.width(7)) comparator_152 (.a(Simbol), .b(7'b0100000), .eq(comparator_152_eq));  // open: gt, lt
  D_Flip_Flop d_ff_84 (.clk(Takt), .D(comparator_135_eq), .Q(d_ff_84_q));  // open: Qn, preset, en, reset
  D_Flip_Flop d_ff_85 (.clk(Takt), .D(and_65_out), .Q(d_ff_85_q));  // open: Qn, preset, en, reset
  and and_65 (and_65_out, d_ff_84_q, comparator_136_eq);
  D_Flip_Flop d_ff_86 (.clk(Takt), .D(and_66_out), .Q(d_ff_86_q));  // open: Qn, preset, en, reset
  and and_66 (and_66_out, d_ff_85_q, comparator_137_eq);
  D_Flip_Flop d_ff_87 (.clk(Takt), .D(and_67_out), .Q(d_ff_87_q));  // open: Qn, preset, en, reset
  and and_67 (and_67_out, d_ff_86_q, comparator_138_eq);
  D_Flip_Flop d_ff_88 (.clk(Takt), .D(and_68_out), .Q(d_ff_88_q));  // open: Qn, preset, en, reset
  and and_68 (and_68_out, d_ff_87_q, comparator_139_eq);
  D_Flip_Flop d_ff_89 (.clk(Takt), .D(and_69_out), .Q(SpJMPF3), .preset(SpJMPF3), .reset(in_3));  // open: Qn, en
  and and_69 (and_69_out, d_ff_88_q, comparator_140_eq);
  D_Flip_Flop d_ff_90 (.clk(Takt), .D(comparator_141_eq), .Q(d_ff_90_q));  // open: Qn, preset, en, reset
  D_Flip_Flop d_ff_91 (.clk(Takt), .D(and_70_out), .Q(d_ff_91_q));  // open: Qn, preset, en, reset
  and and_70 (and_70_out, d_ff_90_q, comparator_142_eq);
  D_Flip_Flop d_ff_92 (.clk(Takt), .D(and_71_out), .Q(d_ff_92_q));  // open: Qn, preset, en, reset
  and and_71 (and_71_out, d_ff_91_q, comparator_143_eq);
  D_Flip_Flop d_ff_93 (.clk(Takt), .D(and_72_out), .Q(d_ff_93_q));  // open: Qn, preset, en, reset
  and and_72 (and_72_out, d_ff_92_q, comparator_144_eq);
  D_Flip_Flop d_ff_94 (.clk(Takt), .D(and_73_out), .Q(d_ff_94_q));  // open: Qn, preset, en, reset
  and and_73 (and_73_out, d_ff_93_q, comparator_145_eq);
  D_Flip_Flop d_ff_95 (.clk(Takt), .D(and_74_out), .Q(SpJMPF4), .preset(SpJMPF4), .reset(in_3));  // open: Qn, en
  and and_74 (and_74_out, d_ff_94_q, comparator_146_eq);
  D_Flip_Flop d_ff_96 (.clk(Takt), .D(comparator_147_eq), .Q(d_ff_96_q));  // open: Qn, preset, en, reset
  D_Flip_Flop d_ff_97 (.clk(Takt), .D(and_75_out), .Q(d_ff_97_q));  // open: Qn, preset, en, reset
  and and_75 (and_75_out, d_ff_96_q, comparator_148_eq);
  D_Flip_Flop d_ff_98 (.clk(Takt), .D(and_76_out), .Q(d_ff_98_q));  // open: Qn, preset, en, reset
  and and_76 (and_76_out, d_ff_97_q, comparator_149_eq);
  D_Flip_Flop d_ff_99 (.clk(Takt), .D(and_77_out), .Q(d_ff_99_q));  // open: Qn, preset, en, reset
  and and_77 (and_77_out, d_ff_98_q, comparator_150_eq);
  D_Flip_Flop d_ff_100 (.clk(Takt), .D(and_78_out), .Q(d_ff_100_q));  // open: Qn, preset, en, reset
  and and_78 (and_78_out, d_ff_99_q, comparator_151_eq);
  D_Flip_Flop d_ff_101 (.clk(Takt), .D(and_79_out), .Q(SpJMPF5), .preset(SpJMPF5), .reset(in_3));  // open: Qn, en
  and and_79 (and_79_out, d_ff_100_q, comparator_152_eq);
  Demultiplexer #(.width(6)) demultiplexer_22 (
    .out1(demultiplexer_22_out1), .in(6'b001011), .sel(d_ff_88_q));  // open: out0, en
  Demultiplexer #(.width(6)) demultiplexer_23 (
    .out1(demultiplexer_23_out1), .in(6'b001100), .sel(d_ff_94_q));  // open: out0, en
  Demultiplexer #(.width(6)) demultiplexer_24 (
    .out1(demultiplexer_24_out1), .in(6'b001101), .sel(d_ff_100_q));  // open: out0, en
  Register #(.width(6), .trigger("falling")) register_29 (
    .D(demultiplexer_22_out1), .Q(JMPF3), .clk(d_ff_88_q), .clr(in_3));  // open: en
  Register #(.width(6), .trigger("falling")) register_30 (
    .D(demultiplexer_23_out1), .Q(JMPF4), .clk(d_ff_94_q), .clr(in_3));  // open: en
  Register #(.width(6), .trigger("falling")) register_31 (
    .D(demultiplexer_24_out1), .Q(JMPF5), .clk(d_ff_100_q), .clr(in_3));  // open: en

  // Other names for the same wires on the sheet: Clear = in_3; INSTR[5:0] = out_4; SPACE = out_5

  // Notes on the sheet:
  //   INP
  //   OUT
  //   MOV
  //   LDO
  //   STO
  //   MV
  //   INVA
  //   AND
  //   SUB
  //   ADD
  //   OR
  //   XOR
  //   SHL
  //   SHR
  //   REG0
  //   REG0
  //   REG0
  //   REG3
  //   JMPF0
  //   JMPF1
  //   JMPF2
  //   JMPF3
  //   JMPF4
  //   JMPF5
endmodule

module Iskl (
  input  y0,
  input  y1,
  input  y2,
  input  y3,
  input  y4,
  input  y5,
  output x
);

  wire and_1_out, and_2_out, and_3_out, and_4_out, not_1_out, not_2_out, not_3_out, not_4_out, not_5_out,
       not_6_out;

  not not_1 (not_1_out, y0);
  not not_2 (not_2_out, y1);
  not not_3 (not_3_out, y3);
  not not_4 (not_4_out, y4);
  and and_1 (and_1_out, not_1_out, not_2_out);
  not not_5 (not_5_out, y2);
  and and_2 (and_2_out, not_3_out, not_4_out);
  not not_6 (not_6_out, y5);
  and and_3 (and_3_out, and_1_out, not_5_out);
  and and_4 (and_4_out, and_2_out, not_6_out);
  and and_5 (x, and_3_out, and_4_out);
endmodule

module _10Takts (
  input  y0,
  input  y1,
  input  y2,
  input  y3,
  output x
);

  wire not_1_out, not_2_out, not_3_out, not_4_out, or_1_out, or_2_out;

  not not_1 (not_1_out, y0);
  or or_1 (or_1_out, not_1_out, not_2_out);
  not not_2 (not_2_out, y1);
  not not_3 (not_3_out, y2);
  or or_2 (or_2_out, not_3_out, not_4_out);
  not not_4 (not_4_out, y3);
  or or_3 (x, or_1_out, or_2_out);
endmodule

module Read (
  input  in_1,
  input  in_2,
  output out_3,
  output out_4
);

  wire and_1_out, and_2_out, n1takts_1_x, not_1_out, or_1_out, undriven, \ф_1_out_2 , \ф_2_out_2 ,
       \ф_4_out_2 ;
  wire [1:0] counter_2_q;
  wire [5:0] counter_1_q;

  _10Takts u_10takts_1 (.y3(undriven));  // open: y0, y1, y2, x
  or or_1 (or_1_out, ~counter_1_q[0], ~counter_1_q[1], ~counter_1_q[2], ~counter_1_q[3], ~counter_1_q[4], ~counter_1_q[5]);  // OR_Gate
  Counter #(.width(6), .max('h3f), .ongoal("stay")) counter_1 (
    .Q(counter_1_q), .clk(in_1), .clr(in_2));  // open: load, D, count, carry
  // AND_Gate and_1 has open pins: out=and_1_out
  and and_2 (and_2_out, or_1_out, in_1);
  not not_1 (not_1_out, or_1_out);
  Counter #(.width(2), .max('h2), .ongoal("stay")) counter_2 (
    .Q(counter_2_q), .clk(and_2_out), .clr(not_1_out));  // open: load, D, count, carry
  \Ф  \u_ф_1  (.in_1(and_2_out), .out_2(\ф_1_out_2 ));
  \Ф  \u_ф_2  (.in_1(\ф_1_out_2 ), .out_2(\ф_2_out_2 ));
  \Ф  \u_ф_3  (.in_1(\ф_4_out_2 ), .out_2(out_3));
  \Ф  \u_ф_4  (.in_1(\ф_2_out_2 ), .out_2(\ф_4_out_2 ));
  _1TAKTS u_1takts_1 (.Y0(counter_2_q[1]), .Y1(counter_2_q[0]), .X(n1takts_1_x));
  and and_3 (out_4, n1takts_1_x, and_2_out);
endmodule

module _1Takts (
  input  in_1,
  input  in_2,
  output out_3
);

  wire [1:0] counter_1_q;

  Counter #(.width(2), .max('h2), .ongoal("stay")) counter_1 (
    .Q(counter_1_q), .clk(in_1), .clr(in_2));  // open: load, D, count, carry
  or or_1 (out_3, counter_1_q[0], ~counter_1_q[1]);  // OR_Gate
endmodule

module _1TAKTS (
  input  Y0,
  input  Y1,
  output X
);

  not not_1 (X, Y0);
endmodule

module ReadNumber (
  input  y0,
  input  y1,
  input  y2,
  output x
);

  wire and_1_out, and_2_out, not_1_out, not_2_out;

  not not_1 (not_1_out, y2);
  not not_2 (not_2_out, y2);
  and and_1 (and_1_out, y1, not_1_out);
  and and_2 (and_2_out, y0, not_2_out);
  or or_1 (x, and_1_out, and_2_out);
endmodule

module DecSimbol (
  input  [6:0] in_1,
  input  in_2,
  output [3:0] out_3
);

  wire and_1_out, comparator_1_eq, comparator_2_eq, comparator_3_eq, comparator_4_eq, comparator_5_eq,
       comparator_6_eq, comparator_7_eq, comparator_8_eq, comparator_9_eq, comparator_10_eq,
       comparator_11_eq, comparator_12_eq, comparator_13_eq, comparator_14_eq, comparator_15_eq,
       comparator_16_eq, comparator_17_eq, comparator_18_gt, or_1_out, \ф_1_out_2 , \ф_2_out_2 , \ф_3_out_2 ,
       \ф_4_out_2 ;
  wire [6:0] multiplexer_1_out, register_1_q, register_2_q, subtractor_1_out;
  wire [7:0] bit_extender_1_out;

  Comparator #(.width(7)) comparator_1 (.a(in_1), .b(7'b0110000), .eq(comparator_1_eq));  // open: gt, lt
  Comparator #(.width(7)) comparator_2 (.a(in_1), .b(7'b0110001), .eq(comparator_2_eq));  // open: gt, lt
  Comparator #(.width(7)) comparator_3 (.a(in_1), .b(7'b0110010), .eq(comparator_3_eq));  // open: gt, lt
  Comparator #(.width(7)) comparator_4 (.a(in_1), .b(7'b0110011), .eq(comparator_4_eq));  // open: gt, lt
  Comparator #(.width(7)) comparator_5 (.a(in_1), .b(7'b0110100), .eq(comparator_5_eq));  // open: gt, lt
  Comparator #(.width(7)) comparator_6 (.a(in_1), .b(7'b0110101), .eq(comparator_6_eq));  // open: gt, lt
  Comparator #(.width(7)) comparator_7 (.a(in_1), .b(7'b0110110), .eq(comparator_7_eq));  // open: gt, lt
  Comparator #(.width(7)) comparator_8 (.a(in_1), .b(7'b0110111), .eq(comparator_8_eq));  // open: gt, lt
  Comparator #(.width(7)) comparator_9 (.a(in_1), .b(7'b0111000), .eq(comparator_9_eq));  // open: gt, lt
  Comparator #(.width(7)) comparator_10 (.a(in_1), .b(7'b0111001), .eq(comparator_10_eq));  // open: gt, lt
  Comparator #(.width(7)) comparator_11 (.a(in_1), .b(7'b1000001), .eq(comparator_11_eq));  // open: gt, lt
  Comparator #(.width(7)) comparator_12 (.a(in_1), .b(7'b1000010), .eq(comparator_12_eq));  // open: gt, lt
  Comparator #(.width(7)) comparator_13 (.a(in_1), .b(7'b1000011), .eq(comparator_13_eq));  // open: gt, lt
  Comparator #(.width(7)) comparator_14 (.a(in_1), .b(7'b1000100), .eq(comparator_14_eq));  // open: gt, lt
  Comparator #(.width(7)) comparator_15 (.a(in_1), .b(7'b1000101), .eq(comparator_15_eq));  // open: gt, lt
  Comparator #(.width(7)) comparator_16 (.a(in_1), .b(7'b1000110), .eq(comparator_16_eq));  // open: gt, lt
  Comparator #(.width(7)) comparator_17 (.a(in_1), .b(7'b0101110), .eq(comparator_17_eq));  // open: gt, lt
  or or_1 (or_1_out, comparator_1_eq, comparator_2_eq, comparator_3_eq, comparator_4_eq, comparator_5_eq, comparator_6_eq, comparator_7_eq, comparator_8_eq, comparator_9_eq, comparator_10_eq, comparator_11_eq, comparator_12_eq, comparator_13_eq, comparator_14_eq, comparator_15_eq, comparator_16_eq);
  and and_1 (and_1_out, or_1_out, in_2);
  Register #(.width(7)) register_1 (.D(in_1), .Q(register_1_q), .clk(and_1_out));  // open: en, clr
  assign bit_extender_1_out = {{1{1'b0}}, register_1_q};  // Bit_Extender bit_extender_1
  Multiplexer #(.width(7)) multiplexer_1 (
    .in0(7'b0110000), .in1(7'b0110111), .out(multiplexer_1_out), .sel(comparator_18_gt));  // open: en
  Comparator comparator_18 (.a(bit_extender_1_out), .b(8'h40), .gt(comparator_18_gt));  // open: eq, lt
  Subtractor #(.width(7)) subtractor_1 (
    .a(register_1_q), .b(multiplexer_1_out), .out(subtractor_1_out));  // open: bin, bout
  Bit_Extender #(.in_width(7), .out_width(4)) bit_extender_2 (.in(register_2_q), .out(out_3));
  Register #(.width(7)) register_2 (
    .D(subtractor_1_out), .Q(register_2_q), .clk(\ф_1_out_2 ), .clr(comparator_17_eq));  // open: en
  \Ф  \u_ф_1  (.in_1(\ф_2_out_2 ), .out_2(\ф_1_out_2 ));
  \Ф  \u_ф_2  (.in_1(\ф_3_out_2 ), .out_2(\ф_2_out_2 ));
  \Ф  \u_ф_3  (.in_1(\ф_4_out_2 ), .out_2(\ф_3_out_2 ));
  \Ф  \u_ф_4  (.in_1(and_1_out), .out_2(\ф_4_out_2 ));
endmodule
