// Logisim project БВТ2003_Тураев_Некруз_№10(Star1).circ as structural Verilog: 13 circuits, main circuit Компилятор
module \Компилятор  (
  output [5:0] out_1,
  output [9:0] out_2,
  output [6:0] XOR,
  output [5:0] out_4,
  output [5:0] OR,
  output [6:0] SUB,
  output [5:0] OUT
);

  wire and_1_out, and_2_out, and_3_out, and_4_out, and_5_out, and_6_out, and_7_out, and_8_out, and_9_out,
       and_10_out, and_11_out, and_12_out, and_13_out, and_14_out, and_15_out, button_1_out, button_2_out,
       comparator_1_eq, comparator_2_eq, comparator_3_eq, comparator_4_eq, comparator_5_eq, comparator_6_eq,
       comparator_7_eq, comparator_8_eq, comparator_9_eq, comparator_10_eq, comparator_11_eq,
       comparator_12_eq, comparator_13_eq, comparator_14_eq, comparator_15_eq, comparator_16_eq,
       comparator_17_eq, comparator_18_eq, comparator_19_eq, comparator_20_eq, comparator_21_eq,
       comparator_22_eq, comparator_23_eq, comparator_24_eq, comparator_25_eq, comparator_26_eq,
       comparator_27_eq, comparator_28_eq, comparator_29_eq, comparator_30_eq, comparator_31_eq,
       comparator_32_eq, comparator_33_eq, comparator_34_eq, comparator_35_eq, comparator_36_eq, d_ff_1_q,
       d_ff_2_q, d_ff_3_q, d_ff_4_q, d_ff_5_q, d_ff_6_q, d_ff_7_q, d_ff_8_q, d_ff_9_q, d_ff_10_q, d_ff_11_q,
       d_ff_12_q, d_ff_13_q, d_ff_13_qn, d_ff_14_q, d_ff_15_q, d_ff_16_q, d_ff_17_q, d_ff_18_q, d_ff_19_q,
       d_ff_20_q, d_ff_21_q, d_ff_22_q, d_ff_23_q, d_ff_24_q, d_ff_25_q, d_ff_26_q, d_ff_27_q, d_ff_28_q,
       d_ff_29_q, d_ff_30_q, d_ff_31_q, d_ff_32_q, d_ff_33_q, d_ff_34_q, d_ff_35_q, d_ff_36_q, register_1_q,
       register_2_q, undriven, \ф_1_out_2 , \ф_2_out_2 ;
  wire [3:0] multiplexer_1_out;
  wire [5:0] demultiplexer_3_out1, demultiplexer_4_out1;
  wire [6:0] demultiplexer_8_out1, demultiplexer_9_out1, demultiplexer_10_out1, demultiplexer_11_out1,
       demultiplexer_12_out1, demultiplexer_13_out1, demultiplexer_14_out1, demultiplexer_15_out1,
       demultiplexer_16_out1, demultiplexer_17_out1, demultiplexer_18_out1, demultiplexer_19_out1,
       demultiplexer_20_out1, demultiplexer_21_out1, demultiplexer_22_out1, demultiplexer_23_out1,
       keyboard_1_data, multiplexer_2_out, register_5_q, register_6_q;

  Button button_1 (.out(button_1_out));
  Button button_2 (.out(button_2_out));
  Comparator #(.width(7)) comparator_1 (.a(keyboard_1_data), .b(7'b1011000), .eq(comparator_1_eq));  // open: gt, lt
  and and_1 (and_1_out, d_ff_1_q, comparator_2_eq);
  Comparator #(.width(7)) comparator_2 (.a(keyboard_1_data), .b(7'b1001111), .eq(comparator_2_eq));  // open: gt, lt
  and and_2 (and_2_out, d_ff_2_q, comparator_3_eq);
  Comparator #(.width(7)) comparator_3 (.a(keyboard_1_data), .b(7'b1010010), .eq(comparator_3_eq));  // open: gt, lt
  Comparator #(.width(7)) comparator_4 (.a(keyboard_1_data), .b(7'b1010011), .eq(comparator_4_eq));  // open: gt, lt
  and and_3 (and_3_out, d_ff_4_q, comparator_5_eq);
  Comparator #(.width(7)) comparator_5 (.a(keyboard_1_data), .b(7'b1010101), .eq(comparator_5_eq));  // open: gt, lt
  and and_4 (and_4_out, d_ff_5_q, comparator_6_eq);
  Comparator #(.width(7)) comparator_6 (.a(keyboard_1_data), .b(7'b1000010), .eq(comparator_6_eq));  // open: gt, lt
  Keyboard keyboard_1 (.clk(button_1_out), .data(keyboard_1_data));  // open: re, clr, avail
  D_Flip_Flop d_ff_1 (.clk(button_1_out), .D(comparator_1_eq), .Q(d_ff_1_q));  // open: Qn, preset, en, reset
  D_Flip_Flop d_ff_2 (.clk(button_1_out), .D(and_1_out), .Q(d_ff_2_q));  // open: Qn, preset, en, reset
  D_Flip_Flop d_ff_3 (.clk(button_1_out), .D(and_2_out), .Q(d_ff_3_q));  // open: Qn, preset, en, reset
  D_Flip_Flop d_ff_4 (.clk(button_1_out), .D(comparator_4_eq), .Q(d_ff_4_q));  // open: Qn, preset, en, reset
  D_Flip_Flop d_ff_5 (.clk(button_1_out), .D(and_3_out), .Q(d_ff_5_q));  // open: Qn, preset, en, reset
  D_Flip_Flop d_ff_6 (.clk(button_1_out), .D(and_4_out), .Q(d_ff_6_q));  // open: Qn, preset, en, reset
  Demultiplexer #(.width(7)) demultiplexer_1 (.out1(XOR), .in(7'b0010101), .sel(d_ff_3_q));  // open: out0, en
  Demultiplexer #(.width(7)) demultiplexer_2 (.out1(SUB), .in(7'b0010010), .sel(d_ff_6_q));  // open: out0, en
  ADR adr_1 ();  // open: in_2, in_3, out_4, in_1
  // Probe on keyboard_1_data
  Comparator #(.width(7)) comparator_7 (.a(keyboard_1_data), .b(7'b1001001), .eq(comparator_7_eq));  // open: gt, lt
  Comparator #(.width(7)) comparator_8 (.a(keyboard_1_data), .b(7'b1001110), .eq(comparator_8_eq));  // open: gt, lt
  Comparator #(.width(7)) comparator_9 (.a(keyboard_1_data), .b(7'b1010000), .eq(comparator_9_eq));  // open: gt, lt
  Comparator #(.width(7)) comparator_10 (.a(keyboard_1_data), .b(7'b0100000), .eq(comparator_10_eq));  // open: gt, lt
  Comparator #(.width(7)) comparator_11 (.a(keyboard_1_data), .b(7'b1001111), .eq(comparator_11_eq));  // open: gt, lt
  Comparator #(.width(7)) comparator_12 (.a(keyboard_1_data), .b(7'b1010101), .eq(comparator_12_eq));  // open: gt, lt
  Comparator #(.width(7)) comparator_13 (.a(keyboard_1_data), .b(7'b1010100), .eq(comparator_13_eq));  // open: gt, lt
  Comparator #(.width(7)) comparator_14 (.a(keyboard_1_data), .b(7'b0100000), .eq(comparator_14_eq));  // open: gt, lt
  TTY tty_1 (.data(keyboard_1_data), .clk(button_1_out), .clr(button_2_out));  // open: we
  and and_5 (and_5_out, d_ff_7_q, comparator_8_eq);
  and and_6 (and_6_out, d_ff_8_q, comparator_9_eq);
  and and_7 (and_7_out, d_ff_9_q, comparator_10_eq);
  ADR adr_2 (.in_2(keyboard_1_data), .in_3(button_1_out), .out_4(out_2), .in_1(register_1_q));
  and and_8 (and_8_out, d_ff_11_q, comparator_12_eq);
  and and_9 (and_9_out, d_ff_12_q, comparator_13_eq);
  and and_10 (and_10_out, d_ff_13_qn, comparator_14_eq);
  D_Flip_Flop d_ff_7 (.clk(button_1_out), .D(comparator_7_eq), .Q(d_ff_7_q));  // open: Qn, preset, en, reset
  D_Flip_Flop d_ff_8 (.clk(button_1_out), .D(and_5_out), .Q(d_ff_8_q));  // open: Qn, preset, en, reset
  D_Flip_Flop d_ff_9 (.clk(button_1_out), .D(and_6_out), .Q(d_ff_9_q));  // open: Qn, preset, en, reset
  D_Flip_Flop d_ff_10 (.clk(button_1_out), .D(and_7_out), .Q(d_ff_10_q));  // open: Qn, preset, en, reset
  Register #(.width(1)) register_1 (.D(d_ff_10_q), .Q(register_1_q), .clk(\ф_1_out_2 ), .clr(d_ff_7_q));  // open: en
  \Ф  \u_ф_1  (.in_1(d_ff_10_q), .out_2(\ф_1_out_2 ));
  // Probe on out_2
  D_Flip_Flop d_ff_11 (.clk(button_1_out), .D(comparator_11_eq), .Q(d_ff_11_q));  // open: Qn, preset, en, reset
  D_Flip_Flop d_ff_12 (.clk(button_1_out), .D(and_8_out), .Q(d_ff_12_q));  // open: Qn, preset, en, reset
  Demultiplexer #(.width(6)) demultiplexer_3 (
    .out1(demultiplexer_3_out1), .in(6'b000010), .sel(d_ff_13_q));  // open: out0, en
  D_Flip_Flop d_ff_13 (.clk(button_1_out), .D(and_9_out), .Q(d_ff_13_q), .Qn(d_ff_13_qn));  // open: preset, en, reset
  D_Flip_Flop d_ff_14 (.clk(button_1_out), .D(and_10_out), .Q(d_ff_14_q));  // open: Qn, preset, en, reset
  Register #(.width(1)) register_2 (.D(d_ff_14_q), .Q(register_2_q), .clk(\ф_2_out_2 ), .clr(undriven));  // open: en
  \Ф  \u_ф_2  (.in_1(d_ff_14_q), .out_2(\ф_2_out_2 ));
  Demultiplexer #(.width(6)) demultiplexer_4 (
    .out1(demultiplexer_4_out1), .in(6'b000001), .sel(d_ff_9_q));  // open: out0, en
  Register #(.width(6), .trigger("falling")) register_3 (.D(demultiplexer_3_out1), .Q(OUT));  // open: en, clk, clr
  Register #(.width(6), .trigger("falling")) register_4 (.D(demultiplexer_4_out1), .clk(d_ff_9_q));  // open: en, Q, clr
  // Probe on out_2
  Comparator #(.width(7)) comparator_15 (.a(keyboard_1_data), .b(7'b1001001), .eq(comparator_15_eq));  // open: gt, lt
  Comparator #(.width(7)) comparator_16 (.a(keyboard_1_data), .b(7'b1001110), .eq(comparator_16_eq));  // open: gt, lt
  Comparator #(.width(7)) comparator_17 (.a(keyboard_1_data), .b(7'b1010110), .eq(comparator_17_eq));  // open: gt, lt
  Comparator #(.width(7)) comparator_18 (.a(keyboard_1_data), .b(7'b1000001), .eq(comparator_18_eq));  // open: gt, lt
  Comparator #(.width(7)) comparator_19 (.a(keyboard_1_data), .b(7'b1001111), .eq(comparator_19_eq));  // open: gt, lt
  Comparator #(.width(7)) comparator_20 (.a(keyboard_1_data), .b(7'b1010010), .eq(comparator_20_eq));  // open: gt, lt
  and and_11 (and_11_out, d_ff_15_q, comparator_16_eq);
  and and_12 (and_12_out, d_ff_16_q, comparator_17_eq);
  and and_13 (and_13_out, d_ff_17_q, comparator_18_eq);
  buf and_14 (and_14_out, comparator_19_eq);  // AND_Gate
  and and_15 (and_15_out, d_ff_19_q, comparator_20_eq);
  D_Flip_Flop d_ff_15 (.clk(button_1_out), .D(comparator_15_eq), .Q(d_ff_15_q));  // open: Qn, preset, en, reset
  D_Flip_Flop d_ff_16 (.clk(button_1_out), .D(and_11_out), .Q(d_ff_16_q));  // open: Qn, preset, en, reset
  D_Flip_Flop d_ff_17 (.clk(button_1_out), .D(and_12_out), .Q(d_ff_17_q));  // open: Qn, preset, en, reset
  Demultiplexer #(.width(6)) demultiplexer_5 (.out1(out_4), .in(6'b011000), .sel(d_ff_18_q));  // open: out0, en
  D_Flip_Flop d_ff_18 (.clk(button_1_out), .D(and_13_out), .Q(d_ff_18_q));  // open: Qn, preset, en, reset
  D_Flip_Flop d_ff_19 (.clk(button_1_out), .D(and_14_out), .Q(d_ff_19_q));  // open: Qn, preset, en, reset
  Demultiplexer #(.width(6)) demultiplexer_6 (.out1(OR), .in(6'b010100), .sel(d_ff_20_q));  // open: out0, en
  D_Flip_Flop d_ff_20 (.clk(button_1_out), .D(and_15_out), .Q(d_ff_20_q));  // open: Qn, preset, en, reset
  Comparator #(.width(7)) comparator_21 (.a(keyboard_1_data), .b(7'b0110000), .eq(comparator_21_eq));  // open: gt, lt
  Comparator #(.width(7)) comparator_22 (.a(keyboard_1_data), .b(7'b0110001), .eq(comparator_22_eq));  // open: gt, lt
  Comparator #(.width(7)) comparator_23 (.a(keyboard_1_data), .b(7'b0110010), .eq(comparator_23_eq));  // open: gt, lt
  Comparator #(.width(7)) comparator_24 (.a(keyboard_1_data), .b(7'b0110011), .eq(comparator_24_eq));  // open: gt, lt
  Comparator #(.width(7)) comparator_25 (.a(keyboard_1_data), .b(7'b0110100), .eq(comparator_25_eq));  // open: gt, lt
  Comparator #(.width(7)) comparator_26 (.a(keyboard_1_data), .b(7'b0110101), .eq(comparator_26_eq));  // open: gt, lt
  Comparator #(.width(7)) comparator_27 (.a(keyboard_1_data), .b(7'b0110110), .eq(comparator_27_eq));  // open: gt, lt
  Comparator #(.width(7)) comparator_28 (.a(keyboard_1_data), .b(7'b0110111), .eq(comparator_28_eq));  // open: gt, lt
  Comparator #(.width(7)) comparator_29 (.a(keyboard_1_data), .b(7'b0111000), .eq(comparator_29_eq));  // open: gt, lt
  Comparator #(.width(7)) comparator_30 (.a(keyboard_1_data), .b(7'b0111001), .eq(comparator_30_eq));  // open: gt, lt
  Comparator #(.width(7)) comparator_31 (.a(keyboard_1_data), .b(7'b1000001), .eq(comparator_31_eq));  // open: gt, lt
  Comparator #(.width(7)) comparator_32 (.a(keyboard_1_data), .b(7'b1000010), .eq(comparator_32_eq));  // open: gt, lt
  Comparator #(.width(7)) comparator_33 (.a(keyboard_1_data), .b(7'b1000011), .eq(comparator_33_eq));  // open: gt, lt
  Comparator #(.width(7)) comparator_34 (.a(keyboard_1_data), .b(7'b1000100), .eq(comparator_34_eq));  // open: gt, lt
  Comparator #(.width(7)) comparator_35 (.a(keyboard_1_data), .b(7'b1000101), .eq(comparator_35_eq));  // open: gt, lt
  Comparator #(.width(7)) comparator_36 (.a(keyboard_1_data), .b(7'b1000110), .eq(comparator_36_eq));  // open: gt, lt
  D_Flip_Flop d_ff_21 (.clk(button_1_out), .D(comparator_21_eq), .Q(d_ff_21_q));  // open: Qn, preset, en, reset
  D_Flip_Flop d_ff_22 (.clk(button_1_out), .D(comparator_22_eq), .Q(d_ff_22_q));  // open: Qn, preset, en, reset
  D_Flip_Flop d_ff_23 (.clk(button_1_out), .D(comparator_23_eq), .Q(d_ff_23_q));  // open: Qn, preset, en, reset
  D_Flip_Flop d_ff_24 (.clk(button_1_out), .D(comparator_24_eq), .Q(d_ff_24_q));  // open: Qn, preset, en, reset
  D_Flip_Flop d_ff_25 (.clk(button_1_out), .D(comparator_25_eq), .Q(d_ff_25_q));  // open: Qn, preset, en, reset
  D_Flip_Flop d_ff_26 (.clk(button_1_out), .D(comparator_26_eq), .Q(d_ff_26_q));  // open: Qn, preset, en, reset
  D_Flip_Flop d_ff_27 (.clk(button_1_out), .D(comparator_27_eq), .Q(d_ff_27_q));  // open: Qn, preset, en, reset
  D_Flip_Flop d_ff_28 (.clk(button_1_out), .D(comparator_28_eq), .Q(d_ff_28_q));  // open: Qn, preset, en, reset
  D_Flip_Flop d_ff_29 (.clk(button_1_out), .D(comparator_29_eq), .Q(d_ff_29_q));  // open: Qn, preset, en, reset
  D_Flip_Flop d_ff_30 (.clk(button_1_out), .D(comparator_30_eq), .Q(d_ff_30_q));  // open: Qn, preset, en, reset
  D_Flip_Flop d_ff_31 (.clk(button_1_out), .D(comparator_31_eq), .Q(d_ff_31_q));  // open: Qn, preset, en, reset
  D_Flip_Flop d_ff_32 (.clk(button_1_out), .D(comparator_32_eq), .Q(d_ff_32_q));  // open: Qn, preset, en, reset
  D_Flip_Flop d_ff_33 (.clk(button_1_out), .D(comparator_33_eq), .Q(d_ff_33_q));  // open: Qn, preset, en, reset
  D_Flip_Flop d_ff_34 (.clk(button_1_out), .D(comparator_34_eq), .Q(d_ff_34_q));  // open: Qn, preset, en, reset
  D_Flip_Flop d_ff_35 (.clk(button_1_out), .D(comparator_35_eq), .Q(d_ff_35_q));  // open: Qn, preset, en, reset
  D_Flip_Flop d_ff_36 (.clk(button_1_out), .D(comparator_36_eq), .Q(d_ff_36_q));  // open: Qn, preset, en, reset
  Demultiplexer #(.width(7)) demultiplexer_7 ();  // open: out0, out1, in, sel, en
  Demultiplexer #(.width(7)) demultiplexer_8 (
    .out1(demultiplexer_8_out1), .in({7{1'b0}}), .sel(d_ff_21_q));  // open: out0, en
  Demultiplexer #(.width(7)) demultiplexer_9 (
    .out1(demultiplexer_9_out1), .in(7'b0000001), .sel(d_ff_22_q));  // open: out0, en
  Demultiplexer #(.width(7)) demultiplexer_10 (
    .out1(demultiplexer_10_out1), .in(7'b0000010), .sel(d_ff_23_q));  // open: out0, en
  Demultiplexer #(.width(7)) demultiplexer_11 (
    .out1(demultiplexer_11_out1), .in(7'b0000011), .sel(d_ff_24_q));  // open: out0, en
  Demultiplexer #(.width(7)) demultiplexer_12 (
    .out1(demultiplexer_12_out1), .in(7'b0000100), .sel(d_ff_25_q));  // open: out0, en
  Demultiplexer #(.width(7)) demultiplexer_13 (
    .out1(demultiplexer_13_out1), .in(7'b0000101), .sel(d_ff_26_q));  // open: out0, en
  Demultiplexer #(.width(7)) demultiplexer_14 (
    .out1(demultiplexer_14_out1), .in(7'b0000110), .sel(d_ff_27_q));  // open: out0, en
  Demultiplexer #(.width(7)) demultiplexer_15 (
    .out1(demultiplexer_15_out1), .in(7'b0000111), .sel(d_ff_28_q));  // open: out0, en
  Demultiplexer #(.width(7)) demultiplexer_16 (
    .out1(demultiplexer_16_out1), .in(7'b0001000), .sel(d_ff_29_q));  // open: out0, en
  Demultiplexer #(.width(7)) demultiplexer_17 (
    .out1(demultiplexer_17_out1), .in(7'b0001001), .sel(d_ff_30_q));  // open: out0, en
  Demultiplexer #(.width(7)) demultiplexer_18 (
    .out1(demultiplexer_18_out1), .in(7'b0001010), .sel(d_ff_31_q));  // open: out0, en
  Demultiplexer #(.width(7)) demultiplexer_19 (
    .out1(demultiplexer_19_out1), .in(7'b0001011), .sel(d_ff_32_q));  // open: out0, en
  Demultiplexer #(.width(7)) demultiplexer_20 (
    .out1(demultiplexer_20_out1), .in(7'b0001100), .sel(d_ff_33_q));  // open: out0, en
  Demultiplexer #(.width(7)) demultiplexer_21 (
    .out1(demultiplexer_21_out1), .in(7'b0001101), .sel(d_ff_34_q));  // open: out0, en
  Demultiplexer #(.width(7)) demultiplexer_22 (
    .out1(demultiplexer_22_out1), .in(7'b0001110), .sel(d_ff_35_q));  // open: out0, en
  Demultiplexer #(.width(7)) demultiplexer_23 (
    .out1(demultiplexer_23_out1), .in(7'b0001111), .sel(d_ff_36_q));  // open: out0, en
  Multiplexer #(.width(4)) multiplexer_1 (.out(multiplexer_1_out));  // open: in0, in1, sel, en
  Multiplexer #(.select(4), .width(7)) multiplexer_2 (
    .in0(demultiplexer_8_out1), .in1(demultiplexer_9_out1), .in2(demultiplexer_10_out1),
    .in3(demultiplexer_11_out1), .in4(demultiplexer_12_out1), .in5(demultiplexer_13_out1),
    .in6(demultiplexer_14_out1), .in7(demultiplexer_15_out1), .in8(demultiplexer_16_out1),
    .in9(demultiplexer_17_out1), .in10(demultiplexer_18_out1), .in11(demultiplexer_19_out1),
    .in12(demultiplexer_20_out1), .in13(demultiplexer_21_out1), .in14(demultiplexer_22_out1),
    .in15(demultiplexer_23_out1), .out(multiplexer_2_out), .sel(multiplexer_1_out));  // open: en
  Register #(.width(7)) register_5 (.D(multiplexer_2_out), .Q(register_5_q));  // open: en, clk, clr
  Register #(.width(7)) register_6 (.D(register_5_q), .Q(register_6_q));  // open: en, clk, clr
  Register #(.width(7)) register_7 (.D(register_6_q));  // open: en, Q, clk, clr
  // Probe on nothing

  // Other names for the same wires on the sheet: ADRESS[9:0] = out_2; INSTR[5:0] = out_1

  // Notes on the sheet:
  //   CLEAR
  //   По аски
  //   INP
  //   INVA
  //   ADR
endmodule

module INP (
  input  q1,
  output w0,
  output w1,
  output w2,
  output w3,
  output w4,
  output w5,
  output out_8
);


  assign w0 = 1'b0;
  assign w1 = 1'b0;
  assign w2 = 1'b0;
  assign w3 = 1'b0;
  assign w4 = 1'b0;
  assign w5 = 1'b0;
endmodule

module XexDec (
  input  y0,
  input  y1,
  input  y2,
  input  y3,
  input  y4,
  input  y5,
  input  y6,
  output x0,
  output x1,
  output x2,
  output x3,
  output x4
);

  wire and_1_out, and_2_out, and_3_out, and_4_out, and_5_out, and_6_out, and_7_out, and_8_out, and_9_out,
       and_10_out, and_11_out, and_12_out, and_13_out, and_14_out, and_15_out, and_16_out, and_17_out,
       and_18_out, and_19_out, and_20_out, and_21_out, and_22_out, and_23_out, and_24_out, and_25_out,
       and_26_out, and_27_out, and_28_out, and_29_out, and_30_out, and_31_out, and_32_out, and_33_out,
       and_34_out, and_35_out, and_36_out, and_37_out, and_38_out, and_39_out, and_40_out, and_41_out,
       not_1_out, not_2_out, not_3_out, not_4_out, not_5_out, not_6_out, not_7_out, not_8_out, not_9_out,
       not_10_out, not_11_out, not_12_out, not_13_out, not_14_out, not_15_out, not_16_out, not_17_out,
       not_18_out, not_19_out, not_20_out, not_21_out, not_22_out, not_23_out, not_24_out, not_25_out,
       not_26_out, not_27_out, not_28_out, not_29_out, not_30_out, not_31_out, not_32_out, not_33_out,
       not_34_out, not_35_out, or_1_out, or_2_out, or_4_out, or_5_out, or_6_out, or_7_out, or_8_out,
       or_9_out, or_10_out, or_11_out, or_12_out, or_13_out, or_14_out, or_15_out, or_16_out, or_17_out,
       or_18_out, or_19_out, or_20_out, or_21_out, or_22_out, or_23_out, or_24_out, or_25_out, or_26_out,
       or_29_out, or_30_out;

  not not_1 (not_1_out, y1);
  not not_2 (not_2_out, y4);
  not not_3 (not_3_out, y5);
  not not_4 (not_4_out, y6);
  not not_5 (not_5_out, y1);
  not not_6 (not_6_out, y1);
  not not_7 (not_7_out, y2);
  not not_8 (not_8_out, y1);
  not not_9 (not_9_out, y5);
  not not_10 (not_10_out, y1);
  not not_11 (not_11_out, y1);
  not not_12 (not_12_out, y4);
  not not_13 (not_13_out, y1);
  not not_14 (not_14_out, y0);
  not not_15 (not_15_out, y1);
  and and_1 (and_1_out, not_1_out, not_2_out);
  and and_2 (and_2_out, not_3_out, not_4_out);
  and and_3 (and_3_out, not_5_out, y4);
  and and_4 (and_4_out, y5, y6);
  not not_16 (not_16_out, y1);
  not not_17 (not_17_out, y2);
  or or_1 (or_1_out, not_6_out, not_7_out);
  or or_2 (or_2_out, y3, y0);
  not not_18 (not_18_out, y0);
  not not_19 (not_19_out, y1);
  and and_5 (and_5_out, not_8_out, not_9_out);
  not not_20 (not_20_out, y6);
  and and_6 (and_6_out, not_10_out, y5);
  not not_21 (not_21_out, y1);
  not not_22 (not_22_out, y2);
  not not_23 (not_23_out, y0);
  not not_24 (not_24_out, y1);
  and and_7 (and_7_out, not_11_out, not_12_out);
  not not_25 (not_25_out, y5);
  not not_26 (not_26_out, y1);
  not not_27 (not_27_out, y1);
  not not_28 (not_28_out, y6);
  not not_29 (not_29_out, y0);
  and and_8 (and_8_out, not_13_out, y4);
  not not_30 (not_30_out, y1);
  not not_31 (not_31_out, y2);
  and and_9 (and_9_out, not_14_out, not_15_out);
  and and_10 (and_10_out, and_1_out, and_2_out);
  and and_11 (and_11_out, and_3_out, and_4_out);
  and and_12 (and_12_out, not_16_out, y3);
  and and_13 (and_13_out, y3, y5);
  and and_14 (and_14_out, y3, y4);
  and and_15 (and_15_out, y1, not_17_out);
  and and_16 (and_16_out, y0, y2);
  or or_3 (x1, or_1_out, or_2_out);
  and and_17 (and_17_out, not_18_out, not_19_out);
  and and_18 (and_18_out, and_5_out, not_20_out);
  and and_19 (and_19_out, and_6_out, y6);
  and and_20 (and_20_out, not_21_out, y3);
  and and_21 (and_21_out, y3, y5);
  and and_22 (and_22_out, y1, not_22_out);
  and and_23 (and_23_out, y0, y2);
  and and_24 (and_24_out, not_23_out, not_24_out);
  and and_25 (and_25_out, and_7_out, not_25_out);
  not not_32 (not_32_out, y0);
  not not_33 (not_33_out, y6);
  and and_26 (and_26_out, not_26_out, y4);
  not not_34 (not_34_out, y1);
  not not_35 (not_35_out, y2);
  and and_27 (and_27_out, not_27_out, not_28_out);
  and and_28 (and_28_out, not_29_out, y6);
  and and_29 (and_29_out, and_8_out, y5);
  and and_30 (and_30_out, not_30_out, y3);
  and and_31 (and_31_out, y3, y5);
  and and_32 (and_32_out, y3, y4);
  and and_33 (and_33_out, y1, not_31_out);
  and and_34 (and_34_out, y0, y2);
  or or_4 (or_4_out, and_9_out, and_10_out);
  or or_5 (or_5_out, and_11_out, and_12_out);
  or or_6 (or_6_out, and_13_out, and_14_out);
  or or_7 (or_7_out, and_15_out, and_16_out);
  or or_8 (or_8_out, and_17_out, and_18_out);
  or or_9 (or_9_out, and_19_out, y4);
  or or_10 (or_10_out, and_20_out, and_21_out);
  or or_11 (or_11_out, and_22_out, and_23_out);
  or or_12 (or_12_out, and_24_out, and_25_out);
  and and_35 (and_35_out, not_32_out, y5);
  and and_36 (and_36_out, y5, not_33_out);
  and and_37 (and_37_out, and_26_out, y6);
  and and_38 (and_38_out, not_34_out, y3);
  and and_39 (and_39_out, y3, y4);
  and and_40 (and_40_out, y1, not_35_out);
  and and_41 (and_41_out, y0, y2);
  or or_13 (or_13_out, and_27_out, and_28_out);
  or or_14 (or_14_out, and_29_out, and_30_out);
  or or_15 (or_15_out, and_31_out, and_32_out);
  or or_16 (or_16_out, and_33_out, and_34_out);
  or or_17 (or_17_out, or_4_out, or_5_out);
  or or_18 (or_18_out, or_6_out, or_7_out);
  or or_19 (or_19_out, or_8_out, or_9_out);
  or or_20 (or_20_out, or_10_out, or_11_out);
  or or_21 (or_21_out, or_12_out, and_35_out);
  or or_22 (or_22_out, and_36_out, and_37_out);
  or or_23 (or_23_out, and_38_out, and_39_out);
  or or_24 (or_24_out, and_40_out, and_41_out);
  or or_25 (or_25_out, or_13_out, or_14_out);
  or or_26 (or_26_out, or_15_out, or_16_out);
  or or_27 (x0, or_17_out, or_18_out);
  or or_28 (x2, or_19_out, or_20_out);
  or or_29 (or_29_out, or_21_out, or_22_out);
  or or_30 (or_30_out, or_23_out, or_24_out);
  or or_31 (x4, or_25_out, or_26_out);
  or or_32 (x3, or_29_out, or_30_out);
endmodule

module ADR (
  input  in_1,
  input  [6:0] in_2,
  input  in_3,
  output [9:0] out_4
);

  wire and_4_out, and_5_out, count_1_x1, not_1_out, not_2_out, not_3_out, not_4_out, not_5_out, not_6_out,
       not_7_out, xexdec_1_x0;
  wire [2:0] undriven;
  wire [3:0] register_1_q, register_2_q, register_3_q, xexdec_1_x4;
  wire [11:0] register_4_q;

  Counter #(.width(6), .max('h3f), .ongoal("stay")) counter_1 (
    .clk(in_3), .clr(not_6_out));  // open: load, D, count, Q, carry
  XexDec xexdec_1 (
    .y0(in_2[6]), .y1(in_2[5]), .y2(in_2[4]), .y3(in_2[3]), .y4(in_2[2]), .y5(in_2[1]), .y6(in_2[0]),
    .x0(xexdec_1_x0), .x1(xexdec_1_x4[3]), .x2(xexdec_1_x4[2]), .x3(xexdec_1_x4[1]), .x4(xexdec_1_x4[0]));
  // Probe on xexdec_1_x4
  // Probe on xexdec_1_x0
  not not_1 (not_1_out, in_1);
  not not_2 (not_2_out, xexdec_1_x0);
  // AND_Gate and_1 has open pins: in0=in_1, in1=not_2_out, in2=in_3, out=open
  not not_3 (not_3_out, xexdec_1_x0);
  // AND_Gate and_2 has open pins: in0=not_3_out, in1=in_3, out=open
  not not_4 (not_4_out, xexdec_1_x0);
  // AND_Gate and_3 has open pins: in0=not_4_out, in1=in_3, out=open
  Count count_1 (.\у0 (undriven[2]), .\у1 (undriven[1]), .y2(undriven[0]), .x1(count_1_x1));
  not not_5 (not_5_out, count_1_x1);
  not not_6 (not_6_out, in_1);
  Register #(.width(4)) register_1 (.D(xexdec_1_x4), .Q(register_1_q), .clk(and_5_out), .clr(not_6_out));  // open: en
  Register #(.width(4)) register_2 (.D(register_1_q), .Q(register_2_q), .clk(and_5_out), .clr(not_6_out));  // open: en
  Register #(.width(4)) register_3 (.D(register_2_q), .Q(register_3_q), .clk(and_5_out), .clr(not_6_out));  // open: en
  and and_4 (and_4_out, not_5_out, in_3);
  not not_7 (not_7_out, xexdec_1_x0);
  and and_5 (and_5_out, not_7_out, in_3);
  // Probe on {register_3_q, register_2_q, register_1_q}
  Register #(.width(12)) register_4 (
    .D({register_3_q, register_2_q, register_1_q}), .Q(register_4_q), .clk(in_3), .clr(not_1_out));  // open: en
  // Probe on out_4
  Bit_Extender #(.in_width(12), .out_width(10)) bit_extender_1 (.in(register_4_q), .out(out_4));
endmodule

module \Ф  (
  input  in_1,
  output out_2
);

  wire not_1_out, not_2_out, not_3_out, not_4_out, not_5_out, not_6_out, not_7_out;

  not not_1 (not_1_out, in_1);
  not not_2 (not_2_out, not_3_out);
  not not_3 (not_3_out, not_1_out);
  not not_4 (not_4_out, not_5_out);
  not not_5 (not_5_out, not_2_out);
  not not_6 (not_6_out, not_4_out);
  not not_7 (not_7_out, not_6_out);
  not not_8 (out_2, not_7_out);
endmodule

module Cout (
  input  \у0 ,
  input  \у1 ,
  output x1
);

  and and_1 (x1, \у0 , \у1 );
endmodule

module Count (
  input  \у0 ,
  input  \у1 ,
  input  y2,
  output x1
);


  assign x1 = \у0 ;
endmodule

module INSTR (
  input  in_1,
  input  [6:0] Simbol,
  input  Takt,
  input  in_4,
  output out_5,
  output [5:0] out_6,
  output [6:0] out_7
);

  wire and_1_out, and_2_out, and_3_out, and_4_out, and_5_out, and_6_out, and_7_out, and_8_out, and_9_out,
       and_10_out, and_11_out, and_12_out, and_13_out, and_14_out, and_15_out, and_16_out, and_17_out,
       and_18_out, and_19_out, and_20_out, and_21_out, and_22_out, and_23_out, and_24_out, and_25_out,
       and_26_out, and_27_out, and_28_out, and_29_out, and_30_out, and_31_out, and_32_out, and_33_out,
       and_34_out, and_35_out, button_1_out, button_2_out, Clear, Clear1, Clear2, Clear3, Clear4, Clear5,
       Clear14, Clear15, Clear16, Clear17, Clear18, Clear19, Clear20, Clear21, Clear22, clock_1_out,
       comparator_1_eq, comparator_2_eq, comparator_3_eq, comparator_4_eq, comparator_5_eq, comparator_6_eq,
       comparator_7_eq, comparator_8_eq, comparator_9_eq, comparator_10_eq, comparator_11_eq,
       comparator_12_eq, comparator_13_eq, comparator_14_eq, comparator_16_eq, comparator_17_eq,
       comparator_18_eq, comparator_19_eq, comparator_20_eq, comparator_21_eq, comparator_22_eq,
       comparator_23_eq, comparator_24_eq, comparator_25_eq, comparator_26_eq, comparator_27_eq,
       comparator_28_eq, comparator_29_eq, comparator_30_eq, comparator_31_eq, comparator_32_eq,
       comparator_33_eq, comparator_34_eq, comparator_35_eq, comparator_36_eq, comparator_37_eq,
       comparator_38_eq, comparator_39_eq, comparator_40_eq, comparator_41_eq, comparator_42_eq,
       comparator_43_eq, comparator_44_eq, comparator_45_eq, comparator_46_eq, comparator_47_eq,
       comparator_48_eq, comparator_49_eq, comparator_50_eq, comparator_51_eq, comparator_52_eq,
       comparator_53_eq, comparator_54_eq, comparator_55_eq, comparator_56_eq, comparator_57_eq,
       comparator_58_eq, comparator_59_eq, comparator_60_eq, comparator_61_eq, comparator_62_eq,
       comparator_63_eq, d_ff_2_q, d_ff_3_q, d_ff_4_q, d_ff_5_q, d_ff_7_q, d_ff_8_q, d_ff_10_q, d_ff_11_q,
       d_ff_12_q, d_ff_13_q, d_ff_14_q, d_ff_15_q, d_ff_16_q, d_ff_18_q, d_ff_19_q, d_ff_20_q, d_ff_22_q,
       d_ff_23_q, d_ff_24_q, d_ff_26_q, d_ff_27_q, d_ff_29_q, d_ff_30_q, d_ff_31_q, d_ff_33_q, d_ff_35_q,
       d_ff_36_q, d_ff_37_q, d_ff_38_q, d_ff_39_q, d_ff_40_q, d_ff_42_q, d_ff_43_q, d_ff_45_q, d_ff_46_q,
       d_ff_48_q, iskl_1_x, not_1_out, not_3_out, or_1_out, or_3_out, read_1_out_3, register_13_q, SpINP,
       SpLDO, SpMOV, SpMV, SpOUT, SpSTO, undriven, undriven_2, undriven_3, \ф_1_out_2 , \ф_2_out_2 ,
       \ф_3_out_2 , \ф_4_out_2 , \ф_5_out_2 , \ф_6_out_2 , \ф_7_out_2 , \ф_8_out_2 , \ф_9_out_2 ,
       \ф_10_out_2 , \ф_11_out_2 , \ф_12_out_2 , \ф_13_out_2 , \ф_14_out_2 , \ф_15_out_2 , \ф_16_out_2 ,
       \ф_17_out_2 ;
  wire [5:0] ADD, AND, demultiplexer_2_out1, demultiplexer_3_out1, demultiplexer_4_out1,
       demultiplexer_5_out1, demultiplexer_6_out1, demultiplexer_7_out1, demultiplexer_8_out1,
       demultiplexer_9_out1, demultiplexer_10_out1, demultiplexer_11_out1, demultiplexer_12_out1,
       demultiplexer_13_out1, demultiplexer_14_out1, demultiplexer_15_out1, INP, INVA, LDO, MOV, MV, OR, OUT,
       register_1_q, SHL, SHR, STO, SUB, XOR;
  wire [6:0] demultiplexer_1_out1, keyboard_1_data;

  Clock clock_1 (.out(clock_1_out));
  \Ф  \u_ф_1  (.in_1(clock_1_out), .out_2(\ф_1_out_2 ));
  not not_1 (not_1_out, or_3_out);
  and and_1 (and_1_out, \ф_1_out_2 , or_1_out);
  or or_1 (or_1_out, not_1_out, iskl_1_x);
  Iskl iskl_1 (.y0(out_6[5]), .y1(out_6[4]), .y2(out_6[3]), .y3(out_6[2]), .y4(out_6[1]), .y5(out_6[0]), .x(iskl_1_x));
  Counter #(.width(6), .max('h3f)) counter_1 (.Q(out_6), .clk(and_1_out), .clr(Clear));  // open: load, D, count, carry
  // OR_Gate or_2 has open pins: in0=Clear1, in1=Clear4, in2=Clear2, in3=Clear5, in4=Clear3, in5=Clear14, in6=Clear19, in7=Clear15, in8=Clear20, in9=Clear16, in10=Clear21, in11=Clear17, in12=Clear22, in13=Clear18, out=open
  Comparator #(.width(6)) comparator_1 (.a(out_6), .b(MV), .eq(comparator_1_eq));  // open: gt, lt
  Comparator #(.width(6)) comparator_2 (.a(out_6), .b(INVA), .eq(comparator_2_eq));  // open: gt, lt
  Comparator #(.width(6)) comparator_3 (.a(out_6), .b(AND), .eq(comparator_3_eq));  // open: gt, lt
  Comparator #(.width(6)) comparator_4 (.a(out_6), .b(SUB), .eq(comparator_4_eq));  // open: gt, lt
  Comparator #(.width(6)) comparator_5 (.a(out_6), .b(ADD), .eq(comparator_5_eq));  // open: gt, lt
  Comparator #(.width(6)) comparator_6 (.a(out_6), .b(OR), .eq(comparator_6_eq));  // open: gt, lt
  Comparator #(.width(6)) comparator_7 (.a(out_6), .b(XOR), .eq(comparator_7_eq));  // open: gt, lt
  Comparator #(.width(6)) comparator_8 (.a(out_6), .b(SHL), .eq(comparator_8_eq));  // open: gt, lt
  Comparator #(.width(6)) comparator_9 (.a(out_6), .b(SHR), .eq(comparator_9_eq));  // open: gt, lt
  Comparator #(.width(6)) comparator_10 (.a(out_6), .b(INP), .eq(comparator_10_eq));  // open: gt, lt
  Comparator #(.width(6)) comparator_11 (.a(out_6), .b(OUT), .eq(comparator_11_eq));  // open: gt, lt
  Comparator #(.width(6)) comparator_12 (.a(out_6), .b(MOV), .eq(comparator_12_eq));  // open: gt, lt
  Comparator #(.width(6)) comparator_13 (.a(out_6), .b(LDO), .eq(comparator_13_eq));  // open: gt, lt
  Comparator #(.width(6)) comparator_14 (.a(out_6), .b(STO), .eq(comparator_14_eq));  // open: gt, lt
  Register #(.width(6), .trigger("falling")) register_1 (
    .D(out_6), .Q(register_1_q), .clk(or_1_out), .clr(Clear));  // open: en
  // NOT_Gate not_2 has open pins: in=out_5, out=open
  Comparator #(.width(6)) comparator_15 (.a(out_6), .b(register_1_q), .eq(out_5));  // open: gt, lt
  or or_3 (or_3_out, comparator_1_eq, comparator_2_eq, comparator_3_eq, comparator_4_eq, comparator_5_eq, comparator_6_eq, comparator_7_eq, comparator_8_eq, comparator_9_eq, comparator_10_eq, comparator_11_eq, comparator_12_eq, comparator_13_eq, comparator_14_eq);
  Button button_1 (.out(button_1_out));
  Button button_2 (.out(button_2_out));
  Read read_1 (.in_2(button_1_out), .out_3(read_1_out_3), .out_4(Clear), .in_1(clock_1_out));
  Comparator #(.width(7)) comparator_16 (.a(keyboard_1_data), .b(7'b1001001), .eq(comparator_16_eq));  // open: gt, lt
  Comparator #(.width(7)) comparator_17 (.a(keyboard_1_data), .b(7'b1001110), .eq(comparator_17_eq));  // open: gt, lt
  Comparator #(.width(7)) comparator_18 (.a(keyboard_1_data), .b(7'b1010000), .eq(comparator_18_eq));  // open: gt, lt
  Comparator #(.width(7)) comparator_19 (.a(keyboard_1_data), .b(7'b0100000), .eq(comparator_19_eq));  // open: gt, lt
  Comparator #(.width(7)) comparator_20 (.a(keyboard_1_data), .b(7'b1001111), .eq(comparator_20_eq));  // open: gt, lt
  Comparator #(.width(7)) comparator_21 (.a(keyboard_1_data), .b(7'b1010101), .eq(comparator_21_eq));  // open: gt, lt
  Comparator #(.width(7)) comparator_22 (.a(keyboard_1_data), .b(7'b1010100), .eq(comparator_22_eq));  // open: gt, lt
  Comparator #(.width(7)) comparator_23 (.a(keyboard_1_data), .b(7'b0100000), .eq(comparator_23_eq));  // open: gt, lt
  Comparator #(.width(7)) comparator_24 (.a(keyboard_1_data), .b(7'b1001101), .eq(comparator_24_eq));  // open: gt, lt
  Comparator #(.width(7)) comparator_25 (.a(keyboard_1_data), .b(7'b1001111), .eq(comparator_25_eq));  // open: gt, lt
  Comparator #(.width(7)) comparator_26 (.a(keyboard_1_data), .b(7'b1010110), .eq(comparator_26_eq));  // open: gt, lt
  Comparator #(.width(7)) comparator_27 (.a(keyboard_1_data), .b(7'b0100000), .eq(comparator_27_eq));  // open: gt, lt
  Comparator #(.width(7)) comparator_28 (.a(keyboard_1_data), .b(7'b1001100), .eq(comparator_28_eq));  // open: gt, lt
  Comparator #(.width(7)) comparator_29 (.a(keyboard_1_data), .b(7'b1000100), .eq(comparator_29_eq));  // open: gt, lt
  Comparator #(.width(7)) comparator_30 (.a(keyboard_1_data), .b(7'b1001111), .eq(comparator_30_eq));  // open: gt, lt
  Comparator #(.width(7)) comparator_31 (.a(keyboard_1_data), .b(7'b0100000), .eq(comparator_31_eq));  // open: gt, lt
  Comparator #(.width(7)) comparator_32 (.a(keyboard_1_data), .b(7'b1010011), .eq(comparator_32_eq));  // open: gt, lt
  Comparator #(.width(7)) comparator_33 (.a(keyboard_1_data), .b(7'b1010100), .eq(comparator_33_eq));  // open: gt, lt
  Comparator #(.width(7)) comparator_34 (.a(keyboard_1_data), .b(7'b1001111), .eq(comparator_34_eq));  // open: gt, lt
  Comparator #(.width(7)) comparator_35 (.a(keyboard_1_data), .b(7'b0100000), .eq(comparator_35_eq));  // open: gt, lt
  and and_2 (and_2_out, Clear1, comparator_17_eq);
  and and_3 (and_3_out, d_ff_2_q, comparator_18_eq);
  and and_4 (and_4_out, d_ff_3_q, comparator_19_eq);
  and and_5 (and_5_out, d_ff_5_q, comparator_21_eq);
  and and_6 (and_6_out, Clear2, comparator_22_eq);
  and and_7 (and_7_out, d_ff_7_q, comparator_23_eq);
  and and_8 (and_8_out, Clear3, comparator_25_eq);
  and and_9 (and_9_out, d_ff_10_q, comparator_26_eq);
  and and_10 (and_10_out, d_ff_11_q, comparator_27_eq);
  and and_11 (and_11_out, d_ff_13_q, comparator_29_eq);
  and and_12 (and_12_out, d_ff_14_q, comparator_30_eq);
  and and_13 (and_13_out, d_ff_15_q, comparator_31_eq);
  and and_14 (and_14_out, Clear5, comparator_33_eq);
  and and_15 (and_15_out, d_ff_18_q, comparator_34_eq);
  and and_16 (and_16_out, d_ff_19_q, comparator_35_eq);
  Demultiplexer #(.width(7)) demultiplexer_1 (
    .out1(demultiplexer_1_out1), .in(7'b0010000), .sel(in_4));  // open: out0, en
  Keyboard keyboard_1 (.clk(read_1_out_3), .clr(button_2_out), .data(keyboard_1_data));  // open: re, avail
  D_Flip_Flop d_ff_1 (.clk(read_1_out_3), .D(comparator_16_eq), .Q(Clear1));  // open: Qn, preset, en, reset
  D_Flip_Flop d_ff_2 (.clk(read_1_out_3), .D(and_2_out), .Q(d_ff_2_q));  // open: Qn, preset, en, reset
  D_Flip_Flop d_ff_3 (.clk(read_1_out_3), .D(and_3_out), .Q(d_ff_3_q));  // open: Qn, preset, en, reset
  D_Flip_Flop d_ff_4 (.clk(read_1_out_3), .D(and_4_out), .Q(d_ff_4_q));  // open: Qn, preset, en, reset
  Register #(.width(1)) register_2 (.D(d_ff_4_q), .Q(SpINP), .clk(\ф_2_out_2 ), .clr(Clear1));  // open: en
  \Ф  \u_ф_2  (.in_1(d_ff_4_q), .out_2(\ф_2_out_2 ));
  D_Flip_Flop d_ff_5 (.clk(read_1_out_3), .D(comparator_20_eq), .Q(d_ff_5_q));  // open: Qn, preset, en, reset
  D_Flip_Flop d_ff_6 (.clk(read_1_out_3), .D(and_5_out), .Q(Clear2));  // open: Qn, preset, en, reset
  Demultiplexer #(.width(6)) demultiplexer_2 (
    .out1(demultiplexer_2_out1), .in(6'b000010), .sel(\ф_3_out_2 ));  // open: out0, en
  D_Flip_Flop d_ff_7 (.clk(read_1_out_3), .D(and_6_out), .Q(d_ff_7_q));  // open: Qn, preset, en, reset
  \Ф  \u_ф_3  (.in_1(d_ff_7_q), .out_2(\ф_3_out_2 ));
  Register #(.width(1)) register_3 (.D(d_ff_8_q), .Q(SpOUT), .clk(\ф_4_out_2 ), .clr(d_ff_5_q));  // open: en
  D_Flip_Flop d_ff_8 (.clk(read_1_out_3), .D(and_7_out), .Q(d_ff_8_q));  // open: Qn, preset, en, reset
  \Ф  \u_ф_4  (.in_1(d_ff_8_q), .out_2(\ф_4_out_2 ));
  D_Flip_Flop d_ff_9 (.clk(read_1_out_3), .D(comparator_24_eq), .Q(Clear3));  // open: Qn, preset, en, reset
  D_Flip_Flop d_ff_10 (.clk(read_1_out_3), .D(and_8_out), .Q(d_ff_10_q));  // open: Qn, preset, en, reset
  Demultiplexer #(.width(6)) demultiplexer_3 (
    .out1(demultiplexer_3_out1), .in(6'b000011), .sel(\ф_5_out_2 ));  // open: out0, en
  D_Flip_Flop d_ff_11 (.clk(read_1_out_3), .D(and_9_out), .Q(d_ff_11_q));  // open: Qn, preset, en, reset
  \Ф  \u_ф_5  (.in_1(d_ff_11_q), .out_2(\ф_5_out_2 ));
  D_Flip_Flop d_ff_12 (.clk(read_1_out_3), .D(and_10_out), .Q(d_ff_12_q));  // open: Qn, preset, en, reset
  Register #(.width(1)) register_4 (.D(d_ff_12_q), .Q(SpMOV), .clk(\ф_6_out_2 ), .clr(Clear3));  // open: en
  \Ф  \u_ф_6  (.in_1(d_ff_12_q), .out_2(\ф_6_out_2 ));
  D_Flip_Flop d_ff_13 (.clk(read_1_out_3), .D(comparator_28_eq), .Q(d_ff_13_q));  // open: Qn, preset, en, reset
  D_Flip_Flop d_ff_14 (.clk(read_1_out_3), .D(and_11_out), .Q(d_ff_14_q));  // open: Qn, preset, en, reset
  Demultiplexer #(.width(6)) demultiplexer_4 (
    .out1(demultiplexer_4_out1), .in(6'b000100), .sel(\ф_7_out_2 ));  // open: out0, en
  D_Flip_Flop d_ff_15 (.clk(read_1_out_3), .D(and_12_out), .Q(d_ff_15_q));  // open: Qn, preset, en, reset
  \Ф  \u_ф_7  (.in_1(d_ff_15_q), .out_2(\ф_7_out_2 ));
  Register #(.width(1)) register_5 (.D(d_ff_16_q), .Q(SpLDO), .clk(\ф_8_out_2 ), .clr(d_ff_14_q));  // open: en
  D_Flip_Flop d_ff_16 (.clk(read_1_out_3), .D(and_13_out), .Q(d_ff_16_q));  // open: Qn, preset, en, reset
  \Ф  \u_ф_8  (.in_1(d_ff_16_q), .out_2(\ф_8_out_2 ));
  D_Flip_Flop d_ff_17 (.clk(read_1_out_3), .D(comparator_32_eq), .Q(Clear5));  // open: Qn, preset, en, reset
  D_Flip_Flop d_ff_18 (.clk(read_1_out_3), .D(and_14_out), .Q(d_ff_18_q));  // open: Qn, preset, en, reset
  Demultiplexer #(.width(6)) demultiplexer_5 (
    .out1(demultiplexer_5_out1), .in(6'b000101), .sel(\ф_9_out_2 ));  // open: out0, en
  \Ф  \u_ф_9  (.in_1(d_ff_19_q), .out_2(\ф_9_out_2 ));
  D_Flip_Flop d_ff_19 (.clk(read_1_out_3), .D(and_15_out), .Q(d_ff_19_q));  // open: Qn, preset, en, reset
  Register #(.width(1)) register_6 (.D(d_ff_20_q), .Q(SpSTO), .clk(\ф_10_out_2 ), .clr(Clear5));  // open: en
  D_Flip_Flop d_ff_20 (.clk(read_1_out_3), .D(and_16_out), .Q(d_ff_20_q));  // open: Qn, preset, en, reset
  \Ф  \u_ф_10  (.in_1(d_ff_20_q), .out_2(\ф_10_out_2 ));
  Register #(.width(7), .trigger("falling")) register_7 (
    .D(demultiplexer_1_out1), .Q(out_7), .clk(in_4), .clr(undriven));  // open: en
  Demultiplexer #(.width(6)) demultiplexer_6 (
    .out1(demultiplexer_6_out1), .in(6'b000001), .sel(d_ff_3_q));  // open: out0, en
  Register #(.width(6), .trigger("falling")) register_8 (
    .D(demultiplexer_2_out1), .Q(OUT), .clk(d_ff_7_q), .clr(Clear));  // open: en
  Register #(.width(6), .trigger("falling")) register_9 (
    .D(demultiplexer_3_out1), .Q(MOV), .clk(d_ff_11_q), .clr(Clear));  // open: en
  Register #(.width(6), .trigger("falling")) register_10 (
    .D(demultiplexer_4_out1), .Q(LDO), .clk(d_ff_15_q), .clr(Clear));  // open: en
  Register #(.width(6), .trigger("falling")) register_11 (
    .D(demultiplexer_5_out1), .Q(STO), .clk(d_ff_19_q), .clr(Clear));  // open: en
  // Probe on keyboard_1_data
  Register #(.width(6), .trigger("falling")) register_12 (
    .D(demultiplexer_6_out1), .Q(INP), .clk(d_ff_3_q), .clr(Clear));  // open: en
  // Probe on out_6
  TTY tty_1 (.data(keyboard_1_data), .clk(read_1_out_3), .clr(button_2_out));  // open: we
  Comparator #(.width(7)) comparator_36 (.a(keyboard_1_data), .b(7'b1001101), .eq(comparator_36_eq));  // open: gt, lt
  Comparator #(.width(7)) comparator_37 (.a(keyboard_1_data), .b(7'b1010110), .eq(comparator_37_eq));  // open: gt, lt
  Comparator #(.width(7)) comparator_38 (.a(keyboard_1_data), .b(7'b0100000), .eq(comparator_38_eq));  // open: gt, lt
  Comparator #(.width(7)) comparator_39 (.a(keyboard_1_data), .b(7'b1001001), .eq(comparator_39_eq));  // open: gt, lt
  Comparator #(.width(7)) comparator_40 (.a(keyboard_1_data), .b(7'b1001110), .eq(comparator_40_eq));  // open: gt, lt
  Comparator #(.width(7)) comparator_41 (.a(keyboard_1_data), .b(7'b1010110), .eq(comparator_41_eq));  // open: gt, lt
  Comparator #(.width(7)) comparator_42 (.a(keyboard_1_data), .b(7'b1000001), .eq(comparator_42_eq));  // open: gt, lt
  Comparator #(.width(7)) comparator_43 (.a(keyboard_1_data), .b(7'b1000001), .eq(comparator_43_eq));  // open: gt, lt
  Comparator #(.width(7)) comparator_44 (.a(keyboard_1_data), .b(7'b1001110), .eq(comparator_44_eq));  // open: gt, lt
  Comparator #(.width(7)) comparator_45 (.a(keyboard_1_data), .b(7'b1000100), .eq(comparator_45_eq));  // open: gt, lt
  Comparator #(.width(7)) comparator_46 (.a(keyboard_1_data), .b(7'b1010011), .eq(comparator_46_eq));  // open: gt, lt
  Comparator #(.width(7)) comparator_47 (.a(keyboard_1_data), .b(7'b1010101), .eq(comparator_47_eq));  // open: gt, lt
  Comparator #(.width(7)) comparator_48 (.a(keyboard_1_data), .b(7'b1000010), .eq(comparator_48_eq));  // open: gt, lt
  Comparator #(.width(7)) comparator_49 (.a(keyboard_1_data), .b(7'b1000001), .eq(comparator_49_eq));  // open: gt, lt
  Comparator #(.width(7)) comparator_50 (.a(keyboard_1_data), .b(7'b1000100), .eq(comparator_50_eq));  // open: gt, lt
  Comparator #(.width(7)) comparator_51 (.a(keyboard_1_data), .b(7'b1000100), .eq(comparator_51_eq));  // open: gt, lt
  Comparator #(.width(7)) comparator_52 (.a(keyboard_1_data), .b(7'b1011000), .eq(comparator_52_eq));  // open: gt, lt
  Comparator #(.width(7)) comparator_53 (.a(keyboard_1_data), .b(7'b1001111), .eq(comparator_53_eq));  // open: gt, lt
  Comparator #(.width(7)) comparator_54 (.a(keyboard_1_data), .b(7'b1010010), .eq(comparator_54_eq));  // open: gt, lt
  Comparator #(.width(7)) comparator_55 (.a(keyboard_1_data), .b(7'b1011000), .eq(comparator_55_eq));  // open: gt, lt
  Comparator #(.width(7)) comparator_56 (.a(keyboard_1_data), .b(7'b1001111), .eq(comparator_56_eq));  // open: gt, lt
  Comparator #(.width(7)) comparator_57 (.a(keyboard_1_data), .b(7'b1010010), .eq(comparator_57_eq));  // open: gt, lt
  Comparator #(.width(7)) comparator_58 (.a(keyboard_1_data), .b(7'b1010011), .eq(comparator_58_eq));  // open: gt, lt
  Comparator #(.width(7)) comparator_59 (.a(keyboard_1_data), .b(7'b1001000), .eq(comparator_59_eq));  // open: gt, lt
  Comparator #(.width(7)) comparator_60 (.a(keyboard_1_data), .b(7'b1001100), .eq(comparator_60_eq));  // open: gt, lt
  Comparator #(.width(7)) comparator_61 (.a(keyboard_1_data), .b(7'b1010011), .eq(comparator_61_eq));  // open: gt, lt
  Comparator #(.width(7)) comparator_62 (.a(keyboard_1_data), .b(7'b1001000), .eq(comparator_62_eq));  // open: gt, lt
  Comparator #(.width(7)) comparator_63 (.a(keyboard_1_data), .b(7'b1010010), .eq(comparator_63_eq));  // open: gt, lt
  and and_17 (and_17_out, Clear14, comparator_37_eq);
  and and_18 (and_18_out, d_ff_22_q, comparator_38_eq);
  and and_19 (and_19_out, d_ff_24_q, comparator_40_eq);
  and and_20 (and_20_out, Clear15, comparator_41_eq);
  and and_21 (and_21_out, d_ff_26_q, comparator_42_eq);
  and and_22 (and_22_out, Clear16, comparator_44_eq);
  and and_23 (and_23_out, d_ff_29_q, comparator_45_eq);
  and and_24 (and_24_out, d_ff_31_q, comparator_47_eq);
  and and_25 (and_25_out, Clear17, comparator_48_eq);
  and and_26 (and_26_out, Clear18, comparator_50_eq);
  and and_27 (and_27_out, d_ff_35_q, comparator_51_eq);
  not not_3 (not_3_out, comparator_52_eq);
  and and_28 (and_28_out, d_ff_37_q, comparator_53_eq);
  and and_29 (and_29_out, d_ff_38_q, comparator_54_eq);
  and and_30 (and_30_out, d_ff_40_q, comparator_56_eq);
  and and_31 (and_31_out, Clear20, comparator_57_eq);
  and and_32 (and_32_out, d_ff_43_q, comparator_59_eq);
  and and_33 (and_33_out, Clear21, comparator_60_eq);
  and and_34 (and_34_out, d_ff_46_q, comparator_62_eq);
  and and_35 (and_35_out, Clear22, comparator_63_eq);
  ADR adr_1 ();  // open: in_2, in_3, out_4, in_1
  D_Flip_Flop d_ff_21 (.clk(read_1_out_3), .D(comparator_36_eq), .Q(Clear14));  // open: Qn, preset, en, reset
  D_Flip_Flop d_ff_22 (.clk(read_1_out_3), .D(and_17_out), .Q(d_ff_22_q));  // open: Qn, preset, en, reset
  D_Flip_Flop d_ff_23 (.clk(read_1_out_3), .D(and_18_out), .Q(d_ff_23_q));  // open: Qn, preset, en, reset
  \Ф  \u_ф_11  (.in_1(d_ff_23_q), .out_2(\ф_11_out_2 ));
  D_Flip_Flop d_ff_24 (.clk(read_1_out_3), .D(comparator_39_eq), .Q(d_ff_24_q));  // open: Qn, preset, en, reset
  D_Flip_Flop d_ff_25 (.clk(read_1_out_3), .D(and_19_out), .Q(Clear15));  // open: Qn, preset, en, reset
  D_Flip_Flop d_ff_26 (.clk(read_1_out_3), .D(and_20_out), .Q(d_ff_26_q));  // open: Qn, preset, en, reset
  D_Flip_Flop d_ff_27 (.clk(read_1_out_3), .D(and_21_out), .Q(d_ff_27_q));  // open: Qn, preset, en, reset
  D_Flip_Flop d_ff_28 (.clk(read_1_out_3), .D(comparator_43_eq), .Q(Clear16));  // open: Qn, preset, en, reset
  D_Flip_Flop d_ff_29 (.clk(read_1_out_3), .D(and_22_out), .Q(d_ff_29_q));  // open: Qn, preset, en, reset
  \Ф  \u_ф_12  (.in_1(d_ff_30_q), .out_2(\ф_12_out_2 ));
  D_Flip_Flop d_ff_30 (.clk(read_1_out_3), .D(and_23_out), .Q(d_ff_30_q));  // open: Qn, preset, en, reset
  D_Flip_Flop d_ff_31 (.clk(read_1_out_3), .D(comparator_46_eq), .Q(d_ff_31_q));  // open: Qn, preset, en, reset
  D_Flip_Flop d_ff_32 (.clk(read_1_out_3), .D(and_24_out), .Q(Clear17));  // open: Qn, preset, en, reset
  D_Flip_Flop d_ff_33 (.clk(read_1_out_3), .D(and_25_out), .Q(d_ff_33_q));  // open: Qn, preset, en, reset
  D_Flip_Flop d_ff_34 (.clk(read_1_out_3), .D(comparator_49_eq), .Q(Clear18));  // open: Qn, preset, en, reset
  D_Flip_Flop d_ff_35 (.clk(read_1_out_3), .D(and_26_out), .Q(d_ff_35_q));  // open: Qn, preset, en, reset
  D_Flip_Flop d_ff_36 (.clk(read_1_out_3), .D(and_27_out), .Q(d_ff_36_q));  // open: Qn, preset, en, reset
  D_Flip_Flop d_ff_37 (.clk(read_1_out_3), .D(not_3_out), .Q(d_ff_37_q));  // open: Qn, preset, en, reset
  D_Flip_Flop d_ff_38 (.clk(read_1_out_3), .D(and_28_out), .Q(d_ff_38_q));  // open: Qn, preset, en, reset
  Demultiplexer #(.width(6)) demultiplexer_7 (
    .out1(demultiplexer_7_out1), .in(6'b010100), .sel(\ф_13_out_2 ));  // open: out0, en
  D_Flip_Flop d_ff_39 (.clk(read_1_out_3), .D(and_29_out), .Q(d_ff_39_q));  // open: Qn, preset, en, reset
  \Ф  \u_ф_13  (.in_1(d_ff_39_q), .out_2(\ф_13_out_2 ));
  D_Flip_Flop d_ff_40 (.clk(read_1_out_3), .D(comparator_55_eq), .Q(d_ff_40_q));  // open: Qn, preset, en, reset
  D_Flip_Flop d_ff_41 (.clk(read_1_out_3), .D(and_30_out), .Q(Clear20));  // open: Qn, preset, en, reset
  \Ф  \u_ф_14  (.in_1(d_ff_42_q), .out_2(\ф_14_out_2 ));
  D_Flip_Flop d_ff_42 (.clk(read_1_out_3), .D(and_31_out), .Q(d_ff_42_q));  // open: Qn, preset, en, reset
  D_Flip_Flop d_ff_43 (.clk(read_1_out_3), .D(comparator_58_eq), .Q(d_ff_43_q));  // open: Qn, preset, en, reset
  D_Flip_Flop d_ff_44 (.clk(read_1_out_3), .D(and_32_out), .Q(Clear21));  // open: Qn, preset, en, reset
  D_Flip_Flop d_ff_45 (.clk(read_1_out_3), .D(and_33_out), .Q(d_ff_45_q));  // open: Qn, preset, en, reset
  \Ф  \u_ф_15  (.in_1(d_ff_45_q), .out_2(\ф_15_out_2 ));
  D_Flip_Flop d_ff_46 (.clk(read_1_out_3), .D(comparator_61_eq), .Q(d_ff_46_q));  // open: Qn, preset, en, reset
  D_Flip_Flop d_ff_47 (.clk(read_1_out_3), .D(and_34_out), .Q(Clear22));  // open: Qn, preset, en, reset
  D_Flip_Flop d_ff_48 (.clk(read_1_out_3), .D(and_35_out), .Q(d_ff_48_q));  // open: Qn, preset, en, reset
  \Ф  \u_ф_16  (.in_1(d_ff_48_q), .out_2(\ф_16_out_2 ));
  Demultiplexer #(.width(6)) demultiplexer_8 (
    .out1(demultiplexer_8_out1), .in(6'b010000), .sel(register_13_q));  // open: out0, en
  Register #(.width(1)) register_13 (.D(d_ff_22_q), .Q(register_13_q), .clk(d_ff_22_q), .clr(Clear));  // open: en
  Register #(.width(1)) register_14 (.D(d_ff_23_q), .Q(SpMV), .clk(\ф_11_out_2 ));  // open: en, clr
  // Register #(.width(1)) register_15: pin names not known; wires that end beside it: d_ff_27_q, d_ff_27_q
  Demultiplexer #(.width(6)) demultiplexer_9 (
    .out1(demultiplexer_9_out1), .in(6'b011000), .sel(undriven_2));  // open: out0, en
  Demultiplexer #(.width(6)) demultiplexer_10 (
    .out1(demultiplexer_10_out1), .in(6'b010001), .sel(\ф_12_out_2 ));  // open: out0, en
  Demultiplexer #(.width(6)) demultiplexer_11 (
    .out1(demultiplexer_11_out1), .in(6'b010010), .sel(d_ff_33_q));  // open: out0, en
  Demultiplexer #(.width(6)) demultiplexer_12 (
    .out1(demultiplexer_12_out1), .in(6'b010011), .sel(\ф_17_out_2 ));  // open: out0, en
  \Ф  \u_ф_17  (.in_1(d_ff_36_q), .out_2(\ф_17_out_2 ));
  Demultiplexer #(.width(6)) demultiplexer_13 (
    .out1(demultiplexer_13_out1), .in(6'b010101), .sel(\ф_14_out_2 ));  // open: out0, en
  Demultiplexer #(.width(6)) demultiplexer_14 (
    .out1(demultiplexer_14_out1), .in(6'b010110), .sel(\ф_15_out_2 ));  // open: out0, en
  Demultiplexer #(.width(6)) demultiplexer_15 (
    .out1(demultiplexer_15_out1), .in(6'b010111), .sel(\ф_16_out_2 ));  // open: out0, en
  Register #(.width(6), .trigger("falling")) register_16 (
    .D(demultiplexer_8_out1), .Q(MV), .clk(d_ff_22_q), .clr(Clear));  // open: en
  Register #(.width(6), .trigger("falling")) register_17 (
    .D(demultiplexer_9_out1), .Q(INVA), .clk(undriven_3), .clr(Clear));  // open: en
  Register #(.width(6), .trigger("falling")) register_18 (
    .D(demultiplexer_10_out1), .Q(AND), .clk(d_ff_30_q), .clr(Clear));  // open: en
  Register #(.width(6), .trigger("falling")) register_19 (
    .D(demultiplexer_11_out1), .Q(SUB), .clk(d_ff_33_q), .clr(Clear));  // open: en
  Register #(.width(6), .trigger("falling")) register_20 (
    .D(demultiplexer_12_out1), .Q(ADD), .clk(d_ff_36_q), .clr(Clear));  // open: en
  Register #(.width(6), .trigger("falling")) register_21 (
    .D(demultiplexer_7_out1), .Q(OR), .clk(d_ff_39_q), .clr(Clear));  // open: en
  Register #(.width(6), .trigger("falling")) register_22 (
    .D(demultiplexer_13_out1), .Q(XOR), .clk(d_ff_42_q), .clr(Clear));  // open: en
  Register #(.width(6), .trigger("falling")) register_23 (
    .D(demultiplexer_14_out1), .Q(SHL), .clk(d_ff_45_q), .clr(Clear));  // open: en
  Register #(.width(6), .trigger("falling")) register_24 (
    .D(demultiplexer_15_out1), .Q(SHR), .clk(d_ff_48_q), .clr(Clear));  // open: en

  // Other names for the same wires on the sheet: INSTR[5:0] = out_6; OK = out_5

  // Notes on the sheet:
  //   CLEAR
  //   По аски
  //   INP
  //   OUT
  //   MOV
  //   LDO
  //   STO
  //   AND
  //   SUB
  //   ADD
  //   OR
  //   XOR
  //   SHL
  //   SHR
  //   MV
  //   INVA
endmodule

module Iskl (
  input  y0,
  input  y1,
  input  y2,
  input  y3,
  input  y4,
  input  y5,
  output x
);

  wire and_1_out, and_2_out, and_3_out, and_4_out, not_1_out, not_2_out, not_3_out, not_4_out, not_5_out,
       not_6_out;

  not not_1 (not_1_out, y0);
  not not_2 (not_2_out, y1);
  not not_3 (not_3_out, y3);
  not not_4 (not_4_out, y4);
  and and_1 (and_1_out, not_1_out, not_2_out);
  not not_5 (not_5_out, y2);
  and and_2 (and_2_out, not_3_out, not_4_out);
  not not_6 (not_6_out, y5);
  and and_3 (and_3_out, and_1_out, not_5_out);
  and and_4 (and_4_out, and_2_out, not_6_out);
  and and_5 (x, and_3_out, and_4_out);
endmodule

module _10Takts (
  input  y0,
  input  y1,
  input  y2,
  input  y3,
  output x
);

  wire not_1_out, not_2_out, not_3_out, not_4_out, or_1_out, or_2_out;

  not not_1 (not_1_out, y0);
  or or_1 (or_1_out, not_1_out, not_2_out);
  not not_2 (not_2_out, y1);
  not not_3 (not_3_out, y2);
  or or_2 (or_2_out, not_3_out, not_4_out);
  not not_4 (not_4_out, y3);
  or or_3 (x, or_1_out, or_2_out);
endmodule

module Read (
  input  in_1,
  input  in_2,
  output out_3,
  output out_4
);

  wire and_1_out, n1takts_1_x, n10takts_1_x, not_1_out, \ф_1_out_2 , \ф_3_out_2 , \ф_4_out_2 ;
  wire [1:0] counter_2_q;
  wire [3:0] counter_1_q;

  _10Takts u_10takts_1 (
    .y0(counter_1_q[0]), .y1(counter_1_q[1]), .y2(counter_1_q[2]), .y3(counter_1_q[3]), .x(n10takts_1_x));
  Counter #(.width(4), .max('hf), .ongoal("stay")) counter_1 (
    .Q(counter_1_q), .clk(in_1), .clr(in_2));  // open: load, D, count, carry
  and and_1 (and_1_out, n10takts_1_x, in_1);
  not not_1 (not_1_out, n10takts_1_x);
  Counter #(.width(2), .max('h2), .ongoal("stay")) counter_2 (
    .Q(counter_2_q), .clk(and_1_out), .clr(not_1_out));  // open: load, D, count, carry
  \Ф  \u_ф_1  (.in_1(\ф_4_out_2 ), .out_2(\ф_1_out_2 ));
  \Ф  \u_ф_2  (.in_1(\ф_1_out_2 ), .out_2(out_3));
  \Ф  \u_ф_3  (.in_1(and_1_out), .out_2(\ф_3_out_2 ));
  \Ф  \u_ф_4  (.in_1(\ф_3_out_2 ), .out_2(\ф_4_out_2 ));
  _1TAKTS u_1takts_1 (.Y0(counter_2_q[1]), .Y1(counter_2_q[0]), .X(n1takts_1_x));
  and and_2 (out_4, n1takts_1_x, and_1_out);
endmodule

module _1Takts (
  input  in_1,
  input  in_2,
  output out_3
);

  wire [1:0] counter_1_q;

  Counter #(.width(2), .max('h2), .ongoal("stay")) counter_1 (
    .Q(counter_1_q), .clk(in_1), .clr(in_2));  // open: load, D, count, carry
  or or_1 (out_3, counter_1_q[0], ~counter_1_q[1]);  // OR_Gate
endmodule

module _1TAKTS (
  input  Y0,
  input  Y1,
  output X
);

  not not_1 (X, Y0);
endmodule
