// Logisim project БВТ2003_Тураев_Некруз_№11(Процессор).circ as structural Verilog: 1 circuit, main circuit main
module main (
  input  [3:0] data_in,
  input  [11:0] in_2,
  input  in_3,
  input  [3:0] in_4,
  output ACC_0,
  output ACC_0_2,
  output [3:0] out_7,
  output [1:0] out_8,
  output [3:0] out_9
);

  wire and_1_out, and_2_out, and_3_out, clock_1_out, not_1_out, not_2_out, or_1_out;
  wire [3:0] adder_1_out, counter_1_q, multiplexer_1_out, ram_1_data, ram_3_data, register_1_q,
       subtractor_1_out;
  wire [11:4] ram_1_data_2;

  and and_1 (and_1_out, ACC_0, ram_1_data_2[5]);
  and and_2 (and_2_out, ram_1_data_2[4], ACC_0_2);
  or or_1 (or_1_out, ram_1_data_2[6], and_1_out, and_2_out);
  not not_1 (not_1_out, or_1_out);
  Clock clock_1 (.out(clock_1_out));
  Counter #(.width(4), .max('hf)) counter_1 (
    .load(or_1_out), .D(ram_1_data), .count(not_1_out), .Q(counter_1_q));  // open: carry, clk, clr
  RAM #(.addrWidth(4), .dataWidth(12), .bus("separate")) ram_1 (
    .addr(counter_1_q), .din(in_2), .data({ram_1_data_2[11:9], out_8, ram_1_data_2[6:4], ram_1_data}),
    .clk(in_3));  // open: str, sel, ld, clr
  and and_3 (and_3_out, ram_1_data_2[10], not_2_out);
  not not_2 (not_2_out, clock_1_out);
  // Probe on ram_3_data
  RAM #(.addrWidth(4), .dataWidth(4), .bus("separate")) ram_2 (
    .addr(ram_1_data), .din(in_4), .data(out_9));  // open: str, sel, clk, ld, clr
  RAM #(.addrWidth(4), .dataWidth(4), .bus("separate")) ram_3 (
    .addr(ram_1_data), .din(register_1_q), .data(ram_3_data), .clk(ram_1_data_2[11]));  // open: str, sel, ld, clr
  Adder #(.width(4)) adder_1 (.a(register_1_q), .b(ram_3_data), .out(adder_1_out));  // open: cin, cout
  Subtractor #(.width(4)) subtractor_1 (.a(register_1_q), .b(ram_3_data), .out(subtractor_1_out));  // open: bin, bout
  Multiplexer #(.select(2), .width(4)) multiplexer_1 (
    .in0(data_in), .in1(adder_1_out), .in2(subtractor_1_out), .in3(ram_3_data), .out(multiplexer_1_out),
    .sel(out_8));  // open: en
  Register #(.width(4)) register_1 (.D(multiplexer_1_out), .Q(register_1_q), .clk(and_3_out));  // open: en, clr
  nor nor_1 (ACC_0, register_1_q[0], register_1_q[1], register_1_q[2], register_1_q[3]);
  Register #(.width(4)) register_2 (.D(register_1_q), .Q(out_7), .clk(ram_1_data_2[9]));  // open: en, clr
  not not_3 (ACC_0_2, ACC_0);

  // Notes on the sheet:
  //   ACC
  //   OUT
endmodule
