// Logisim project БВТ2003_Тураев_Некруз_№2.circ as structural Verilog: 1 circuit, main circuit main
module main (
  input  \А ,
  input  \А_2 ,
  input  \А_3 ,
  input  \В ,
  input  \А_4 ,
  input  \А_5 ,
  input  \В_2 ,
  input  \В_3 ,
  input  \В_4 ,
  input  \В_5 ,
  input  in_11,
  input  in_12,
  input  \А_6 ,
  input  \А_7 ,
  input  \В_6 ,
  input  in_16,
  input  \В_7 ,
  input  in_18,
  input  in_19,
  input  in_20,
  input  in_21,
  input  in_22,
  input  in_23,
  input  in_24,
  input  in_25,
  input  in_26,
  input  in_27,
  input  in_28,
  input  in_29,
  input  in_30,
  output out_31,
  output out_32,
  output out_33,
  output out_34,
  output out_35,
  output out_36,
  output out_37,
  output out_38,
  output out_39,
  output out_40,
  output out_41,
  output out_42,
  output out_43,
  output out_44,
  output out_45,
  output out_46,
  output out_47,
  output out_48,
  output out_49
);

  wire transistor_4_out, transistor_5_out, transistor_6_out, transistor_10_out, transistor_13_out,
       transistor_17_out, transistor_19_out, transistor_25_out, transistor_26_out, transistor_29_out,
       transistor_31_out, transistor_33_out, transistor_34_out, transistor_38_out, transistor_41_out,
       transistor_42_out, transistor_47_out, transistor_49_out, transistor_50_out, transistor_53_out,
       transistor_55_out, transistor_56_out, transistor_57_out, transistor_61_out, transistor_62_out,
       transistor_65_out, transistor_66_out, transistor_70_out, transistor_73_out, transistor_75_out,
       transistor_76_out, transistor_79_out;

  Transistor transistor_1 (.in(1'b1), .out(out_37), .gate(in_11));
  Transistor #(.\type ("n")) transistor_2 (.in(1'b0), .out(out_37), .gate(in_11));
  Transistor #(.\type ("n")) transistor_3 (.in(transistor_4_out), .out(out_42), .gate(\А_7 ));
  Transistor transistor_4 (.in(1'b0), .out(transistor_4_out), .gate(\В_7 ));
  Transistor #(.\type ("n")) transistor_5 (.in(1'b1), .out(transistor_5_out), .gate(in_18));
  Transistor #(.\type ("n")) transistor_6 (.in(transistor_5_out), .out(transistor_6_out), .gate(in_22));
  Transistor #(.\type ("n")) transistor_7 (.in(transistor_6_out), .out(out_45), .gate(in_26));
  Transistor transistor_8 (.in(1'b0), .out(out_45), .gate(in_26));
  Transistor transistor_9 (.in(1'b0), .out(out_45), .gate(in_22));
  Transistor transistor_10 (.in(1'b1), .out(transistor_10_out), .gate(\А_7 ));
  Transistor #(.\type ("n")) transistor_11 (.in(transistor_10_out), .out(out_42), .gate(\В_7 ));
  Transistor transistor_12 (.in(1'b0), .out(out_45), .gate(in_18));
  Transistor #(.\type ("n")) transistor_13 (.in(1'b1), .out(transistor_13_out), .gate(\А_3 ));
  Transistor #(.\type ("n")) transistor_14 (.in(transistor_13_out), .out(out_32), .gate(\В_2 ));
  Transistor transistor_15 (.in(1'b0), .out(out_32), .gate(\А_3 ));
  Transistor transistor_16 (.in(1'b0), .out(out_32), .gate(\В_2 ));
  Transistor #(.\type ("n")) transistor_17 (.in(1'b1), .out(transistor_17_out), .gate(\А_7 ));
  Transistor #(.\type ("n")) transistor_18 (.in(transistor_17_out), .out(out_42), .gate(\В_7 ));
  Transistor transistor_19 (.in(1'b1), .out(transistor_19_out), .gate(\А_7 ));
  Transistor transistor_20 (.in(transistor_19_out), .out(out_42), .gate(\В_7 ));
  Transistor #(.\type ("n")) transistor_21 (.in(1'b1), .out(out_48), .gate(in_21));
  Transistor #(.\type ("n")) transistor_22 (.in(1'b1), .out(out_48), .gate(in_25));
  Transistor #(.\type ("n")) transistor_23 (.in(1'b1), .out(out_48), .gate(in_29));
  Transistor transistor_24 (.in(\В ), .out(out_33), .gate(\А ));
  Transistor transistor_25 (.in(1'b0), .out(transistor_25_out), .gate(in_21));
  Transistor transistor_26 (.in(transistor_25_out), .out(transistor_26_out), .gate(in_25));
  Transistor transistor_27 (.in(transistor_26_out), .out(out_48), .gate(in_29));
  Transistor #(.\type ("n")) transistor_28 (.in(1'b1), .out(out_33), .gate(\А ));
  Transistor transistor_29 (.in(1'b1), .out(transistor_29_out), .gate(in_12));
  Transistor transistor_30 (.in(transistor_29_out), .out(out_41), .gate(in_16));
  Transistor #(.\type ("n")) transistor_31 (.in(1'b1), .out(transistor_31_out), .gate(in_12));
  Transistor #(.\type ("n")) transistor_32 (.in(transistor_31_out), .out(out_41), .gate(in_16));
  Transistor #(.\type ("n")) transistor_33 (.in(1'b0), .out(transistor_33_out), .gate(in_20));
  Transistor #(.\type ("n")) transistor_34 (.in(transistor_33_out), .out(transistor_34_out), .gate(in_24));
  Transistor #(.\type ("n")) transistor_35 (.in(transistor_34_out), .out(out_47), .gate(in_28));
  Transistor transistor_36 (.in(1'b1), .out(out_47), .gate(in_28));
  Transistor #(.\type ("n")) transistor_37 (.in(transistor_38_out), .out(out_35), .gate(\А_4 ));
  Transistor #(.\type ("n")) transistor_38 (.in(1'b0), .out(transistor_38_out), .gate(\В_4 ));
  Transistor transistor_39 (.in(transistor_41_out), .out(out_41), .gate(in_12));
  Transistor #(.\type ("n")) transistor_40 (.in(transistor_42_out), .out(out_41), .gate(in_12));
  Transistor #(.\type ("n")) transistor_41 (.in(1'b0), .out(transistor_41_out), .gate(in_16));
  Transistor transistor_42 (.in(1'b0), .out(transistor_42_out), .gate(in_16));
  Transistor transistor_43 (.in(1'b1), .out(out_47), .gate(in_24));
  Transistor transistor_44 (.in(1'b1), .out(out_47), .gate(in_20));
  Transistor transistor_45 (.in(1'b1), .out(out_35), .gate(\А_4 ));
  Transistor transistor_46 (.in(1'b1), .out(out_35), .gate(\В_4 ));
  Transistor transistor_47 (.in(1'b1), .out(transistor_47_out), .gate(\А_2 ));
  Transistor transistor_48 (.in(transistor_47_out), .out(out_34), .gate(\В_3 ));
  Transistor #(.\type ("n")) transistor_49 (.in(1'b0), .out(transistor_49_out), .gate(\А_2 ));
  Transistor #(.\type ("n")) transistor_50 (.in(1'b0), .out(transistor_50_out), .gate(\А_2 ));
  Transistor transistor_51 (.in(transistor_49_out), .out(out_34), .gate(\В_3 ));
  Transistor transistor_52 (.in(transistor_50_out), .out(out_34), .gate(\В_3 ));
  Transistor transistor_53 (.in(1'b1), .out(transistor_53_out), .gate(\А_6 ));
  Transistor transistor_54 (.in(transistor_53_out), .out(out_40), .gate(\В_6 ));
  Transistor #(.\type ("n")) transistor_55 (.in(1'b0), .out(transistor_55_out), .gate(in_19));
  Transistor #(.\type ("n")) transistor_56 (.in(transistor_55_out), .out(transistor_56_out), .gate(in_23));
  Transistor #(.\type ("n")) transistor_57 (.in(transistor_56_out), .out(transistor_57_out), .gate(in_27));
  Transistor #(.\type ("n")) transistor_58 (.in(transistor_57_out), .out(out_46), .gate(in_30));
  Transistor transistor_59 (.in(1'b1), .out(out_46), .gate(in_27));
  Transistor transistor_60 (.in(1'b1), .out(out_46), .gate(in_23));
  Transistor #(.\type ("n")) transistor_61 (.in(1'b0), .out(transistor_61_out), .gate(\А_2 ));
  Transistor transistor_62 (.in(1'b0), .out(transistor_62_out), .gate(\А_2 ));
  Transistor #(.\type ("n")) transistor_63 (.in(transistor_62_out), .out(out_34), .gate(\В_3 ));
  Transistor #(.\type ("n")) transistor_64 (.in(transistor_61_out), .out(out_34), .gate(\В_3 ));
  Transistor #(.\type ("n")) transistor_65 (.in(1'b0), .out(transistor_65_out), .gate(\А_6 ));
  Transistor #(.\type ("n")) transistor_66 (.in(1'b1), .out(transistor_66_out), .gate(\А_6 ));
  Transistor #(.\type ("n")) transistor_67 (.in(transistor_66_out), .out(out_40), .gate(\В_6 ));
  Transistor transistor_68 (.in(transistor_65_out), .out(out_40), .gate(\В_6 ));
  Transistor transistor_69 (.in(1'b1), .out(out_46), .gate(in_19));
  Transistor transistor_70 (.in(1'b0), .out(transistor_70_out), .gate(\А_6 ));
  Transistor #(.\type ("n")) transistor_71 (.in(transistor_70_out), .out(out_40), .gate(\В_6 ));
  Transistor transistor_72 (.in(1'b1), .out(out_46), .gate(in_30));
  Transistor transistor_73 (.in(1'b0), .out(transistor_73_out), .gate(\А_5 ));
  Transistor transistor_74 (.in(transistor_73_out), .out(out_36), .gate(\В_5 ));
  Transistor #(.\type ("n")) transistor_75 (.in(1'b1), .out(transistor_75_out), .gate(\А_5 ));
  Transistor #(.\type ("n")) transistor_76 (.in(1'b0), .out(transistor_76_out), .gate(\А_5 ));
  Transistor #(.\type ("n")) transistor_77 (.in(transistor_76_out), .out(out_36), .gate(\В_5 ));
  Transistor transistor_78 (.in(transistor_75_out), .out(out_36), .gate(\В_5 ));
  Transistor transistor_79 (.in(1'b1), .out(transistor_79_out), .gate(\А_5 ));
  Transistor #(.\type ("n")) transistor_80 (.in(transistor_79_out), .out(out_36), .gate(\В_5 ));

  assign out_31 = 1'b1;
  assign out_38 = 1'b0;
  assign out_39 = 1'b1;
  assign out_43 = 1'b0;
  assign out_44 = 1'b1;
  assign out_49 = 1'b0;

  // Notes on the sheet:
  //   Элемент Не
  //   Элемент импликация или следствие
  //   Элесмент 3И
  //   1
  //   2
  //   Элемент и
  //   3
  //   4
  //   5
  //   6
  //   7
  //   8
  //   Элемент или
  //   Элемент 3ИЛИ
  //   2 н-типа
  //   1 п-типа
  //   Если А=1, то транзистор 1 ничего не проводит,
  //   а 2 транзистор проводит 1, либо 0
  //   Если А=0, то 2 транзистор ничего не проводит,
  //   а 1 транзистор проводит либо 1, либо 0
  //   Элемент эквивалентность
  //   Элесмент 3И - НЕ
  //   Элемент И-НЕ
  //   Элемент ИЛИ-НЕ
  //   Элемент Исключащее ИЛИ - НЕ
  //   Элесмент 3И - НЕ
  //   Элемент Исключащее ИЛИ
endmodule
