// Logisim project БВТ2003_Тураев_Некруз_№3.circ as structural Verilog: 2 circuits, main circuit main
module main (
  input  [7:0] in_1,
  input  [7:0] in_2,
  input  in_3,
  output [7:0] out_4,
  output out_5
);

  wire adder_1_cout;
  wire [7:0] \инвентор_1_out_3 ;

  \инвентор  \u_инвентор_1  (.in_1(in_2), .in_2(in_3), .out_3(\инвентор_1_out_3 ));
  Adder adder_1 (.a(in_1), .b(\инвентор_1_out_3 ), .out(out_4), .cin(in_3), .cout(adder_1_cout));
  xor xor_1 (out_5, in_3, adder_1_cout);
endmodule

module \инвентор  (
  input  [7:0] in_1,
  input  in_2,
  output [7:0] out_3
);

  xor xor_1 (out_3[7], in_2, in_1[7]);
  xor xor_2 (out_3[6], in_2, in_1[6]);
  xor xor_3 (out_3[5], in_2, in_1[5]);
  xor xor_4 (out_3[4], in_2, in_1[4]);
  xor xor_5 (out_3[3], in_2, in_1[3]);
  xor xor_6 (out_3[2], in_2, in_1[2]);
  xor xor_7 (out_3[1], in_2, in_1[1]);
  xor xor_8 (out_3[0], in_2, in_1[0]);
endmodule
