// Logisim project БВТ2003_Тураев_Некруз_№4.circ as structural Verilog: 2 circuits, main circuit main
module main (
  input  [7:0] \Число_А ,
  input  [7:0] \Число_В ,
  input  in_3,
  input  \Перенос ,
  output [7:0] out_5,
  output [7:0] \Сумма 
);

  wire button_1_out;
  wire [7:0] multiplexer_1_out;

  Adder adder_1 (.a(multiplexer_1_out), .b(\Число_А ), .out(\Сумма ), .cin(1'b0), .cout(\Перенос ));
  Button button_1 (.out(button_1_out));
  \_8_битовая_защёлка  \u_8_битовая_защёлка_1  (.in_1(button_1_out), .in_2(\Сумма ), .out_3(out_5));
  Multiplexer #(.width(8)) multiplexer_1 (
    .in0(out_5), .in1(\Число_В ), .out(multiplexer_1_out), .sel(in_3));  // open: en

  // Notes on the sheet:
  //   Кнопка сохранения суммы
  //   0
  //   1
  //   Число которое хранится
  //   Канал, который проходит
endmodule

module \_8_битовая_защёлка  (
  input  in_1,
  input  [7:0] in_2,
  output [7:0] out_3
);

  wire button_1_out, or_1_out;

  Button button_1 (.out(button_1_out));
  or or_1 (or_1_out, in_1, button_1_out);
  D_Flip_Flop d_ff_1 (.clk(or_1_out), .D(in_2[0]), .Q(out_3[0]));  // open: Qn, preset, en, reset
  D_Flip_Flop d_ff_2 (.clk(or_1_out), .D(in_2[1]), .Q(out_3[1]));  // open: Qn, preset, en, reset
  D_Flip_Flop d_ff_3 (.clk(or_1_out), .D(in_2[2]), .Q(out_3[2]));  // open: Qn, preset, en, reset
  D_Flip_Flop d_ff_4 (.clk(or_1_out), .D(in_2[3]), .Q(out_3[3]));  // open: Qn, preset, en, reset
  D_Flip_Flop d_ff_5 (.clk(or_1_out), .D(in_2[4]), .Q(out_3[4]));  // open: Qn, preset, en, reset
  D_Flip_Flop d_ff_6 (.clk(or_1_out), .D(in_2[5]), .Q(out_3[5]));  // open: Qn, preset, en, reset
  D_Flip_Flop d_ff_7 (.clk(or_1_out), .D(in_2[6]), .Q(out_3[6]));  // open: Qn, preset, en, reset
  D_Flip_Flop d_ff_8 (.clk(or_1_out), .D(in_2[7]), .Q(out_3[7]));  // open: Qn, preset, en, reset
endmodule
