// Logisim project БВТ2003_Тураев_Некруз_№5.circ as structural Verilog: 1 circuit, main circuit main
module main (
  input  in_1
);

  wire and_1_out, and_2_out, and_3_out, clock_1_out, clock_2_out, not_1_out, not_2_out;
  wire [1:0] ram_1_data, ram_2_data;
  wire [2:0] counter_1_q, counter_2_q;
  wire [7:0] adder_1_out, adder_2_out, ram_3_data, ram_4_data, register_1_q, register_2_q;

  Clock clock_1 (.out(clock_1_out));
  Clock clock_2 (.out(clock_2_out));
  Counter #(.width(3), .max('h7)) counter_1 (.Q(counter_1_q), .clk(clock_1_out));  // open: load, D, count, carry, clr
  Counter #(.width(3), .max('h7)) counter_2 (.Q(counter_2_q), .clk(clock_2_out));  // open: load, D, count, carry, clr
  RAM #(.addrWidth(3), .dataWidth(2)) ram_1 (.addr(counter_1_q), .data(ram_1_data));  // open: sel, clk, ld, clr
  RAM #(.addrWidth(3), .dataWidth(2)) ram_2 (.addr(counter_2_q), .data(ram_2_data));  // open: sel, clk, ld, clr
  not not_1 (not_1_out, clock_1_out);
  not not_2 (not_2_out, clock_2_out);
  RAM #(.addrWidth(3), .bus("separate")) ram_3 (
    .addr(counter_1_q), .din(register_1_q), .data(ram_3_data), .clk(ram_1_data[1]));  // open: str, sel, ld, clr
  RAM #(.addrWidth(3), .bus("separate")) ram_4 (
    .addr(counter_2_q), .din(register_2_q), .data(ram_4_data), .clk(ram_2_data[1]));  // open: str, sel, ld, clr
  Adder adder_1 (.a(register_1_q), .b(ram_3_data), .out(adder_1_out));  // open: cin, cout
  and and_1 (and_1_out, ram_1_data[1], ram_1_data[0]);
  and and_2 (and_2_out, ram_1_data[0], not_1_out);
  Adder adder_2 (.a(register_2_q), .b(ram_4_data), .out(adder_2_out));  // open: cin, cout
  and and_3 (and_3_out, ram_2_data[0], not_2_out);
  Register register_1 (.D(adder_1_out), .Q(register_1_q), .clk(and_2_out), .clr(and_1_out));  // open: en
  Register register_2 (.D(adder_2_out), .Q(register_2_q), .clk(and_3_out), .clr(in_1));  // open: en

  // Notes on the sheet:
  //   3 Очистить аккум
  //   Загрузить число из ОЗУ в аккумулятор
  //   1 Загрузить число из сумматора в аккумулятор
  //   2 Сохранить число из аккумулятора в ОЗУ
  //   аккум
  //   аккум
endmodule
