// Logisim project БВТ2003_Тураев_Некруз_№6(архитектура Фон-Неймана c дешифратором).circ as structural Verilog: 2 circuits, main circuit main
module main (
  input  [7:0] in_1,
  input  in_2,
  output [7:0] out_3,
  output [7:0] out_4,
  output [1:0] out_5,
  output out_6
);

  wire and_1_out, and_2_out, and_3_out, and_4_out, and_5_out, button_1_out, clock_1_out, not_1_out, not_2_out;
  wire [3:0] counter_1_q, multiplexer_1_out, register_1_q, register_4_q;
  wire [7:0] adder_1_out, multiplexer_2_out, ram_1_data, register_2_q, subtractor_1_out;

  Button button_1 (.out(button_1_out));
  not not_1 (not_1_out, and_5_out);
  Clock clock_1 (.out(clock_1_out));
  Counter #(.width(4), .max('hf)) counter_1 (
    .load(and_5_out), .D(register_1_q), .count(not_1_out), .Q(counter_1_q), .clk(clock_1_out),
    .clr(button_1_out));  // open: carry
  not not_2 (not_2_out, clock_1_out);
  Multiplexer #(.width(4)) multiplexer_1 (
    .in0(counter_1_q), .in1(register_1_q), .out(multiplexer_1_out), .sel(not_2_out));  // open: en
  and and_1 (and_1_out, clock_1_out, and_4_out, ~register_4_q[2], ~register_4_q[3]);  // AND_Gate
  // Probe on ram_1_data
  RAM #(.addrWidth(4), .bus("separate")) ram_1 (
    .addr(multiplexer_1_out), .din(out_3), .data(ram_1_data), .clk(and_1_out));  // open: str, sel, ld, clr
  // Probe on ram_1_data[3:0]
  // Probe on ram_1_data[7:4]
  Register #(.width(4)) register_1 (.D(ram_1_data[3:0]), .Q(register_1_q), .clk(not_2_out));  // open: en, clr
  // Probe on in_1
  Register #(.trigger("falling")) register_2 (
    .D(ram_1_data), .Q(register_2_q), .clk(and_2_out), .clr(button_1_out));  // open: en
  Register #(.trigger("falling")) register_3 (.D(in_1), .clk(in_2));  // open: en, Q, clr
  Register #(.width(4)) register_4 (.D(ram_1_data[7:4]), .Q(register_4_q), .clk(not_2_out));  // open: en, clr
  Adder adder_1 (.a(out_3), .b(register_2_q), .out(adder_1_out));  // open: cin, cout
  Subtractor subtractor_1 (.a(out_3), .b(register_2_q), .out(subtractor_1_out));  // open: bin, bout
  and and_2 (and_2_out, register_4_q[0], ~register_4_q[1], ~register_4_q[2], and_3_out);  // AND_Gate
  and and_3 (and_3_out, ~register_4_q[3], not_2_out);  // AND_Gate
  and and_4 (and_4_out, register_4_q[1], ~register_4_q[0]);  // AND_Gate
  and and_5 (and_5_out, register_4_q[3], ~register_4_q[2], ~register_4_q[1], ~register_4_q[0]);  // AND_Gate
  Multiplexer #(.select(2), .width(8)) multiplexer_2 (
    .in0(register_2_q), .in1(adder_1_out), .in2(subtractor_1_out), .in3(out_4), .out(multiplexer_2_out),
    .sel(out_5));  // open: en
  \Дешифратор  \u_дешифратор_1  (
    .q0(register_4_q[3]), .q1(register_4_q[2]), .y1(out_5[0]), .q2(register_4_q[1]), .q3(register_4_q[0]),
    .y2(out_5[1]));
  Register #(.trigger("falling")) register_5 (
    .D(multiplexer_2_out), .Q(out_3), .clk(and_2_out), .clr(button_1_out));  // open: en
  // Probe on nothing

  // Notes on the sheet:
  //   Add(x) = 0001 - сложить с аккум
  //   STM(x) = 0010 - записать в память
  //   JMP = 1000 - безусловный переход
  //   LDT(x) = 0100 - загрузить из адреса в регистр темп
  //   STM(x) = 0010
  //   Запись
  //   в память
  //   Адрес
  //   0011(3 канал дешифратора)
  //   0101(2 канал дешифратора)
  //   0110(1 канал дешифратора
  //   Приостальных занчениях 0 канал
  //   Инструкция
  //   Add(x) = 0001 в акк
  //   0011
  //   1 0 - 0
  //   0 1 - 0 
  //   JMP = 0100
  //   Безусловный переход
  //   -  01
  //   ACCUM
endmodule

module \Дешифратор  (
  input  q0,
  input  q1,
  input  q2,
  input  q3,
  output y1,
  output y2
);

  wire and_1_out, and_2_out, and_3_out, and_4_out, not_1_out, not_2_out, not_3_out, not_4_out, not_5_out,
       not_6_out, not_7_out, not_8_out;

  not not_1 (not_1_out, q0);
  not not_2 (not_2_out, q1);
  not not_3 (not_3_out, q0);
  not not_4 (not_4_out, q3);
  not not_5 (not_5_out, q0);
  not not_6 (not_6_out, q1);
  and and_1 (and_1_out, not_5_out, not_6_out, q3);
  not not_7 (not_7_out, q0);
  not not_8 (not_8_out, q2);
  and and_2 (and_2_out, not_7_out, not_8_out, q3);
  and and_3 (and_3_out, not_1_out, not_2_out, q2, q3);
  or or_1 (y1, and_3_out, and_4_out);
  and and_4 (and_4_out, not_3_out, q1, q2, not_4_out);
  or or_2 (y2, and_1_out, and_2_out);
endmodule
