// Logisim project БВТ2003_Тураев_Некруз_№7.2.circ as structural Verilog: 6 circuits, main circuit main
module main (
  input  in_1,
  input  in_2,
  input  in_3,
  input  in_4,
  input  in_5,
  input  in_6,
  input  in_7,
  input  in_8,
  input  in_9,
  input  [3:0] in_10,
  output [3:0] out_11,
  output [3:0] out_12,
  output [3:0] out_13,
  output [3:0] out_14,
  output [3:0] out_15,
  output [3:0] out_16,
  output out_17,
  output out_18,
  output out_19,
  output out_20
);

  wire _0_out, _1_out, _2_out, _3_out, _4_out, _5_out, _6_out, _7_out, _8_out, _9_out, Backspace_out,
       bittoind_1_w0, bittoind_1_w1, bittoind_1_w2, bittoind_1_w3, bittoind_1_w4, bittoind_1_w5,
       bittoind_1_w6, bittoind_1_w7, bittoind_2_w0, bittoind_2_w1, bittoind_2_w2, bittoind_2_w3,
       bittoind_2_w4, bittoind_2_w5, bittoind_2_w6, bittoind_2_w7, bittoind_3_w0, bittoind_3_w1,
       bittoind_3_w2, bittoind_3_w3, bittoind_3_w4, bittoind_3_w5, bittoind_3_w6, bittoind_3_w7,
       bittoind_4_w0, bittoind_4_w1, bittoind_4_w2, bittoind_4_w3, bittoind_4_w4, bittoind_4_w5,
       bittoind_4_w6, bittoind_4_w7, bittoind_5_w0, bittoind_5_w1, bittoind_5_w2, bittoind_5_w3,
       bittoind_5_w4, bittoind_5_w5, bittoind_5_w6, bittoind_5_w7, bittoind_6_w0, bittoind_6_w1,
       bittoind_6_w2, bittoind_6_w3, bittoind_6_w4, bittoind_6_w5, bittoind_6_w6, bittoind_6_w7,
       bittoind_8_w0, bittoind_8_w1, bittoind_8_w2, bittoind_8_w3, bittoind_8_w4, bittoind_8_w5,
       bittoind_8_w6, bittoind_8_w7, bittoind_9_w0, bittoind_9_w1, bittoind_9_w2, bittoind_9_w3,
       bittoind_9_w4, bittoind_9_w5, bittoind_9_w6, bittoind_9_w7, bittoind_10_w0, bittoind_10_w1,
       bittoind_10_w2, bittoind_10_w3, bittoind_10_w4, bittoind_10_w5, bittoind_10_w6, bittoind_10_w7,
       bittoind_11_w0, bittoind_11_w1, bittoind_11_w2, bittoind_11_w3, bittoind_11_w4, bittoind_11_w5,
       bittoind_11_w6, bittoind_11_w7, not_1_out, or_1_out, or_2_out, or_3_out, \Очистить_out ;
  wire [1:0] counter_2_q;
  wire [2:0] counter_1_q;
  wire [3:0] multiplexer_1_out, multiplexer_2_out, multiplexer_3_out, multiplexer_4_out, multiplexer_5_out,
       register_1_q, register_2_q, register_3_q, register_4_q, register_5_q, register_6_q, register_7_q,
       register_8_q, register_9_q, register_10_q, register_11_q, register_14_q;

  Button _0 (.out(_0_out));
  Button _1 (.out(_1_out));
  Button _2 (.out(_2_out));
  Button _3 (.out(_3_out));
  Button _4 (.out(_4_out));
  Button _5 (.out(_5_out));
  Button _6 (.out(_6_out));
  Button _7 (.out(_7_out));
  Button _8 (.out(_8_out));
  Button _9 (.out(_9_out));
  Button Backspace (.out(Backspace_out));
  Button \u_Очистить  (.out(\Очистить_out ));
  or or_1 (or_1_out, _0_out, _1_out, _2_out, _3_out, _4_out, _5_out, _6_out, _7_out, _8_out, _9_out);
  DecToBit dectobit_1 (
    .q0(_0_out), .q1(_1_out), .q2(_2_out), .q3(_3_out), .q4(_4_out), .q5(_5_out), .q6(_6_out), .q7(_7_out),
    .q8(_8_out), .q9(_9_out), .w0(out_15[3]), .w1(out_15[2]), .w2(out_15[1]), .w3(out_15[0]));
  Counter #(.width(3), .max('h7)) counter_1 (.Q(counter_1_q));  // open: load, D, count, carry, clk, clr
  not not_1 (not_1_out, or_2_out);
  Multiplexer #(.width(4)) multiplexer_1 (
    .in0(register_7_q), .in1(register_2_q), .out(multiplexer_1_out), .sel(Backspace_out));  // open: en
  Register #(.width(4), .trigger("falling")) register_1 (
    .D(multiplexer_1_out), .Q(register_1_q), .clk(or_3_out), .clr(\Очистить_out ));  // open: en
  Register #(.width(4), .trigger("falling")) register_2 (
    .D(multiplexer_2_out), .Q(register_2_q), .clk(or_3_out), .clr(\Очистить_out ));  // open: en
  Multiplexer #(.width(4)) multiplexer_2 (
    .in0(register_1_q), .in1(register_3_q), .out(multiplexer_2_out), .sel(Backspace_out));  // open: en
  Multiplexer #(.width(4)) multiplexer_3 (
    .in0(register_2_q), .in1(register_4_q), .out(multiplexer_3_out), .sel(Backspace_out));  // open: en
  Register #(.width(4), .trigger("falling")) register_3 (
    .D(multiplexer_3_out), .Q(register_3_q), .clk(or_3_out), .clr(\Очистить_out ));  // open: en
  Register #(.width(4), .trigger("falling")) register_4 (
    .D(multiplexer_4_out), .Q(register_4_q), .clk(or_3_out), .clr(\Очистить_out ));  // open: en
  Multiplexer #(.width(4)) multiplexer_4 (
    .in0(register_3_q), .in1(register_5_q), .out(multiplexer_4_out), .sel(Backspace_out));  // open: en
  Multiplexer #(.width(4)) multiplexer_5 (
    .in0(register_4_q), .in1(register_6_q), .out(multiplexer_5_out), .sel(Backspace_out));  // open: en
  Register #(.width(4), .trigger("falling")) register_5 (
    .D(multiplexer_5_out), .Q(register_5_q), .clk(or_3_out), .clr(\Очистить_out ));  // open: en
  Register #(.width(4), .trigger("falling")) register_6 (.D(in_10), .Q(register_6_q));  // open: en, clk, clr
  Register #(.width(4), .trigger("falling")) register_7 (
    .D(out_15), .Q(register_7_q), .clk(not_1_out));  // open: en, clr
  or or_2 (or_2_out, out_15[0], out_15[1], out_15[2], out_15[3], _0_out);
  or or_3 (or_3_out, Backspace_out, or_2_out);
  RAM #(.addrWidth(3), .dataWidth(2), .bus("separate")) ram_1 (.addr(counter_1_q));  // open: din, data, str, sel, clk, ld, clr
  BITtoIND bittoind_1 (
    .q0(register_7_q[3]), .q1(register_7_q[2]), .q2(register_7_q[1]), .q3(register_7_q[0]),
    .w0(bittoind_1_w0), .w1(bittoind_1_w1), .w2(bittoind_1_w2), .w3(bittoind_1_w3), .w4(bittoind_1_w4),
    .w5(bittoind_1_w5), .w6(bittoind_1_w6), .w7(bittoind_1_w7));
  Register #(.width(4), .trigger("falling")) register_8 (
    .D(register_9_q), .Q(register_8_q), .clk(or_2_out), .clr(\Очистить_out ));  // open: en
  Counter #(.width(2), .max('h3)) counter_2 (.Q(counter_2_q), .clk(or_1_out));  // open: load, D, count, carry, clr
  Register #(.width(4), .trigger("falling")) register_9 (
    .D(register_10_q), .Q(register_9_q), .clk(or_2_out), .clr(\Очистить_out ));  // open: en
  Demultiplexer #(.select(2), .width(4)) demultiplexer_1 (
    .out0(out_11), .out1(out_12), .out2(out_13), .out3(out_14), .in(out_15), .sel(counter_2_q));  // open: en
  Register #(.width(4), .trigger("falling")) register_10 (
    .D(register_11_q), .Q(register_10_q), .clk(or_2_out), .clr(\Очистить_out ));  // open: en
  Register #(.width(4), .trigger("falling")) register_11 (
    .D(register_7_q), .Q(register_11_q), .clk(or_2_out), .clr(\Очистить_out ));  // open: en
  BITtoIND bittoind_2 (
    .q0(register_4_q[3]), .q1(register_4_q[2]), .q2(register_4_q[1]), .q3(register_4_q[0]),
    .w0(bittoind_2_w0), .w1(bittoind_2_w1), .w2(bittoind_2_w2), .w3(bittoind_2_w3), .w4(bittoind_2_w4),
    .w5(bittoind_2_w5), .w6(bittoind_2_w6), .w7(bittoind_2_w7));
  Register #(.width(4), .trigger("falling")) register_12 (.D(out_14), .clk(or_2_out));  // open: en, Q, clr
  _7_Segment_Display u_7_segment_display_1 (
    .g(bittoind_1_w3), .f(bittoind_1_w2), .a(bittoind_1_w1), .b(bittoind_1_w0), .e(bittoind_1_w4),
    .d(bittoind_1_w5), .c(bittoind_1_w6), .dp(bittoind_1_w7));
  BITtoIND bittoind_3 (
    .q0(register_8_q[3]), .q1(register_8_q[2]), .q2(register_8_q[1]), .q3(register_8_q[0]),
    .w0(bittoind_3_w0), .w1(bittoind_3_w1), .w2(bittoind_3_w2), .w3(bittoind_3_w3), .w4(bittoind_3_w4),
    .w5(bittoind_3_w5), .w6(bittoind_3_w6), .w7(bittoind_3_w7));
  _7_Segment_Display u_7_segment_display_2 (
    .g(bittoind_2_w3), .f(bittoind_2_w2), .a(bittoind_2_w1), .b(bittoind_2_w0), .e(bittoind_2_w4),
    .d(bittoind_2_w5), .c(bittoind_2_w6), .dp(bittoind_2_w7));
  Register #(.width(4), .trigger("falling")) register_13 (.D(out_13), .clk(or_2_out));  // open: en, Q, clr
  _7_Segment_Display u_7_segment_display_3 (
    .g(bittoind_3_w3), .f(bittoind_3_w2), .a(bittoind_3_w1), .b(bittoind_3_w0), .e(bittoind_3_w4),
    .d(bittoind_3_w5), .c(bittoind_3_w6), .dp(bittoind_3_w7));
  Register #(.width(4), .trigger("falling")) register_14 (
    .D(out_12), .Q(register_14_q), .clk(or_2_out));  // open: en, clr
  Multiplexer multiplexer_6 ();  // open: in0, in1, out, sel, en
  Demultiplexer demultiplexer_2 (.out0(out_17), .out1(out_18), .in(in_7), .sel(in_8), .en(in_9));
  BITtoIND bittoind_4 (
    .q0(register_3_q[3]), .q1(register_3_q[2]), .q2(register_3_q[1]), .q3(register_3_q[0]),
    .w0(bittoind_4_w0), .w1(bittoind_4_w1), .w2(bittoind_4_w2), .w3(bittoind_4_w3), .w4(bittoind_4_w4),
    .w5(bittoind_4_w5), .w6(bittoind_4_w6), .w7(bittoind_4_w7));
  Register #(.width(4), .trigger("falling")) register_15 (.D(out_11), .clk(or_2_out));  // open: en, Q, clr
  BITtoIND bittoind_5 (
    .q0(register_9_q[3]), .q1(register_9_q[2]), .q2(register_9_q[1]), .q3(register_9_q[0]),
    .w0(bittoind_5_w0), .w1(bittoind_5_w1), .w2(bittoind_5_w2), .w3(bittoind_5_w3), .w4(bittoind_5_w4),
    .w5(bittoind_5_w5), .w6(bittoind_5_w6), .w7(bittoind_5_w7));
  _7_Segment_Display u_7_segment_display_4 (
    .g(bittoind_4_w3), .f(bittoind_4_w2), .a(bittoind_4_w1), .b(bittoind_4_w0), .e(bittoind_4_w4),
    .d(bittoind_4_w5), .c(bittoind_4_w6), .dp(bittoind_4_w7));
  BITtoIND bittoind_6 (
    .q0(register_14_q[3]), .q1(register_14_q[2]), .q2(register_14_q[1]), .q3(register_14_q[0]),
    .w0(bittoind_6_w0), .w1(bittoind_6_w1), .w2(bittoind_6_w2), .w3(bittoind_6_w3), .w4(bittoind_6_w4),
    .w5(bittoind_6_w5), .w6(bittoind_6_w6), .w7(bittoind_6_w7));
  BITtoIND bittoind_7 ();  // open: q0, q1, q2, q3, w0, w1, w2, w3, w4, w5, w6, w7
  _7_Segment_Display u_7_segment_display_5 (
    .g(bittoind_5_w3), .f(bittoind_5_w2), .a(bittoind_5_w1), .b(bittoind_5_w0), .e(bittoind_5_w4),
    .d(bittoind_5_w5), .c(bittoind_5_w6), .dp(bittoind_5_w7));
  _7_Segment_Display u_7_segment_display_6 (
    .g(bittoind_6_w3), .f(bittoind_6_w2), .a(bittoind_6_w1), .b(bittoind_6_w0), .e(bittoind_6_w4),
    .d(bittoind_6_w5), .c(bittoind_6_w6), .dp(bittoind_6_w7));
  Register #(.width(4)) register_16 ();  // open: D, en, Q, clk, clr
  BITtoIND bittoind_8 (
    .q0(register_10_q[3]), .q1(register_10_q[2]), .q2(register_10_q[1]), .q3(register_10_q[0]),
    .w0(bittoind_8_w0), .w1(bittoind_8_w1), .w2(bittoind_8_w2), .w3(bittoind_8_w3), .w4(bittoind_8_w4),
    .w5(bittoind_8_w5), .w6(bittoind_8_w6), .w7(bittoind_8_w7));
  BITtoIND bittoind_9 (
    .q0(register_2_q[3]), .q1(register_2_q[2]), .q2(register_2_q[1]), .q3(register_2_q[0]),
    .w0(bittoind_9_w0), .w1(bittoind_9_w1), .w2(bittoind_9_w2), .w3(bittoind_9_w3), .w4(bittoind_9_w4),
    .w5(bittoind_9_w5), .w6(bittoind_9_w6), .w7(bittoind_9_w7));
  _7_Segment_Display u_7_segment_display_7 (
    .g(bittoind_9_w3), .f(bittoind_9_w2), .a(bittoind_9_w1), .b(bittoind_9_w0), .e(bittoind_9_w4),
    .d(bittoind_9_w5), .c(bittoind_9_w6), .dp(bittoind_9_w7));
  Register #(.width(4)) register_17 (.D({in_2, in_3, in_4, in_5}), .Q(out_16), .clk(in_6));  // open: en, clr
  _7_Segment_Display u_7_segment_display_8 (
    .g(bittoind_8_w3), .f(bittoind_8_w2), .a(bittoind_8_w1), .b(bittoind_8_w0), .e(bittoind_8_w4),
    .d(bittoind_8_w5), .c(bittoind_8_w6), .dp(bittoind_8_w7));
  BITtoIND bittoind_10 (
    .q0(register_1_q[3]), .q1(register_1_q[2]), .q2(register_1_q[1]), .q3(register_1_q[0]),
    .w0(bittoind_10_w0), .w1(bittoind_10_w1), .w2(bittoind_10_w2), .w3(bittoind_10_w3), .w4(bittoind_10_w4),
    .w5(bittoind_10_w5), .w6(bittoind_10_w6), .w7(bittoind_10_w7));
  BITtoIND bittoind_11 (
    .q0(register_11_q[3]), .q1(register_11_q[2]), .q2(register_11_q[1]), .q3(register_11_q[0]),
    .w0(bittoind_11_w0), .w1(bittoind_11_w1), .w2(bittoind_11_w2), .w3(bittoind_11_w3), .w4(bittoind_11_w4),
    .w5(bittoind_11_w5), .w6(bittoind_11_w6), .w7(bittoind_11_w7));
  _7_Segment_Display u_7_segment_display_9 (
    .g(bittoind_10_w3), .f(bittoind_10_w2), .a(bittoind_10_w1), .b(bittoind_10_w0), .e(bittoind_10_w4),
    .d(bittoind_10_w5), .c(bittoind_10_w6), .dp(bittoind_10_w7));
  _7_Segment_Display u_7_segment_display_10 (
    .g(bittoind_11_w3), .f(bittoind_11_w2), .a(bittoind_11_w1), .b(bittoind_11_w0), .e(bittoind_11_w4),
    .d(bittoind_11_w5), .c(bittoind_11_w6), .dp(bittoind_11_w7));

  // Notes on the sheet:
  //   6 памятов, последний хранит число 0
  //   Сам Калькулятор
endmodule

module DECtoBIT (
  input  q0,
  input  q1,
  input  q2,
  input  q3,
  input  q4,
  input  q5,
  input  q6,
  input  q7,
  input  q8,
  input  q9,
  output b0,
  output b1,
  output b2,
  output b3
);

  wire and_1_out, and_2_out, and_3_out, and_4_out, and_5_out, and_6_out, and_7_out, and_8_out, and_9_out,
       and_10_out, and_11_out, and_12_out, and_13_out, and_14_out, and_15_out, and_16_out, and_17_out,
       not_1_out, not_2_out, not_3_out, not_4_out, not_5_out, not_6_out, not_7_out, not_8_out, not_9_out,
       not_10_out, not_11_out, not_12_out, not_13_out, not_14_out, not_15_out, not_16_out, not_17_out,
       not_18_out, not_19_out, not_20_out, not_21_out, not_22_out, not_23_out, not_24_out, not_25_out;

  not not_1 (not_1_out, q0);
  not not_2 (not_2_out, q1);
  not not_3 (not_3_out, q2);
  not not_4 (not_4_out, q3);
  not not_5 (not_5_out, q4);
  not not_6 (not_6_out, q5);
  not not_7 (not_7_out, q6);
  not not_8 (not_8_out, q7);
  not not_9 (not_9_out, q0);
  not not_10 (not_10_out, q1);
  not not_11 (not_11_out, q3);
  not not_12 (not_12_out, q8);
  not not_13 (not_13_out, q0);
  not not_14 (not_14_out, q1);
  not not_15 (not_15_out, q5);
  not not_16 (not_16_out, q8);
  not not_17 (not_17_out, q0);
  not not_18 (not_18_out, q2);
  and and_1 (and_1_out, not_1_out, not_2_out);
  and and_2 (and_2_out, not_3_out, not_4_out);
  and and_3 (and_3_out, not_5_out, not_6_out);
  and and_4 (and_4_out, not_7_out, not_8_out);
  and and_5 (and_5_out, not_9_out, not_10_out);
  not not_19 (not_19_out, q2);
  and and_6 (and_6_out, not_11_out, not_12_out);
  not not_20 (not_20_out, q9);
  and and_7 (and_7_out, not_13_out, not_14_out);
  not not_21 (not_21_out, q4);
  and and_8 (and_8_out, not_15_out, not_16_out);
  not not_22 (not_22_out, q9);
  and and_9 (and_9_out, not_17_out, not_18_out);
  not not_23 (not_23_out, q4);
  not not_24 (not_24_out, q6);
  not not_25 (not_25_out, q8);
  and and_10 (and_10_out, and_1_out, and_2_out);
  and and_11 (and_11_out, and_3_out, and_4_out);
  and and_12 (and_12_out, and_5_out, not_19_out);
  and and_13 (and_13_out, and_6_out, not_20_out);
  and and_14 (and_14_out, and_7_out, not_21_out);
  and and_15 (and_15_out, and_8_out, not_22_out);
  and and_16 (and_16_out, and_9_out, not_23_out);
  and and_17 (and_17_out, not_24_out, not_25_out);
  and and_18 (b0, and_10_out, and_11_out);
  and and_19 (b1, and_12_out, and_13_out);
  and and_20 (b2, and_14_out, and_15_out);
  and and_21 (b3, and_16_out, and_17_out);
endmodule

module BITtoIND (
  input  q0,
  input  q1,
  input  q2,
  input  q3,
  output w0,
  output w1,
  output w2,
  output w3,
  output w4,
  output w5,
  output w6,
  output w7
);

  wire and_1_out, and_2_out, and_3_out, and_4_out, and_5_out, and_6_out, and_7_out, and_8_out, and_9_out,
       and_10_out, and_11_out, and_12_out, and_13_out, and_14_out, and_15_out, and_16_out, and_17_out,
       not_1_out, not_2_out, not_3_out, not_4_out, not_5_out, not_6_out, not_7_out, not_8_out, not_9_out,
       not_10_out, not_11_out, not_12_out, not_13_out, not_14_out, not_15_out, not_16_out, not_17_out,
       not_18_out, not_19_out, not_20_out, not_21_out, or_1_out, or_2_out, or_3_out, or_4_out, or_5_out,
       or_6_out, or_7_out, or_8_out, or_10_out, or_16_out, or_17_out;

  not not_1 (not_1_out, q1);
  not not_2 (not_2_out, q2);
  and and_1 (and_1_out, not_2_out, not_3_out);
  not not_3 (not_3_out, q3);
  not not_4 (not_4_out, q1);
  and and_2 (and_2_out, not_4_out, not_5_out);
  not not_5 (not_5_out, q3);
  and and_3 (and_3_out, q1, q3);
  not not_6 (not_6_out, q2);
  and and_4 (and_4_out, not_6_out, not_7_out);
  not not_7 (not_7_out, q3);
  and and_5 (and_5_out, q1, not_8_out);
  not not_8 (not_8_out, q2);
  and and_6 (and_6_out, q1, not_9_out);
  not not_9 (not_9_out, q3);
  not not_10 (not_10_out, q1);
  and and_7 (and_7_out, not_10_out, q2);
  and and_8 (and_8_out, q1, not_11_out);
  not not_11 (not_11_out, q2);
  and and_9 (and_9_out, q1, not_12_out);
  not not_12 (not_12_out, q3);
  not not_13 (not_13_out, q1);
  and and_10 (and_10_out, not_13_out, not_14_out);
  not not_14 (not_14_out, q3);
  and and_11 (and_11_out, q2, not_15_out);
  not not_15 (not_15_out, q3);
  not not_16 (not_16_out, q1);
  and and_12 (and_12_out, not_16_out, not_17_out);
  not not_17 (not_17_out, q3);
  not not_18 (not_18_out, q1);
  and and_13 (and_13_out, not_18_out, q2);
  not not_19 (not_19_out, q3);
  and and_14 (and_14_out, q1, not_20_out);
  not not_20 (not_20_out, q2);
  not not_21 (not_21_out, q2);
  or or_1 (or_1_out, not_21_out, q3);
  or or_2 (or_2_out, not_1_out, and_1_out);
  and and_15 (and_15_out, q2, q3);
  or or_3 (or_3_out, and_2_out, q2);
  or or_4 (or_4_out, and_3_out, q0);
  or or_5 (or_5_out, and_4_out, and_5_out);
  or or_6 (or_6_out, and_6_out, q0);
  or or_7 (or_7_out, and_7_out, and_8_out);
  or or_8 (or_8_out, and_9_out, q0);
  or or_9 (w4, and_10_out, and_11_out);
  or or_10 (or_10_out, and_12_out, and_13_out);
  and and_16 (and_16_out, q2, not_19_out);
  and and_17 (and_17_out, and_14_out, q3);
  or or_11 (w6, or_1_out, q1);
  or or_12 (w0, or_2_out, and_15_out);
  or or_13 (w1, or_3_out, or_4_out);
  or or_14 (w2, or_5_out, or_6_out);
  or or_15 (w3, or_7_out, or_8_out);
  or or_16 (or_16_out, or_10_out, and_16_out);
  or or_17 (or_17_out, and_17_out, q0);
  or or_18 (w5, or_16_out, or_17_out);

  assign w7 = 1'b0;
endmodule

module DecToBit (
  input  q0,
  input  q1,
  input  q2,
  input  q3,
  input  q4,
  input  q5,
  input  q6,
  input  q7,
  input  q8,
  input  q9,
  output w0,
  output w1,
  output w2,
  output w3
);

  wire or_2_out, or_3_out, or_4_out, or_5_out, or_6_out, or_9_out, or_10_out;

  or or_1 (w0, q9, q8);
  or or_2 (or_2_out, q7, q6);
  or or_3 (or_3_out, q5, q4);
  or or_4 (or_4_out, q7, q6);
  or or_5 (or_5_out, q3, q2);
  or or_6 (or_6_out, q9, q7);
  or or_7 (w1, or_2_out, or_3_out);
  or or_8 (w2, or_4_out, or_5_out);
  or or_9 (or_9_out, or_6_out, q5);
  or or_10 (or_10_out, q3, q1);
  or or_11 (w3, or_9_out, or_10_out);
endmodule

module BitToInd (
  input  q0,
  input  q1,
  input  q2,
  input  q3,
  output b0,
  output b1,
  output b2,
  output b3,
  output b4,
  output b5,
  output b6,
  output b7
);

  wire and_1_out, and_2_out, and_3_out, and_4_out, and_5_out, and_6_out, and_7_out, and_8_out, and_9_out,
       and_10_out, and_11_out, and_12_out, and_13_out, and_14_out, and_15_out, and_16_out, and_17_out,
       and_18_out, and_19_out, and_20_out, and_21_out, and_22_out, not_1_out, not_2_out, not_3_out,
       not_4_out, not_5_out, not_6_out, not_7_out, not_8_out, not_9_out, not_10_out, not_11_out, not_12_out,
       not_13_out, not_14_out, not_15_out, not_16_out, not_17_out, not_18_out, not_19_out, not_20_out,
       not_21_out, not_22_out, not_23_out, not_24_out, not_25_out, or_1_out, or_2_out, or_3_out, or_4_out,
       or_5_out, or_6_out, or_7_out, or_8_out, or_9_out, or_10_out, or_16_out, or_17_out;

  not not_1 (not_1_out, q1);
  not not_2 (not_2_out, q2);
  and and_1 (and_1_out, not_2_out, not_3_out);
  not not_3 (not_3_out, q3);
  not not_4 (not_4_out, q1);
  and and_2 (and_2_out, not_4_out, not_5_out);
  not not_5 (not_5_out, q3);
  and and_3 (and_3_out, q1, q3);
  not not_6 (not_6_out, q2);
  and and_4 (and_4_out, not_6_out, not_7_out);
  not not_7 (not_7_out, q3);
  and and_5 (and_5_out, q1, not_8_out);
  not not_8 (not_8_out, q2);
  and and_6 (and_6_out, q1, not_9_out);
  not not_9 (not_9_out, q3);
  not not_10 (not_10_out, q1);
  and and_7 (and_7_out, not_10_out, q2);
  and and_8 (and_8_out, q1, not_11_out);
  not not_11 (not_11_out, q3);
  not not_12 (not_12_out, q1);
  and and_9 (and_9_out, not_12_out, not_13_out);
  not not_13 (not_13_out, q3);
  and and_10 (and_10_out, q2, not_14_out);
  not not_14 (not_14_out, q3);
  and and_11 (and_11_out, q1, not_15_out);
  not not_15 (not_15_out, q2);
  not not_16 (not_16_out, q1);
  and and_12 (and_12_out, not_16_out, not_17_out);
  not not_17 (not_17_out, q3);
  not not_18 (not_18_out, q1);
  and and_13 (and_13_out, not_18_out, q2);
  not not_19 (not_19_out, q3);
  and and_14 (and_14_out, q1, not_20_out);
  not not_20 (not_20_out, q2);
  not not_21 (not_21_out, q2);
  and and_15 (and_15_out, not_21_out, not_22_out);
  not not_22 (not_22_out, q3);
  and and_16 (and_16_out, q2, q3);
  not not_23 (not_23_out, q0);
  and and_17 (and_17_out, not_23_out, not_24_out);
  not not_24 (not_24_out, q1);
  not not_25 (not_25_out, q2);
  and and_18 (and_18_out, not_25_out, q3);
  or or_1 (or_1_out, not_1_out, and_1_out);
  and and_19 (and_19_out, q2, q3);
  or or_2 (or_2_out, and_2_out, q2);
  or or_3 (or_3_out, and_3_out, q0);
  or or_4 (or_4_out, and_4_out, and_5_out);
  or or_5 (or_5_out, and_6_out, q0);
  or or_6 (or_6_out, and_7_out, and_8_out);
  or or_7 (or_7_out, and_9_out, and_10_out);
  and and_20 (and_20_out, and_11_out, q3);
  or or_8 (or_8_out, and_12_out, and_13_out);
  and and_21 (and_21_out, q2, not_19_out);
  and and_22 (and_22_out, and_14_out, q3);
  or or_9 (or_9_out, and_15_out, and_16_out);
  or or_10 (or_10_out, q1, q0);
  and and_23 (b7, and_17_out, and_18_out);
  or or_11 (b0, or_1_out, and_19_out);
  or or_12 (b1, or_2_out, or_3_out);
  or or_13 (b2, or_4_out, or_5_out);
  or or_14 (b3, or_6_out, q0);
  or or_15 (b4, or_7_out, and_20_out);
  or or_16 (or_16_out, or_8_out, and_21_out);
  or or_17 (or_17_out, and_22_out, q0);
  or or_18 (b6, or_9_out, or_10_out);
  or or_19 (b5, or_16_out, or_17_out);
endmodule

module Calc (
  input  [3:0] in_1,
  output [3:0] out_2
);

  wire _0_out, _1_out, _2_out, _3_out, _4_out, _5_out, _6_out, _7_out, _8_out, _9_out, Backspace_out,
       bittoind_1_w0, bittoind_1_w1, bittoind_1_w2, bittoind_1_w3, bittoind_1_w4, bittoind_1_w5,
       bittoind_1_w6, bittoind_1_w7, bittoind_2_w0, bittoind_2_w1, bittoind_2_w2, bittoind_2_w3,
       bittoind_2_w4, bittoind_2_w5, bittoind_2_w6, bittoind_2_w7, bittoind_3_w0, bittoind_3_w1,
       bittoind_3_w2, bittoind_3_w3, bittoind_3_w4, bittoind_3_w5, bittoind_3_w6, bittoind_3_w7,
       bittoind_4_w0, bittoind_4_w1, bittoind_4_w2, bittoind_4_w3, bittoind_4_w4, bittoind_4_w5,
       bittoind_4_w6, bittoind_4_w7, not_1_out, or_1_out, or_2_out, \Очистить_out ;
  wire [3:0] multiplexer_1_out, multiplexer_2_out, multiplexer_3_out, multiplexer_4_out, multiplexer_5_out,
       register_1_q, register_2_q, register_3_q, register_4_q, register_5_q, register_6_q, register_7_q;

  Button _0 (.out(_0_out));
  Button _1 (.out(_1_out));
  Button _2 (.out(_2_out));
  Button _3 (.out(_3_out));
  Button _4 (.out(_4_out));
  Button _5 (.out(_5_out));
  Button _6 (.out(_6_out));
  Button _7 (.out(_7_out));
  Button _8 (.out(_8_out));
  Button _9 (.out(_9_out));
  Button Backspace (.out(Backspace_out));
  Button \u_Очистить  (.out(\Очистить_out ));
  DecToBit dectobit_1 (
    .q0(_0_out), .q1(_1_out), .q2(_2_out), .q3(_3_out), .q4(_4_out), .q5(_5_out), .q6(_6_out), .q7(_7_out),
    .q8(_8_out), .q9(_9_out), .w0(out_2[3]), .w1(out_2[2]), .w2(out_2[1]), .w3(out_2[0]));
  not not_1 (not_1_out, or_1_out);
  Register #(.width(4), .trigger("falling")) register_1 (
    .D(out_2), .Q(register_1_q), .clk(not_1_out));  // open: en, clr
  or or_1 (or_1_out, out_2[0], out_2[1], out_2[2], out_2[3], _0_out);
  or or_2 (or_2_out, Backspace_out, or_1_out);
  Multiplexer #(.width(4)) multiplexer_1 (
    .in0(register_1_q), .in1(register_3_q), .out(multiplexer_1_out), .sel(Backspace_out));  // open: en
  Register #(.width(4), .trigger("falling")) register_2 (
    .D(multiplexer_1_out), .Q(register_2_q), .clk(or_2_out), .clr(\Очистить_out ));  // open: en
  Multiplexer #(.width(4)) multiplexer_2 (
    .in0(register_2_q), .in1(register_4_q), .out(multiplexer_2_out), .sel(Backspace_out));  // open: en
  Register #(.width(4), .trigger("falling")) register_3 (
    .D(multiplexer_2_out), .Q(register_3_q), .clk(or_2_out), .clr(\Очистить_out ));  // open: en
  Multiplexer #(.width(4)) multiplexer_3 (
    .in0(register_3_q), .in1(register_5_q), .out(multiplexer_3_out), .sel(Backspace_out));  // open: en
  Register #(.width(4), .trigger("falling")) register_4 (
    .D(multiplexer_3_out), .Q(register_4_q), .clk(or_2_out), .clr(\Очистить_out ));  // open: en
  Multiplexer #(.width(4)) multiplexer_4 (
    .in0(register_4_q), .in1(register_6_q), .out(multiplexer_4_out), .sel(Backspace_out));  // open: en
  Register #(.width(4), .trigger("falling")) register_5 (
    .D(multiplexer_4_out), .Q(register_5_q), .clk(or_2_out), .clr(\Очистить_out ));  // open: en
  Multiplexer #(.width(4)) multiplexer_5 (
    .in0(register_5_q), .in1(register_7_q), .out(multiplexer_5_out), .sel(Backspace_out));  // open: en
  Register #(.width(4), .trigger("falling")) register_6 (
    .D(multiplexer_5_out), .Q(register_6_q), .clk(or_2_out), .clr(\Очистить_out ));  // open: en
  Register #(.width(4), .trigger("falling")) register_7 (.D(in_1), .Q(register_7_q));  // open: en, clk, clr
  BITtoIND bittoind_1 (
    .q0(register_5_q[3]), .q1(register_5_q[2]), .q2(register_5_q[1]), .q3(register_5_q[0]),
    .w0(bittoind_1_w0), .w1(bittoind_1_w1), .w2(bittoind_1_w2), .w3(bittoind_1_w3), .w4(bittoind_1_w4),
    .w5(bittoind_1_w5), .w6(bittoind_1_w6), .w7(bittoind_1_w7));
  _7_Segment_Display u_7_segment_display_1 (
    .g(bittoind_1_w3), .f(bittoind_1_w2), .a(bittoind_1_w1), .b(bittoind_1_w0), .e(bittoind_1_w4),
    .d(bittoind_1_w5), .c(bittoind_1_w6), .dp(bittoind_1_w7));
  BITtoIND bittoind_2 (
    .q0(register_4_q[3]), .q1(register_4_q[2]), .q2(register_4_q[1]), .q3(register_4_q[0]),
    .w0(bittoind_2_w0), .w1(bittoind_2_w1), .w2(bittoind_2_w2), .w3(bittoind_2_w3), .w4(bittoind_2_w4),
    .w5(bittoind_2_w5), .w6(bittoind_2_w6), .w7(bittoind_2_w7));
  _7_Segment_Display u_7_segment_display_2 (
    .g(bittoind_2_w3), .f(bittoind_2_w2), .a(bittoind_2_w1), .b(bittoind_2_w0), .e(bittoind_2_w4),
    .d(bittoind_2_w5), .c(bittoind_2_w6), .dp(bittoind_2_w7));
  BITtoIND bittoind_3 (
    .q0(register_3_q[3]), .q1(register_3_q[2]), .q2(register_3_q[1]), .q3(register_3_q[0]),
    .w0(bittoind_3_w0), .w1(bittoind_3_w1), .w2(bittoind_3_w2), .w3(bittoind_3_w3), .w4(bittoind_3_w4),
    .w5(bittoind_3_w5), .w6(bittoind_3_w6), .w7(bittoind_3_w7));
  _7_Segment_Display u_7_segment_display_3 (
    .g(bittoind_3_w3), .f(bittoind_3_w2), .a(bittoind_3_w1), .b(bittoind_3_w0), .e(bittoind_3_w4),
    .d(bittoind_3_w5), .c(bittoind_3_w6), .dp(bittoind_3_w7));
  BITtoIND bittoind_4 (
    .q0(register_2_q[3]), .q1(register_2_q[2]), .q2(register_2_q[1]), .q3(register_2_q[0]),
    .w0(bittoind_4_w0), .w1(bittoind_4_w1), .w2(bittoind_4_w2), .w3(bittoind_4_w3), .w4(bittoind_4_w4),
    .w5(bittoind_4_w5), .w6(bittoind_4_w6), .w7(bittoind_4_w7));
  _7_Segment_Display u_7_segment_display_4 (
    .g(bittoind_4_w3), .f(bittoind_4_w2), .a(bittoind_4_w1), .b(bittoind_4_w0), .e(bittoind_4_w4),
    .d(bittoind_4_w5), .c(bittoind_4_w6), .dp(bittoind_4_w7));

  // Notes on the sheet:
  //   6 памятов, последний хранит число 0
  //   Сам Калькулятор
endmodule
