// Logisim project БВТ2003_Тураев_Некруз_№7.circ as structural Verilog: 4 circuits, main circuit main
module main (
);

  wire _0_out, _1_out, _2_out, _3_out, _4_out, _5_out, _6_out, _7_out, _8_out, _9_out, bittoind_1_w0,
       bittoind_1_w1, bittoind_1_w2, bittoind_1_w3, bittoind_1_w4, bittoind_1_w5, bittoind_1_w6,
       bittoind_1_w7, or_1_out;
  wire [3:0] dectobit_1_w0, register_1_q;

  Button _0 (.out(_0_out));
  Button _1 (.out(_1_out));
  Button _2 (.out(_2_out));
  Button _3 (.out(_3_out));
  Button _4 (.out(_4_out));
  Button _5 (.out(_5_out));
  Button _6 (.out(_6_out));
  Button _7 (.out(_7_out));
  Button _8 (.out(_8_out));
  Button _9 (.out(_9_out));
  DecToBit dectobit_1 (
    .q0(_0_out), .q1(_1_out), .q2(_2_out), .q3(_3_out), .q4(_4_out), .q5(_5_out), .q6(_6_out), .q7(_7_out),
    .q8(_8_out), .q9(_9_out), .w0(dectobit_1_w0[0]), .w1(dectobit_1_w0[1]), .w2(dectobit_1_w0[2]),
    .w3(dectobit_1_w0[3]));
  Register #(.width(4)) register_1 (.D(dectobit_1_w0), .Q(register_1_q), .clk(or_1_out));  // open: en, clr
  BITtoIND bittoind_1 (
    .q0(register_1_q[0]), .q1(register_1_q[1]), .q2(register_1_q[2]), .q3(register_1_q[3]),
    .w0(bittoind_1_w0), .w1(bittoind_1_w1), .w2(bittoind_1_w2), .w3(bittoind_1_w3), .w4(bittoind_1_w4),
    .w5(bittoind_1_w5), .w6(bittoind_1_w6), .w7(bittoind_1_w7));
  or or_1 (or_1_out, dectobit_1_w0[3], dectobit_1_w0[2], dectobit_1_w0[1], dectobit_1_w0[0], _0_out);
  _7_Segment_Display u_7_segment_display_1 (
    .g(bittoind_1_w3), .f(bittoind_1_w2), .a(bittoind_1_w1), .b(bittoind_1_w0), .e(bittoind_1_w4),
    .d(bittoind_1_w5), .c(bittoind_1_w6), .dp(bittoind_1_w7));
endmodule

module DECtoBIT (
  input  q0,
  input  q1,
  input  q2,
  input  q3,
  input  q4,
  input  q5,
  input  q6,
  input  q7,
  input  q8,
  input  q9,
  output b0,
  output b1,
  output b2,
  output b3
);

  wire and_1_out, and_2_out, and_3_out, and_4_out, and_5_out, and_6_out, and_7_out, and_8_out, and_9_out,
       and_10_out, and_11_out, and_12_out, and_13_out, and_14_out, and_15_out, and_16_out, and_17_out,
       not_1_out, not_2_out, not_3_out, not_4_out, not_5_out, not_6_out, not_7_out, not_8_out, not_9_out,
       not_10_out, not_11_out, not_12_out, not_13_out, not_14_out, not_15_out, not_16_out, not_17_out,
       not_18_out, not_19_out, not_20_out, not_21_out, not_22_out, not_23_out, not_24_out, not_25_out;

  not not_1 (not_1_out, q0);
  not not_2 (not_2_out, q1);
  not not_3 (not_3_out, q2);
  not not_4 (not_4_out, q3);
  not not_5 (not_5_out, q4);
  not not_6 (not_6_out, q5);
  not not_7 (not_7_out, q6);
  not not_8 (not_8_out, q7);
  not not_9 (not_9_out, q0);
  not not_10 (not_10_out, q1);
  not not_11 (not_11_out, q3);
  not not_12 (not_12_out, q8);
  not not_13 (not_13_out, q0);
  not not_14 (not_14_out, q1);
  not not_15 (not_15_out, q5);
  not not_16 (not_16_out, q8);
  not not_17 (not_17_out, q0);
  not not_18 (not_18_out, q2);
  and and_1 (and_1_out, not_1_out, not_2_out);
  and and_2 (and_2_out, not_3_out, not_4_out);
  and and_3 (and_3_out, not_5_out, not_6_out);
  and and_4 (and_4_out, not_7_out, not_8_out);
  and and_5 (and_5_out, not_9_out, not_10_out);
  not not_19 (not_19_out, q2);
  and and_6 (and_6_out, not_11_out, not_12_out);
  not not_20 (not_20_out, q9);
  and and_7 (and_7_out, not_13_out, not_14_out);
  not not_21 (not_21_out, q4);
  and and_8 (and_8_out, not_15_out, not_16_out);
  not not_22 (not_22_out, q9);
  and and_9 (and_9_out, not_17_out, not_18_out);
  not not_23 (not_23_out, q4);
  not not_24 (not_24_out, q6);
  not not_25 (not_25_out, q8);
  and and_10 (and_10_out, and_1_out, and_2_out);
  and and_11 (and_11_out, and_3_out, and_4_out);
  and and_12 (and_12_out, and_5_out, not_19_out);
  and and_13 (and_13_out, and_6_out, not_20_out);
  and and_14 (and_14_out, and_7_out, not_21_out);
  and and_15 (and_15_out, and_8_out, not_22_out);
  and and_16 (and_16_out, and_9_out, not_23_out);
  and and_17 (and_17_out, not_24_out, not_25_out);
  and and_18 (b0, and_10_out, and_11_out);
  and and_19 (b1, and_12_out, and_13_out);
  and and_20 (b2, and_14_out, and_15_out);
  and and_21 (b3, and_16_out, and_17_out);
endmodule

module BITtoIND (
  input  q0,
  input  q1,
  input  q2,
  input  q3,
  output w0,
  output w1,
  output w2,
  output w3,
  output w4,
  output w5,
  output w6,
  output w7
);

  wire and_1_out, and_2_out, and_3_out, and_4_out, and_5_out, and_6_out, and_7_out, and_8_out, and_9_out,
       and_10_out, and_11_out, and_12_out, and_13_out, and_14_out, and_15_out, and_16_out, and_17_out,
       not_1_out, not_2_out, not_3_out, not_4_out, not_5_out, not_6_out, not_7_out, not_8_out, not_9_out,
       not_10_out, not_11_out, not_12_out, not_13_out, not_14_out, not_15_out, not_16_out, not_17_out,
       not_18_out, not_19_out, not_20_out, not_21_out, or_1_out, or_2_out, or_3_out, or_4_out, or_5_out,
       or_6_out, or_7_out, or_8_out, or_10_out, or_16_out, or_17_out;

  not not_1 (not_1_out, q1);
  not not_2 (not_2_out, q2);
  and and_1 (and_1_out, not_2_out, not_3_out);
  not not_3 (not_3_out, q3);
  not not_4 (not_4_out, q1);
  and and_2 (and_2_out, not_4_out, not_5_out);
  not not_5 (not_5_out, q3);
  and and_3 (and_3_out, q1, q3);
  not not_6 (not_6_out, q2);
  and and_4 (and_4_out, not_6_out, not_7_out);
  not not_7 (not_7_out, q3);
  and and_5 (and_5_out, q1, not_8_out);
  not not_8 (not_8_out, q2);
  and and_6 (and_6_out, q1, not_9_out);
  not not_9 (not_9_out, q3);
  not not_10 (not_10_out, q1);
  and and_7 (and_7_out, not_10_out, q2);
  and and_8 (and_8_out, q1, not_11_out);
  not not_11 (not_11_out, q2);
  and and_9 (and_9_out, q1, not_12_out);
  not not_12 (not_12_out, q3);
  not not_13 (not_13_out, q1);
  and and_10 (and_10_out, not_13_out, not_14_out);
  not not_14 (not_14_out, q3);
  and and_11 (and_11_out, q2, not_15_out);
  not not_15 (not_15_out, q3);
  not not_16 (not_16_out, q1);
  and and_12 (and_12_out, not_16_out, not_17_out);
  not not_17 (not_17_out, q3);
  not not_18 (not_18_out, q1);
  and and_13 (and_13_out, not_18_out, q2);
  not not_19 (not_19_out, q3);
  and and_14 (and_14_out, q1, not_20_out);
  not not_20 (not_20_out, q2);
  not not_21 (not_21_out, q2);
  or or_1 (or_1_out, not_21_out, q3);
  or or_2 (or_2_out, not_1_out, and_1_out);
  and and_15 (and_15_out, q2, q3);
  or or_3 (or_3_out, and_2_out, q2);
  or or_4 (or_4_out, and_3_out, q0);
  or or_5 (or_5_out, and_4_out, and_5_out);
  or or_6 (or_6_out, and_6_out, q0);
  or or_7 (or_7_out, and_7_out, and_8_out);
  or or_8 (or_8_out, and_9_out, q0);
  or or_9 (w4, and_10_out, and_11_out);
  or or_10 (or_10_out, and_12_out, and_13_out);
  and and_16 (and_16_out, q2, not_19_out);
  and and_17 (and_17_out, and_14_out, q3);
  or or_11 (w6, or_1_out, q1);
  or or_12 (w0, or_2_out, and_15_out);
  or or_13 (w1, or_3_out, or_4_out);
  or or_14 (w2, or_5_out, or_6_out);
  or or_15 (w3, or_7_out, or_8_out);
  or or_16 (or_16_out, or_10_out, and_16_out);
  or or_17 (or_17_out, and_17_out, q0);
  or or_18 (w5, or_16_out, or_17_out);

  assign w7 = 1'b0;
endmodule

module DecToBit (
  input  q0,
  input  q1,
  input  q2,
  input  q3,
  input  q4,
  input  q5,
  input  q6,
  input  q7,
  input  q8,
  input  q9,
  output w0,
  output w1,
  output w2,
  output w3
);

  wire or_2_out, or_3_out, or_4_out, or_5_out, or_6_out, or_9_out, or_10_out;

  or or_1 (w0, q9, q8);
  or or_2 (or_2_out, q7, q6);
  or or_3 (or_3_out, q5, q4);
  or or_4 (or_4_out, q7, q6);
  or or_5 (or_5_out, q3, q2);
  or or_6 (or_6_out, q9, q7);
  or or_7 (w1, or_2_out, or_3_out);
  or or_8 (w2, or_4_out, or_5_out);
  or or_9 (or_9_out, or_6_out, q5);
  or or_10 (or_10_out, q3, q1);
  or or_11 (w3, or_9_out, or_10_out);
endmodule
