// Logisim project процессор Гарвардская.circ as structural Verilog: 1 circuit, main circuit main
module main (
);

  wire clock_1_out, not_1_out, undriven;
  wire [3:0] counter_1_q, multiplexer_1_out, ram_1_data, register_1_q, register_3_q, undriven_2;
  wire [7:0] adder_1_out, register_2_q, register_4_q;
  wire [7:4] ram_1_data_2;

  Clock clock_1 (.out(clock_1_out));
  Counter #(.width(4), .max('hf)) counter_1 (
    .D(undriven_2), .count(undriven), .Q(counter_1_q), .clk(clock_1_out));  // open: load, carry, clr
  not not_1 (not_1_out, clock_1_out);
  Multiplexer #(.width(4)) multiplexer_1 (
    .in0(counter_1_q), .in1(register_1_q), .out(multiplexer_1_out), .sel(not_1_out));  // open: en
  // Probe on {ram_1_data_2, ram_1_data}
  RAM #(.addrWidth(4), .bus("separate")) ram_1 (
    .addr(multiplexer_1_out), .data({ram_1_data_2, ram_1_data}));  // open: din, str, sel, clk, ld, clr
  // Probe on ram_1_data
  // Probe on ram_1_data_2
  Register #(.width(4)) register_1 (.D(ram_1_data), .Q(register_1_q), .clk(not_1_out));  // open: en, clr
  Register #(.trigger("falling")) register_2 (
    .D({ram_1_data_2, ram_1_data}), .Q(register_2_q), .clk(clock_1_out));  // open: en, clr
  Register #(.width(4)) register_3 (.D(ram_1_data_2), .Q(register_3_q));  // open: en, clk, clr
  Adder adder_1 (.a(register_4_q), .b(register_2_q), .out(adder_1_out));  // open: cin, cout
  // AND_Gate and_1 is placed but not wired
  // Probe on nothing
  Register register_4 (.D(adder_1_out), .Q(register_4_q));  // open: en, clk, clr

  // Notes on the sheet:
  //   Add(x) = 001
  //   STA(x) = 0010
  //   BRZ(x)
  //   Sub = 0100
  //   Адрес
  //   Инструкция
  //   ACCUM
endmodule
